// Logisim project ALU.circ as structural Verilog: 4 circuits, main circuit ALU
module ALU (
  input  Cin,
  input  [15:0] AX,
  input  [15:0] BX,
  input  [15:0] CX,
  input  [15:0] DX,
  input  [15:0] EX,
  input  [15:0] DR,
  input  [15:0] IR,
  input  AX_2,
  input  BX_2,
  input  CX_2,
  input  DX_2,
  input  EX_2,
  input  DR_2,
  input  IR_2,
  input  AX_3,
  input  BX_3,
  input  CX_3,
  input  DX_3,
  input  EX_3,
  input  DR_3,
  input  IR_3,
  input  AND,
  input  OR,
  input  XOR,
  input  ADD,
  input  ADC,
  input  SUB,
  input  SBB,
  input  MUL,
  input  DIV,
  input  CMP,
  output [15:0] MAIN_OUT,
  output [15:0] SECOND_OUT,
  output Zero,
  output Cout
);

  wire add_adc_1_cout, and_2_out, and_3_out, cmp_1_a___b, cmp_1_a___b_2, cmp_1_a___b_3, or_2_out, or_3_out,
       sub_sbb_1_bout;
  wire [6:0] signal_distributor_1__7_bit;
  wire [13:0] signal_distributor_1__14_bit;
  wire [15:0] add_adc_1_output, and_1_out_15, div_1_quotient, div_1_remainder, mul_1_high_16, mul_1_low_16,
       or_1_out_15, sub_sbb_1_output, xor_1_out_15;

  SIGNAL_DISTRIBUTOR signal_distributor_1 (
    .AX(AX_2), .BX(BX_2), .CX(CX_2), .DX(DX_2), .EX(EX_2), .DR(DR_2), .IR(IR_2), .AX_2(AX_3), .BX_2(BX_3),
    .CX_2(CX_3), .DX_2(DX_3), .EX_2(EX_3), .DR_2(DR_3), .IR_2(IR_3), ._7_BIT(signal_distributor_1__7_bit),
    ._14_BIT(signal_distributor_1__14_bit));
  AND and_1 (
    .AX_2(signal_distributor_1__7_bit[0]), .BX_2(signal_distributor_1__7_bit[1]),
    .CX_2(signal_distributor_1__7_bit[2]), .DX_2(signal_distributor_1__7_bit[3]),
    .EX_2(signal_distributor_1__7_bit[4]), .DR_2(signal_distributor_1__7_bit[5]),
    .IR_2(signal_distributor_1__7_bit[6]), .AX(AX), .BX(BX), .CX(CX), .DX(DX), .EX(EX), .DR(DR), .IR(IR),
    .out_15(and_1_out_15));
  OR or_1 (
    .AX_2(signal_distributor_1__7_bit[0]), .BX_2(signal_distributor_1__7_bit[1]),
    .CX_2(signal_distributor_1__7_bit[2]), .DX_2(signal_distributor_1__7_bit[3]),
    .EX_2(signal_distributor_1__7_bit[4]), .DR_2(signal_distributor_1__7_bit[5]),
    .IR_2(signal_distributor_1__7_bit[6]), .AX(AX), .BX(AX), .CX(CX), .DX(DX), .EX(EX), .DR(DR), .IR(IR),
    .out_15(or_1_out_15));
  MUL mul_1 (
    .AX(AX), .BX_2(BX), .CX_2(CX), .DX_2(DX), .EX_2(EX), .DR_2(DR), .IR_2(IR),
    .AX_2(signal_distributor_1__7_bit[0]), .BX(signal_distributor_1__7_bit[1]),
    .CX(signal_distributor_1__7_bit[2]), .DX(signal_distributor_1__7_bit[3]),
    .EX(signal_distributor_1__7_bit[4]), .DR(signal_distributor_1__7_bit[5]),
    .IR(signal_distributor_1__7_bit[6]), .LOW_16(mul_1_low_16), .HIGH_16(mul_1_high_16));
  DIV div_1 (
    .AX_3(AX), .BX_3(BX), .CX_3(CX), .DX_3(DX), .EX_3(EX), .DR_3(DR), .IR_3(IR),
    .AX(signal_distributor_1__14_bit[13]), .BX(signal_distributor_1__14_bit[12]),
    .CX(signal_distributor_1__14_bit[11]), .DX(signal_distributor_1__14_bit[10]),
    .EX(signal_distributor_1__14_bit[9]), .DR(signal_distributor_1__14_bit[8]),
    .IR(signal_distributor_1__14_bit[7]), .AX_2(signal_distributor_1__14_bit[6]),
    .BX_2(signal_distributor_1__14_bit[5]), .CX_2(signal_distributor_1__14_bit[4]),
    .DX_2(signal_distributor_1__14_bit[3]), .EX_2(signal_distributor_1__14_bit[2]),
    .DR_2(signal_distributor_1__14_bit[1]), .IR_2(signal_distributor_1__14_bit[0]),
    .QUOTIENT(div_1_quotient), .REMAINDER(div_1_remainder));
  CMP cmp_1 (
    .AX_3(AX), .BX_3(BX), .CX_3(CX), .DX_3(DX), .EX_3(EX), .DR_3(DR), .IR_3(IR),
    .AX(signal_distributor_1__14_bit[13]), .BX(signal_distributor_1__14_bit[12]),
    .CX(signal_distributor_1__14_bit[11]), .DX(signal_distributor_1__14_bit[10]),
    .EX(signal_distributor_1__14_bit[9]), .DR(signal_distributor_1__14_bit[8]),
    .IR(signal_distributor_1__14_bit[7]), .AX_2(signal_distributor_1__14_bit[6]),
    .BX_2(signal_distributor_1__14_bit[5]), .CX_2(signal_distributor_1__14_bit[4]),
    .DX_2(signal_distributor_1__14_bit[3]), .EX_2(signal_distributor_1__14_bit[2]),
    .DR_2(signal_distributor_1__14_bit[1]), .IR_2(signal_distributor_1__14_bit[0]), .A___B(cmp_1_a___b),
    .A___B_2(cmp_1_a___b_2), .A___B_3(cmp_1_a___b_3));
  ADD_ADC add_adc_1 (
    .AX_2(signal_distributor_1__7_bit[0]), .BX_2(signal_distributor_1__7_bit[1]),
    .CX_2(signal_distributor_1__7_bit[2]), .DX_2(signal_distributor_1__7_bit[3]),
    .EX_2(signal_distributor_1__7_bit[4]), .DR_2(signal_distributor_1__7_bit[5]),
    .IR_2(signal_distributor_1__7_bit[6]), .AX(AX), .BX(BX), .CX(CX), .DX(DX), .EX(EX), .DR(DR), .IR(IR),
    .Cin(and_2_out), .OUTPUT(add_adc_1_output), .Cout(add_adc_1_cout));
  XOR xor_1 (
    .AX_2(signal_distributor_1__7_bit[0]), .BX_2(signal_distributor_1__7_bit[1]),
    .CX_2(signal_distributor_1__7_bit[2]), .DX_2(signal_distributor_1__7_bit[3]),
    .EX_2(signal_distributor_1__7_bit[4]), .DR_2(signal_distributor_1__7_bit[5]),
    .IR_2(signal_distributor_1__7_bit[6]), .AX(AX), .BX(AX), .CX(CX), .DX(DX), .EX(EX), .DR(DR), .IR(IR),
    .out_15(xor_1_out_15));
  and and_2 (and_2_out, Cin, ADC);
  SUB_SBB sub_sbb_1 (
    .AX_2(signal_distributor_1__14_bit[13]), .BX_2(signal_distributor_1__14_bit[12]),
    .CX_2(signal_distributor_1__14_bit[11]), .DX_2(signal_distributor_1__14_bit[10]),
    .EX_2(signal_distributor_1__14_bit[9]), .DR_2(signal_distributor_1__14_bit[8]),
    .IR_2(signal_distributor_1__14_bit[7]), .AX_3(signal_distributor_1__14_bit[6]),
    .BX_3(signal_distributor_1__14_bit[5]), .CX_3(signal_distributor_1__14_bit[4]),
    .DX_3(signal_distributor_1__14_bit[3]), .EX_3(signal_distributor_1__14_bit[2]),
    .DR_3(signal_distributor_1__14_bit[1]), .IR_3(signal_distributor_1__14_bit[0]), .AX(AX), .BX(BX),
    .CX(CX), .DX(DX), .EX(EX), .DR(DR), .IR(IR), .Bin(and_3_out), .OUTPUT(sub_sbb_1_output),
    .Bout(sub_sbb_1_bout));
  assign MAIN_OUT = MUL ? mul_1_high_16 : 16'bz;  // Controlled_Buffer controlled_buffer_1
  assign MAIN_OUT = DIV ? div_1_quotient : 16'bz;  // Controlled_Buffer controlled_buffer_2
  assign SECOND_OUT = DIV ? div_1_remainder : 16'bz;  // Controlled_Buffer controlled_buffer_3
  and and_3 (and_3_out, Cin, SBB);
  assign MAIN_OUT = XOR ? xor_1_out_15 : 16'bz;  // Controlled_Buffer controlled_buffer_4
  assign MAIN_OUT = OR ? or_1_out_15 : 16'bz;  // Controlled_Buffer controlled_buffer_5
  assign SECOND_OUT = MUL ? mul_1_low_16 : 16'bz;  // Controlled_Buffer controlled_buffer_6
  assign MAIN_OUT = or_2_out ? add_adc_1_output : 16'bz;  // Controlled_Buffer controlled_buffer_7
  assign MAIN_OUT = AND ? and_1_out_15 : 16'bz;  // Controlled_Buffer controlled_buffer_8
  or or_2 (or_2_out, ADD, ADC);
  assign MAIN_OUT = or_3_out ? sub_sbb_1_output : 16'bz;  // Controlled_Buffer controlled_buffer_9
  or or_3 (or_3_out, SUB, SBB);
  ALU_Zero alu_zero_1 (
    .MAIN_OUT(MAIN_OUT), .A___B(cmp_1_a___b), .A___B_2(cmp_1_a___b_2), .A___B_3(cmp_1_a___b_3), .CMP(CMP),
    .Zero(Zero));
  ALU_Cout alu_cout_1 (
    .ADD(ADD), .ADC(ADC), .Cout_from_add(add_adc_1_cout), .SUB(SUB), .SBB(SBB),
    .Bout_from_sub(sub_sbb_1_bout), .A___B(cmp_1_a___b), .A___B_2(cmp_1_a___b_2), .A___B_3(cmp_1_a___b_3),
    .CMP(CMP), .OUT(Cout));
endmodule

module SIGNAL_DISTRIBUTOR (
  input  AX,
  input  BX,
  input  CX,
  input  DX,
  input  EX,
  input  DR,
  input  IR,
  input  AX_2,
  input  BX_2,
  input  CX_2,
  input  DX_2,
  input  EX_2,
  input  DR_2,
  input  IR_2,
  output [6:0] _7_BIT,
  output [13:0] _14_BIT
);

  or or_1 (_7_BIT[0], AX, AX_2);
  or or_2 (_7_BIT[1], BX, BX_2);
  or or_3 (_7_BIT[2], CX, CX_2);
  or or_4 (_7_BIT[3], DX, DX_2);
  or or_5 (_7_BIT[4], EX, EX_2);
  or or_6 (_7_BIT[5], DR, DR_2);
  or or_7 (_7_BIT[6], IR, IR_2);

  assign _14_BIT = {AX, BX, CX, DX, EX, DR, IR, AX_2, BX_2, CX_2, DX_2, EX_2, DR_2, IR_2};
endmodule

module ALU_Cout (
  input  ADD,
  input  ADC,
  input  Cout_from_add,
  input  SUB,
  input  SBB,
  input  Bout_from_sub,
  input  A___B,
  input  A___B_2,
  input  A___B_3,
  input  CMP,
  output OUT
);

  wire and_1_out, and_2_out, and_3_out, and_4_out, and_5_out, nand_1_out, not_1_out, or_1_out, or_2_out,
       or_3_out, or_4_out, or_5_out;

  or or_1 (or_1_out, ADD, ADC);
  or or_2 (or_2_out, SUB, SBB);
  or or_3 (or_3_out, A___B_2, A___B_3);
  and and_1 (and_1_out, or_1_out, Cout_from_add);
  and and_2 (and_2_out, or_2_out, Bout_from_sub);
  nand nand_1 (nand_1_out, A___B, CMP);
  and and_3 (and_3_out, or_3_out, CMP);
  or or_4 (or_4_out, and_1_out, and_2_out);
  or or_5 (or_5_out, nand_1_out, and_3_out);
  and and_4 (and_4_out, or_4_out, not_1_out);
  not not_1 (not_1_out, CMP);
  and and_5 (and_5_out, or_5_out, CMP);
  or or_6 (OUT, and_4_out, and_5_out);
endmodule

module ALU_Zero (
  input  [15:0] MAIN_OUT,
  input  A___B,
  input  A___B_2,
  input  A___B_3,
  input  CMP,
  output Zero
);

  wire and_1_out, and_2_out, not_1_out, not_2_out, not_3_out, or_1_out, or_2_out;

  or or_1 (or_1_out, A___B, A___B_2);
  not not_1 (not_1_out, A___B_3);
  and and_1 (and_1_out, CMP, not_1_out, or_1_out);
  not not_2 (not_2_out, CMP);
  or or_2 (or_2_out, MAIN_OUT[0], MAIN_OUT[1], MAIN_OUT[2], MAIN_OUT[3], MAIN_OUT[4], MAIN_OUT[5], MAIN_OUT[6], MAIN_OUT[7], MAIN_OUT[8], MAIN_OUT[9], MAIN_OUT[10], MAIN_OUT[11], MAIN_OUT[12], MAIN_OUT[13], MAIN_OUT[14], MAIN_OUT[15], 1'b0);
  not not_3 (not_3_out, or_2_out);
  and and_2 (and_2_out, not_3_out, not_2_out);
  or or_3 (Zero, and_2_out, and_1_out);
endmodule
