// Logisim project CONTROL UNIT.circ as structural Verilog
module PC (
  input  T0,
  input  T1,
  input  T3,
  input  T4,
  input  M201,
  input  M202,
  input  M203,
  input  M204,
  input  M205,
  input  M206,
  input  M207,
  input  M208,
  input  M209,
  input  M210,
  input  M211,
  input  M212,
  input  M213,
  input  M214,
  input  M215,
  input  M216,
  input  M217,
  input  M218,
  output PC_BUS,
  output PC_INC,
  output PC_LOAD
);

  wire and_1_out, and_2_out, and_3_out, and_4_out, and_5_out, and_6_out, and_7_out, and_8_out, and_9_out,
       and_10_out, and_11_out, and_12_out, and_13_out, and_14_out, and_15_out, and_16_out, and_17_out,
       and_18_out;

  and and_1 (and_1_out, M201, T4);
  and and_2 (and_2_out, M202, T3);
  and and_3 (and_3_out, M203, T3);
  and and_4 (and_4_out, M204, T4);
  and and_5 (and_5_out, M205, T3);
  and and_6 (and_6_out, M206, T3);
  and and_7 (and_7_out, M207, T4);
  and and_8 (and_8_out, M208, T3);
  and and_9 (and_9_out, M209, T3);
  and and_10 (and_10_out, M210, T4);
  and and_11 (and_11_out, M211, T3);
  and and_12 (and_12_out, M212, T3);
  and and_13 (and_13_out, M213, T4);
  and and_14 (and_14_out, M214, T3);
  and and_15 (and_15_out, M215, T3);
  and and_16 (and_16_out, M216, T4);
  and and_17 (and_17_out, M217, T3);
  and and_18 (and_18_out, M218, T3);
  or or_1 (PC_LOAD, and_1_out, and_2_out, and_3_out, and_4_out, and_5_out, and_6_out, and_7_out, and_8_out, and_9_out, and_10_out, and_11_out, and_12_out, and_13_out, and_14_out, and_15_out, and_16_out, and_17_out, and_18_out);

  assign PC_BUS = T0;
  assign PC_INC = T1;
endmodule

module IR (
  input  T1,
  input  T2,
  output IR_BUS,
  output IR_LOAD
);


  assign IR_BUS = T2;
  assign IR_LOAD = T1;
endmodule

module AR (
  input  C,
  input  Z,
  input  T0,
  input  T2,
  input  T3,
  input  T4,
  input  M0,
  input  M1,
  input  M2,
  input  M3,
  input  M4,
  input  M17,
  input  M18,
  input  M19,
  input  M20,
  input  M21,
  input  M34,
  input  M35,
  input  M36,
  input  M37,
  input  M38,
  input  M51,
  input  M52,
  input  M53,
  input  M54,
  input  M55,
  input  M68,
  input  M69,
  input  M70,
  input  M71,
  input  M72,
  input  M85,
  input  M86,
  input  M87,
  input  M88,
  input  M89,
  input  M102,
  input  M103,
  input  M104,
  input  M105,
  input  M106,
  input  M119,
  input  M120,
  input  M121,
  input  M122,
  input  M123,
  input  M136,
  input  M137,
  input  M138,
  input  M139,
  input  M140,
  input  M153,
  input  M154,
  input  M155,
  input  M156,
  input  M157,
  input  M170,
  input  M171,
  input  M172,
  input  M173,
  input  M174,
  input  M180,
  input  M181,
  input  M182,
  input  M183,
  input  M184,
  input  M201,
  input  M202,
  input  M204,
  input  M205,
  input  M207,
  input  M208,
  input  M210,
  input  M211,
  input  M213,
  input  M214,
  input  M216,
  input  M217,
  output AR_BUS,
  output AR_LOAD
);

  wire and_1_out, and_2_out, and_3_out, and_4_out, and_5_out, and_6_out, and_7_out, and_8_out, and_9_out,
       and_10_out, and_11_out, and_12_out, not_1_out, not_2_out, not_3_out, not_4_out, not_5_out, not_6_out,
       or_1_out, or_2_out, or_3_out, or_4_out;

  not not_1 (not_1_out, Z);
  not not_2 (not_2_out, Z);
  not not_3 (not_3_out, Z);
  not not_4 (not_4_out, Z);
  not not_5 (not_5_out, C);
  not not_6 (not_6_out, C);
  and and_1 (and_1_out, M201, T4);
  and and_2 (and_2_out, M202, T3);
  and and_3 (and_3_out, M204, T4, Z);
  and and_4 (and_4_out, M205, T3, Z);
  and and_5 (and_5_out, M207, T4, not_1_out);
  and and_6 (and_6_out, M208, T3, not_2_out);
  and and_7 (and_7_out, M210, T4, not_3_out, C);
  and and_8 (and_8_out, M211, T3, not_4_out, C);
  and and_9 (and_9_out, M213, T4, Z, not_5_out);
  and and_10 (and_10_out, M214, T3, Z, not_6_out);
  and and_11 (and_11_out, M216, T4, Z, C);
  and and_12 (and_12_out, M217, T3, Z, C);
  or or_1 (or_1_out, M216, M213, M210, M207, M204, M201, M184, M183, M182, M181, M180, M174, M173, M172, M171, M170, M157, M156, M155, M154, M153, M140);
  or or_2 (or_2_out, M139, M138, M137, M136, M123, M122, M121, M120, M119, M106, M105, M104, M103, M102, M89, M88, M87, M86, M85, M72, M71, M70);
  or or_3 (or_3_out, M69, M68, M55, M54, M53, M52, M51, M38, M37, M36, M35, M34, M21, M20, M19, M18, M17, M4, M3, M2, M1, M0);
  or or_4 (or_4_out, or_1_out, or_2_out, or_3_out);
  or or_5 (AR_BUS, and_1_out, and_2_out, and_3_out, and_4_out, and_5_out, and_6_out, and_7_out, and_8_out, and_9_out, and_10_out, and_11_out, and_12_out);
  and and_13 (AR_LOAD, or_4_out, T3);
endmodule
