// Logisim project CONTROL_UNITS.circ as structural Verilog
module PC (
  input  C,
  input  Z,
  input  T0,
  input  T1,
  input  T3,
  input  T4,
  input  M196,
  input  M197,
  input  M198,
  input  M199,
  input  M200,
  input  M201,
  input  M202,
  input  M203,
  input  M204,
  input  M205,
  input  M206,
  input  M207,
  input  M208,
  input  M209,
  input  M210,
  input  M211,
  input  M212,
  input  M213,
  output PC_BUS,
  output PC_INC,
  output PC_LOAD
);

  wire and_1_out, and_2_out, and_3_out, and_4_out, and_5_out, and_6_out, and_7_out, and_8_out, and_9_out,
       and_10_out, and_11_out, and_12_out, and_13_out, and_14_out, and_15_out, and_16_out, and_17_out,
       or_1_out, or_2_out;

  and and_1 (and_1_out, M199, Z);
  and and_2 (and_2_out, M202, ~Z);  // AND_Gate
  and and_3 (and_3_out, M205, C, ~Z);  // AND_Gate
  and and_4 (and_4_out, M208, ~C, Z);  // AND_Gate
  and and_5 (and_5_out, M211, Z, C);
  and and_6 (and_6_out, M200, Z);
  and and_7 (and_7_out, M201, Z);
  and and_8 (and_8_out, M203, ~Z);  // AND_Gate
  and and_9 (and_9_out, M204, ~Z);  // AND_Gate
  and and_10 (and_10_out, M206, C, ~Z);  // AND_Gate
  and and_11 (and_11_out, M207, C, ~Z);  // AND_Gate
  and and_12 (and_12_out, M209, ~C, Z);  // AND_Gate
  and and_13 (and_13_out, M210, ~C, Z);  // AND_Gate
  and and_14 (and_14_out, M212, C, Z);
  and and_15 (and_15_out, M213, C, Z);
  or or_1 (or_1_out, M196, and_1_out, and_2_out, and_3_out, and_4_out, and_5_out);
  and and_16 (and_16_out, or_1_out, T4);
  or or_2 (or_2_out, M197, M198, and_6_out, and_7_out, and_8_out, and_9_out, and_10_out, and_11_out, and_12_out, and_13_out, and_14_out, and_15_out);
  and and_17 (and_17_out, or_2_out, T3);
  or or_3 (PC_LOAD, and_16_out, and_17_out);

  assign PC_BUS = T0;
  assign PC_INC = T1;
endmodule

module IR (
  input  T1,
  input  T2,
  input  T3,
  input  M190,
  input  M191,
  input  M192,
  input  M193,
  input  M194,
  output IR_BUS,
  output IR_LOAD
);

  wire and_1_out, or_1_out;

  or or_1 (or_1_out, M194, M193, M192, M191, M190);
  and and_1 (and_1_out, or_1_out, T3);
  or or_2 (IR_BUS, and_1_out, T2);

  assign IR_LOAD = T1;
endmodule

module AR (
  input  C,
  input  Z,
  input  T0,
  input  T2,
  input  T3,
  input  T4,
  input  M0,
  input  M1,
  input  M2,
  input  M3,
  input  M4,
  input  M17,
  input  M18,
  input  M19,
  input  M20,
  input  M21,
  input  M34,
  input  M35,
  input  M36,
  input  M37,
  input  M38,
  input  M51,
  input  M52,
  input  M53,
  input  M54,
  input  M55,
  input  M68,
  input  M69,
  input  M70,
  input  M71,
  input  M72,
  input  M85,
  input  M86,
  input  M87,
  input  M88,
  input  M89,
  input  M102,
  input  M103,
  input  M104,
  input  M105,
  input  M106,
  input  M119,
  input  M120,
  input  M121,
  input  M122,
  input  M123,
  input  M136,
  input  M137,
  input  M138,
  input  M139,
  input  M140,
  input  M153,
  input  M154,
  input  M155,
  input  M156,
  input  M157,
  input  M170,
  input  M171,
  input  M172,
  input  M173,
  input  M174,
  input  M180,
  input  M181,
  input  M182,
  input  M183,
  input  M184,
  input  M196,
  input  M197,
  input  M199,
  input  M200,
  input  M202,
  input  M203,
  input  M205,
  input  M206,
  input  M208,
  input  M209,
  input  M211,
  input  M212,
  output AR_LOAD,
  output AR_BUS
);

  wire and_1_out, and_2_out, and_3_out, and_4_out, and_5_out, and_6_out, and_7_out, and_8_out, and_9_out,
       and_10_out, and_11_out, and_12_out, and_13_out, or_1_out, or_2_out, or_3_out, or_4_out;

  and and_1 (and_1_out, M196, T4);
  and and_2 (and_2_out, M197, T3);
  and and_3 (and_3_out, M199, T4, Z);
  and and_4 (and_4_out, M200, T3, Z);
  and and_5 (and_5_out, M202, T4, ~Z);  // AND_Gate
  and and_6 (and_6_out, M203, T3, ~Z);  // AND_Gate
  and and_7 (and_7_out, M205, T4, ~Z, C);  // AND_Gate
  and and_8 (and_8_out, M206, T3, ~Z, C);  // AND_Gate
  and and_9 (and_9_out, M208, T4, Z, ~C);  // AND_Gate
  and and_10 (and_10_out, M209, T3, Z, ~C);  // AND_Gate
  and and_11 (and_11_out, M211, T4, Z, C);
  and and_12 (and_12_out, M212, T3, Z, C);
  or or_1 (or_1_out, M211, M208, M205, M202, M199, M196, M184, M183, M182, M181, M180, M174, M173, M172, M171, M170, M157, M156, M155, M154, M153, M140);
  or or_2 (or_2_out, M139, M138, M137, M136, M123, M122, M121, M120, M119, M106, M105, M104, M103, M102, M89, M88, M87, M86, M85, M72, M71, M70);
  or or_3 (or_3_out, M69, M68, M55, M54, M53, M52, M51, M38, M37, M36, M35, M34, M21, M20, M19, M18, M17, M4, M3, M2, M1, M0);
  or or_4 (or_4_out, or_1_out, or_2_out, or_3_out);
  or or_5 (AR_BUS, and_1_out, and_2_out, and_3_out, and_4_out, and_5_out, and_6_out, and_7_out, and_8_out, and_9_out, and_10_out, and_11_out, and_12_out);
  and and_13 (and_13_out, or_4_out, T3);
  or or_6 (AR_LOAD, and_13_out, T2, T0);
endmodule

module DR (
  input  T3,
  input  T4,
  input  T5,
  input  M0,
  input  M1,
  input  M2,
  input  M3,
  input  M4,
  input  M5,
  input  M6,
  input  M7,
  input  M8,
  input  M9,
  input  M15,
  input  M17,
  input  M18,
  input  M19,
  input  M20,
  input  M21,
  input  M22,
  input  M23,
  input  M24,
  input  M25,
  input  M26,
  input  M32,
  input  M34,
  input  M35,
  input  M36,
  input  M37,
  input  M38,
  input  M39,
  input  M40,
  input  M41,
  input  M42,
  input  M43,
  input  M49,
  input  M51,
  input  M52,
  input  M53,
  input  M54,
  input  M55,
  input  M56,
  input  M57,
  input  M58,
  input  M59,
  input  M60,
  input  M66,
  input  M68,
  input  M69,
  input  M70,
  input  M71,
  input  M72,
  input  M73,
  input  M74,
  input  M75,
  input  M76,
  input  M77,
  input  M83,
  input  M85,
  input  M86,
  input  M87,
  input  M88,
  input  M89,
  input  M90,
  input  M91,
  input  M92,
  input  M93,
  input  M94,
  input  M100,
  input  M102,
  input  M103,
  input  M104,
  input  M105,
  input  M106,
  input  M107,
  input  M108,
  input  M109,
  input  M110,
  input  M111,
  input  M117,
  input  M119,
  input  M120,
  input  M121,
  input  M122,
  input  M123,
  input  M124,
  input  M125,
  input  M126,
  input  M127,
  input  M128,
  input  M134,
  input  M136,
  input  M137,
  input  M138,
  input  M139,
  input  M140,
  input  M141,
  input  M142,
  input  M143,
  input  M144,
  input  M145,
  input  M151,
  input  M153,
  input  M154,
  input  M155,
  input  M156,
  input  M157,
  input  M158,
  input  M159,
  input  M160,
  input  M161,
  input  M162,
  input  M168,
  input  M170,
  input  M171,
  input  M172,
  input  M173,
  input  M174,
  input  M175,
  input  M176,
  input  M177,
  input  M178,
  input  M179,
  output DR_LOAD,
  output DR_BUS
);

  wire and_1_out, and_2_out, and_3_out, and_4_out, or_1_out, or_2_out, or_3_out, or_4_out, or_5_out,
       or_6_out, or_7_out, or_8_out, or_9_out;

  or or_1 (or_1_out, M179, M178, M177, M176, M175);
  or or_2 (or_2_out, M174, M173, M172, M171, M170);
  or or_3 (or_3_out, M179, M178, M177, M176, M175, M168, M162, M161, M160, M159, M158, M151, M145, M144, M143, M142, M141, M134, M128, M127, M126, M125);
  or or_4 (or_4_out, M124, M117, M111, M110, M109, M108, M107, M100, M94, M93, M92, M91, M90, M83, M77, M76, M75, M74, M73, M66, M60, M59);
  or or_5 (or_5_out, M58, M57, M56, M49, M43, M42, M41, M40, M39, M32, M26, M25, M24, M23, M22, M15, M9, M8, M7, M6, M5);
  or or_6 (or_6_out, M174, M173, M172, M171, M170, M157, M156, M155, M154, M153, M140, M139, M138, M137, M136, M123, M122, M121, M120, M119, M106, M105, M104, M103, M102, M89, M88, M87);
  or or_7 (or_7_out, M86, M85, M72, M71, M70, M69, M68, M55, M54, M53, M52, M51, M38, M37, M36, M35, M34, M21, M20, M19, M18, M17, M4, M3, M2, M1, M0);
  and and_1 (and_1_out, or_1_out, T4);
  and and_2 (and_2_out, T5, or_2_out);
  or or_8 (or_8_out, or_3_out, or_4_out, or_5_out);
  and and_3 (and_3_out, or_8_out, T3);
  or or_9 (or_9_out, or_6_out, or_7_out);
  and and_4 (and_4_out, or_9_out, T4);
  or or_10 (DR_BUS, and_1_out, and_2_out);
  or or_11 (DR_LOAD, and_3_out, and_4_out);
endmodule

module SPECIAL_PURPOSE (
  input  C,
  input  Z,
  input  T0,
  input  T1,
  input  T2,
  input  T3,
  input  T4,
  input  T5,
  input  M0,
  input  M1,
  input  M2,
  input  M3,
  input  M4,
  input  M5,
  input  M6,
  input  M7,
  input  M8,
  input  M9,
  input  M15,
  input  M17,
  input  M18,
  input  M19,
  input  M20,
  input  M21,
  input  M22,
  input  M23,
  input  M24,
  input  M25,
  input  M26,
  input  M32,
  input  M34,
  input  M35,
  input  M36,
  input  M37,
  input  M38,
  input  M39,
  input  M40,
  input  M41,
  input  M42,
  input  M43,
  input  M49,
  input  M51,
  input  M52,
  input  M53,
  input  M54,
  input  M55,
  input  M56,
  input  M57,
  input  M58,
  input  M59,
  input  M60,
  input  M66,
  input  M68,
  input  M69,
  input  M70,
  input  M71,
  input  M72,
  input  M73,
  input  M74,
  input  M75,
  input  M76,
  input  M77,
  input  M83,
  input  M85,
  input  M86,
  input  M87,
  input  M88,
  input  M89,
  input  M90,
  input  M91,
  input  M92,
  input  M93,
  input  M94,
  input  M100,
  input  M102,
  input  M103,
  input  M104,
  input  M105,
  input  M106,
  input  M107,
  input  M108,
  input  M109,
  input  M110,
  input  M111,
  input  M117,
  input  M119,
  input  M120,
  input  M121,
  input  M122,
  input  M123,
  input  M124,
  input  M125,
  input  M126,
  input  M127,
  input  M128,
  input  M134,
  input  M136,
  input  M137,
  input  M138,
  input  M139,
  input  M140,
  input  M141,
  input  M142,
  input  M143,
  input  M144,
  input  M145,
  input  M151,
  input  M153,
  input  M154,
  input  M155,
  input  M156,
  input  M157,
  input  M158,
  input  M159,
  input  M160,
  input  M161,
  input  M162,
  input  M168,
  input  M170,
  input  M171,
  input  M172,
  input  M173,
  input  M174,
  input  M175,
  input  M176,
  input  M177,
  input  M178,
  input  M179,
  input  M180,
  input  M181,
  input  M182,
  input  M183,
  input  M184,
  input  M190,
  input  M191,
  input  M192,
  input  M193,
  input  M194,
  input  M196,
  input  M197,
  input  M198,
  input  M199,
  input  M200,
  input  M201,
  input  M202,
  input  M203,
  input  M204,
  input  M205,
  input  M206,
  input  M207,
  input  M208,
  input  M209,
  input  M210,
  input  M211,
  input  M212,
  input  M213,
  output PC_BUS,
  output PC_INC,
  output PC_LOAD,
  output IR_BUS,
  output IR_LOAD,
  output AR_LOAD,
  output AR_BUS,
  output DR_LOAD,
  output DR_BUS
);

  IR ir_1 (
    .T1(T1), .T2(T2), .T3(T3), .M190(M190), .M191(M191), .M192(M192), .M193(M193), .M194(M194),
    .IR_BUS(IR_BUS), .IR_LOAD(IR_LOAD));
  PC pc_1 (
    .C(C), .Z(Z), .T0(T0), .T1(T1), .T3(T3), .T4(T4), .M196(M196), .M197(M197), .M198(M198), .M199(M199),
    .M200(M200), .M201(M201), .M202(M202), .M203(M203), .M204(M204), .M205(M205), .M206(M206), .M207(M207),
    .M208(M208), .M209(M209), .M210(M210), .M211(M211), .M212(M212), .M213(M213), .PC_BUS(PC_BUS),
    .PC_INC(PC_INC), .PC_LOAD(PC_LOAD));
  AR ar_1 (
    .C(C), .Z(Z), .T0(T0), .T2(T2), .T3(T3), .T4(T4), .M0(M0), .M1(M1), .M2(M2), .M3(M3), .M4(M4), .M17(M17),
    .M18(M18), .M19(M19), .M20(M20), .M21(M21), .M34(M34), .M35(M35), .M36(M36), .M37(M37), .M38(M38),
    .M51(M51), .M52(M52), .M53(M53), .M54(M54), .M55(M55), .M68(M68), .M69(M69), .M70(M70), .M71(M71),
    .M72(M72), .M85(M85), .M86(M86), .M87(M87), .M88(M88), .M89(M89), .M102(M102), .M103(M103), .M104(M104),
    .M105(M105), .M106(M106), .M119(M119), .M120(M120), .M121(M121), .M122(M122), .M123(M123), .M136(M136),
    .M137(M137), .M138(M138), .M139(M139), .M140(M140), .M153(M153), .M154(M154), .M155(M155), .M156(M156),
    .M157(M157), .M170(M170), .M171(M171), .M172(M172), .M173(M173), .M174(M174), .M180(M180), .M181(M181),
    .M182(M182), .M183(M183), .M184(M184), .M196(M196), .M197(M197), .M199(M199), .M200(M200), .M202(M202),
    .M203(M203), .M205(M205), .M206(M206), .M208(M208), .M209(M209), .M211(M211), .M212(M212),
    .AR_LOAD(AR_LOAD), .AR_BUS(AR_BUS));
  DR dr_1 (
    .T3(T3), .T4(T4), .T5(T5), .M0(M0), .M1(M1), .M2(M2), .M3(M3), .M4(M4), .M5(M5), .M6(M6), .M7(M7),
    .M8(M8), .M9(M9), .M15(M15), .M17(M17), .M18(M18), .M19(M19), .M20(M20), .M21(M21), .M22(M22), .M23(M23),
    .M24(M24), .M25(M25), .M26(M26), .M32(M32), .M34(M34), .M35(M35), .M36(M36), .M37(M37), .M38(M38),
    .M39(M39), .M40(M40), .M41(M41), .M42(M42), .M43(M43), .M49(M49), .M51(M51), .M52(M52), .M53(M53),
    .M54(M54), .M55(M55), .M56(M56), .M57(M57), .M58(M58), .M59(M59), .M60(M60), .M66(M66), .M68(M68),
    .M69(M69), .M70(M70), .M71(M71), .M72(M72), .M73(M73), .M74(M74), .M75(M75), .M76(M76), .M77(M77),
    .M83(M83), .M85(M85), .M86(M86), .M87(M87), .M88(M88), .M89(M89), .M90(M90), .M91(M91), .M92(M92),
    .M93(M93), .M94(M94), .M100(M100), .M102(M102), .M103(M103), .M104(M104), .M105(M105), .M106(M106),
    .M107(M107), .M108(M108), .M109(M109), .M110(M110), .M111(M111), .M117(M117), .M119(M119), .M120(M120),
    .M121(M121), .M122(M122), .M123(M123), .M124(M124), .M125(M125), .M126(M126), .M127(M127), .M128(M128),
    .M134(M134), .M136(M136), .M137(M137), .M138(M138), .M139(M139), .M140(M140), .M141(M141), .M142(M142),
    .M143(M143), .M144(M144), .M145(M145), .M151(M151), .M153(M153), .M154(M154), .M155(M155), .M156(M156),
    .M157(M157), .M158(M158), .M159(M159), .M160(M160), .M161(M161), .M162(M162), .M168(M168), .M170(M170),
    .M171(M171), .M172(M172), .M173(M173), .M174(M174), .M175(M175), .M176(M176), .M177(M177), .M178(M178),
    .M179(M179), .DR_LOAD(DR_LOAD), .DR_BUS(DR_BUS));
endmodule

module AX (
  input  C,
  input  Z,
  input  T3,
  input  T4,
  input  T5,
  input  E0,
  input  E1,
  input  E2,
  input  E3,
  input  E4,
  input  E20,
  input  E21,
  input  E22,
  input  E23,
  input  E24,
  input  M0,
  input  M5,
  input  M10,
  input  M15,
  input  M16,
  input  M17,
  input  M22,
  input  M27,
  input  M32,
  input  M33,
  input  M34,
  input  M39,
  input  M44,
  input  M49,
  input  M50,
  input  M51,
  input  M56,
  input  M61,
  input  M66,
  input  M67,
  input  M68,
  input  M73,
  input  M78,
  input  M83,
  input  M84,
  input  M85,
  input  M90,
  input  M95,
  input  M100,
  input  M101,
  input  M102,
  input  M107,
  input  M112,
  input  M117,
  input  M118,
  input  M119,
  input  M123,
  input  M124,
  input  M128,
  input  M129,
  input  M133,
  input  M134,
  input  M135,
  input  M136,
  input  M140,
  input  M141,
  input  M145,
  input  M146,
  input  M150,
  input  M151,
  input  M152,
  input  M170,
  input  M175,
  input  M180,
  input  M185,
  input  M190,
  input  M195,
  input  M198,
  input  M201,
  input  M204,
  input  M207,
  input  M210,
  input  M213,
  input  M214,
  input  M215,
  input  M216,
  input  M217,
  input  M218,
  input  M219,
  input  M220,
  input  M221,
  output AX_INC,
  output AX_DEC,
  output AX_SHL,
  output AX_SHR,
  output AX_CIL,
  output AX_CIR,
  output AX_CML,
  output AX_CLR,
  output AX_LOAD,
  output AX_BUS
);

  wire and_9_out, and_10_out, and_11_out, and_12_out, and_13_out, and_14_out, and_15_out, and_16_out,
       and_17_out, and_18_out, and_19_out, and_20_out, and_21_out, and_22_out, and_23_out, and_24_out,
       or_1_out, or_2_out, or_3_out, or_4_out, or_5_out, or_6_out, or_7_out, or_8_out, or_9_out, or_10_out,
       or_11_out, or_12_out, or_13_out, or_14_out;

  and and_1 (AX_INC, M220, E0, T3);
  and and_2 (AX_DEC, M221, E0, T3);
  and and_3 (AX_SHL, M216, E0, T3);
  and and_4 (AX_SHR, M217, E0, T3);
  and and_5 (AX_CIL, M218, E0, T3);
  and and_6 (AX_CIR, M219, E0, T3);
  and and_7 (AX_CML, M215, E0, T3);
  and and_8 (AX_CLR, M214, E0, T3);
  or or_1 (or_1_out, E4, E3, E2, E1, E0);
  or or_2 (or_2_out, M118, M101, M84, M67, M50, M33, M16);
  or or_3 (or_3_out, M152, M135);
  or or_4 (or_4_out, E3, E2, E1, E0);
  or or_5 (or_5_out, M190, M150, M146, M133, M129, M112, M95, M78, M61, M44, M27, M10);
  or or_6 (or_6_out, M117, M100, M83, M66, M49, M32, M15);
  or or_7 (or_7_out, M175, M145, M141, M128, M124, M107, M90, M73, M56, M39, M22, M5);
  or or_8 (or_8_out, M170, M140, M136, M123, M119, M102, M85, M68, M51, M34, M17, M0);
  and and_9 (and_9_out, M180, T4);
  and and_10 (and_10_out, M201, Z);
  and and_11 (and_11_out, M204, ~Z);  // AND_Gate
  and and_12 (and_12_out, M207, C, ~Z);  // AND_Gate
  and and_13 (and_13_out, M210, ~C, Z);  // AND_Gate
  and and_14 (and_14_out, M213, C, Z);
  or or_9 (or_9_out, or_1_out, E24, E23, E22, E21, E20);
  and and_15 (and_15_out, or_4_out, M195);
  and and_16 (and_16_out, or_1_out, or_6_out);
  or or_10 (or_10_out, M151, M134);
  and and_17 (and_17_out, or_8_out, T5);
  and and_18 (and_18_out, or_1_out, or_2_out);
  and and_19 (and_19_out, or_9_out, or_3_out);
  and and_20 (and_20_out, or_9_out, or_10_out);
  or or_11 (or_11_out, M198, and_10_out, and_11_out, and_12_out, and_13_out, and_14_out);
  and and_21 (and_21_out, or_11_out, E0);
  or or_12 (or_12_out, and_18_out, and_19_out, and_15_out, or_5_out);
  or or_13 (or_13_out, and_16_out, and_20_out, or_7_out);
  or or_14 (or_14_out, M185, and_21_out);
  and and_22 (and_22_out, or_14_out, T3);
  and and_23 (and_23_out, or_12_out, T3);
  and and_24 (and_24_out, or_13_out, T4);
  or or_15 (AX_BUS, and_9_out, and_22_out);
  or or_16 (AX_LOAD, and_23_out, and_24_out, and_17_out);
endmodule

module BX (
  input  C,
  input  Z,
  input  T3,
  input  T4,
  input  T5,
  input  E0,
  input  E1,
  input  E2,
  input  E3,
  input  E4,
  input  E5,
  input  E6,
  input  E7,
  input  E8,
  input  E9,
  input  M1,
  input  M6,
  input  M11,
  input  M15,
  input  M16,
  input  M18,
  input  M23,
  input  M28,
  input  M32,
  input  M33,
  input  M35,
  input  M40,
  input  M45,
  input  M49,
  input  M50,
  input  M52,
  input  M57,
  input  M62,
  input  M66,
  input  M67,
  input  M69,
  input  M74,
  input  M79,
  input  M83,
  input  M84,
  input  M86,
  input  M91,
  input  M96,
  input  M100,
  input  M101,
  input  M103,
  input  M108,
  input  M113,
  input  M117,
  input  M118,
  input  M119,
  input  M120,
  input  M124,
  input  M125,
  input  M129,
  input  M130,
  input  M134,
  input  M135,
  input  M136,
  input  M137,
  input  M141,
  input  M142,
  input  M146,
  input  M147,
  input  M151,
  input  M152,
  input  M171,
  input  M176,
  input  M181,
  input  M186,
  input  M191,
  input  M195,
  input  M198,
  input  M201,
  input  M204,
  input  M207,
  input  M210,
  input  M213,
  input  M214,
  input  M215,
  input  M216,
  input  M217,
  input  M218,
  input  M219,
  input  M220,
  input  M221,
  output BX_INC,
  output BX_DEC,
  output BX_SHL,
  output BX_SHR,
  output BX_CIL,
  output BX_CIR,
  output BX_CML,
  output BX_CLR,
  output BX_LOAD,
  output BX_BUS
);

  wire and_9_out, and_10_out, and_11_out, and_12_out, and_13_out, and_14_out, and_15_out, and_16_out,
       and_17_out, and_18_out, and_19_out, and_20_out, and_21_out, and_22_out, and_23_out, and_24_out,
       or_1_out, or_2_out, or_3_out, or_4_out, or_5_out, or_6_out, or_7_out, or_8_out, or_9_out, or_10_out,
       or_12_out;

  and and_1 (BX_INC, M220, E1, T3);
  and and_2 (BX_DEC, M221, E1, T3);
  and and_3 (BX_SHL, M216, E1, T3);
  and and_4 (BX_SHR, M217, E1, T3);
  and and_5 (BX_CIL, M218, E1, T3);
  and and_6 (BX_CIR, M219, E1, T3);
  and and_7 (BX_CML, M215, E1, T3);
  and and_8 (BX_CLR, M214, E1, T3);
  or or_1 (or_1_out, E9, E8, E7, E6, E5);
  or or_2 (or_2_out, M118, M101, M84, M67, M50, M33, M16);
  or or_3 (or_3_out, M152, M135);
  or or_4 (or_4_out, E7, E6, E5, E4);
  or or_5 (or_5_out, M151, M134);
  and and_9 (and_9_out, M181, T4);
  and and_10 (and_10_out, M198, E1);
  and and_11 (and_11_out, M201, E1, Z);
  and and_12 (and_12_out, M204, E1, ~Z);  // AND_Gate
  and and_13 (and_13_out, M207, E1, ~Z, C);  // AND_Gate
  and and_14 (and_14_out, M210, E1, Z, ~C);  // AND_Gate
  and and_15 (and_15_out, M213, E1, Z, C);
  or or_6 (or_6_out, or_1_out, E4, E3, E2, E1, E0);
  or or_7 (or_7_out, M117, M100, M83, M66, M49, M32, M15);
  or or_8 (or_8_out, M171, M137, M136, M120, M119, M103, M86, M69, M52, M35, M18, M1);
  and and_16 (and_16_out, or_8_out, T5);
  and and_17 (and_17_out, or_1_out, or_2_out);
  and and_18 (and_18_out, or_6_out, or_3_out);
  and and_19 (and_19_out, M195, or_4_out);
  and and_20 (and_20_out, or_1_out, or_7_out);
  and and_21 (and_21_out, or_6_out, or_5_out);
  or or_9 (or_9_out, M186, and_10_out, and_11_out, and_12_out, and_13_out, and_14_out, and_15_out);
  and and_22 (and_22_out, or_9_out, T3);
  or or_10 (or_10_out, and_17_out, and_18_out, and_19_out, M191, M147, M146, M130, M129, M113, M96, M79, M62, M45, M28, M11);
  or or_11 (BX_BUS, and_9_out, and_22_out);
  and and_23 (and_23_out, or_10_out, T3);
  or or_12 (or_12_out, and_20_out, and_21_out, M176, M142, M141, M125, M124, M108, M91, M74, M57, M40, M23, M6);
  and and_24 (and_24_out, or_12_out, T4);
  or or_13 (BX_LOAD, and_23_out, and_24_out, and_16_out);
endmodule

module CX (
  input  C,
  input  Z,
  input  T3,
  input  T4,
  input  T5,
  input  E2,
  input  E5,
  input  E6,
  input  E7,
  input  E8,
  input  E9,
  input  E10,
  input  E11,
  input  E12,
  input  E13,
  input  E14,
  input  M2,
  input  M7,
  input  M12,
  input  M15,
  input  M16,
  input  M19,
  input  M24,
  input  M29,
  input  M32,
  input  M33,
  input  M36,
  input  M41,
  input  M46,
  input  M49,
  input  M50,
  input  M53,
  input  M58,
  input  M63,
  input  M66,
  input  M67,
  input  M70,
  input  M75,
  input  M80,
  input  M83,
  input  M84,
  input  M87,
  input  M92,
  input  M97,
  input  M100,
  input  M101,
  input  M104,
  input  M109,
  input  M114,
  input  M117,
  input  M118,
  input  M120,
  input  M121,
  input  M125,
  input  M126,
  input  M130,
  input  M131,
  input  M134,
  input  M135,
  input  M137,
  input  M138,
  input  M142,
  input  M143,
  input  M147,
  input  M148,
  input  M151,
  input  M152,
  input  M172,
  input  M177,
  input  M182,
  input  M187,
  input  M192,
  input  M195,
  input  M198,
  input  M201,
  input  M204,
  input  M207,
  input  M210,
  input  M213,
  input  M214,
  input  M215,
  input  M216,
  input  M217,
  input  M218,
  input  M219,
  input  M220,
  input  M221,
  output CX_INC,
  output CX_DEC,
  output CX_SHL,
  output CX_SHR,
  output CX_CIL,
  output CX_CIR,
  output CX_CML,
  output CX_CLR,
  output CX_LOAD,
  output CX_BUS
);

  wire and_9_out, and_10_out, and_11_out, and_12_out, and_13_out, and_14_out, and_15_out, and_16_out,
       and_17_out, and_18_out, and_19_out, and_20_out, and_21_out, and_22_out, and_23_out, and_24_out,
       or_1_out, or_2_out, or_3_out, or_4_out, or_5_out, or_6_out, or_7_out, or_8_out, or_9_out, or_10_out,
       or_11_out, or_12_out, or_14_out;

  and and_1 (CX_INC, M220, E2, T3);
  and and_2 (CX_DEC, M221, E2, T3);
  and and_3 (CX_SHL, M216, E2, T3);
  and and_4 (CX_SHR, M217, E2, T3);
  and and_5 (CX_CIL, M218, E2, T3);
  and and_6 (CX_CIR, M219, E2, T3);
  and and_7 (CX_CML, M215, E2, T3);
  and and_8 (CX_CLR, M214, E2, T3);
  or or_1 (or_1_out, E14, E13, E12, E11, E10);
  or or_2 (or_2_out, M118, M101, M84, M67, M50, M33, M16);
  or or_3 (or_3_out, M152, M135);
  or or_4 (or_4_out, E11, E10, E9, E8);
  or or_5 (or_5_out, M192, M148, M147, M131, M130, M114, M97, M80, M63, M46, M29, M12);
  or or_6 (or_6_out, M117, M100, M83, M66, M49, M32, M15);
  or or_7 (or_7_out, M151, M134);
  or or_8 (or_8_out, M177, M143, M142, M126, M125, M109, M92, M75, M58, M41, M24, M7);
  or or_9 (or_9_out, M172, M138, M137, M121, M120, M104, M87, M70, M53, M36, M19, M2);
  and and_9 (and_9_out, M182, T4);
  and and_10 (and_10_out, M198, E2);
  and and_11 (and_11_out, M201, E2, Z);
  and and_12 (and_12_out, M204, E2, ~Z);  // AND_Gate
  and and_13 (and_13_out, M207, E2, ~Z, C);  // AND_Gate
  and and_14 (and_14_out, M210, E2, Z, ~C);  // AND_Gate
  and and_15 (and_15_out, M213, E2, Z, C);
  or or_10 (or_10_out, or_1_out, E9, E8, E7, E6, E5);
  and and_16 (and_16_out, or_4_out, M195);
  and and_17 (and_17_out, or_1_out, or_6_out);
  and and_18 (and_18_out, or_9_out, T5);
  or or_11 (or_11_out, M187, and_10_out, and_11_out, and_12_out, and_13_out, and_14_out, and_15_out);
  and and_19 (and_19_out, or_1_out, or_2_out);
  and and_20 (and_20_out, or_10_out, or_3_out);
  and and_21 (and_21_out, or_10_out, or_7_out);
  and and_22 (and_22_out, or_11_out, T3);
  or or_12 (or_12_out, and_17_out, and_21_out, or_8_out);
  or or_13 (CX_BUS, and_9_out, and_22_out);
  or or_14 (or_14_out, and_19_out, and_20_out, and_16_out, or_5_out);
  and and_23 (and_23_out, or_12_out, T4);
  and and_24 (and_24_out, or_14_out, T3);
  or or_15 (CX_LOAD, and_24_out, and_23_out, and_18_out);
endmodule

module DX (
  input  C,
  input  Z,
  input  T3,
  input  T4,
  input  T5,
  input  E3,
  input  E10,
  input  E11,
  input  E12,
  input  E13,
  input  E14,
  input  E15,
  input  E16,
  input  E17,
  input  E18,
  input  E19,
  input  M3,
  input  M8,
  input  M13,
  input  M15,
  input  M16,
  input  M20,
  input  M25,
  input  M30,
  input  M32,
  input  M33,
  input  M37,
  input  M42,
  input  M47,
  input  M49,
  input  M50,
  input  M54,
  input  M59,
  input  M64,
  input  M66,
  input  M67,
  input  M71,
  input  M76,
  input  M81,
  input  M83,
  input  M84,
  input  M88,
  input  M93,
  input  M98,
  input  M100,
  input  M101,
  input  M105,
  input  M110,
  input  M115,
  input  M117,
  input  M118,
  input  M121,
  input  M122,
  input  M126,
  input  M127,
  input  M131,
  input  M132,
  input  M134,
  input  M135,
  input  M138,
  input  M139,
  input  M143,
  input  M144,
  input  M148,
  input  M149,
  input  M151,
  input  M152,
  input  M173,
  input  M178,
  input  M183,
  input  M188,
  input  M193,
  input  M195,
  input  M198,
  input  M201,
  input  M204,
  input  M207,
  input  M210,
  input  M213,
  input  M214,
  input  M215,
  input  M216,
  input  M217,
  input  M218,
  input  M219,
  input  M220,
  input  M221,
  output DX_INC,
  output DX_DEC,
  output CX_SHL,
  output DX_SHR,
  output DX_CIL,
  output DX_CIR,
  output DX_CML,
  output DX_CLR,
  output DX_LOAD,
  output DX_BUS
);

  wire and_9_out, and_10_out, and_11_out, and_12_out, and_13_out, and_14_out, and_15_out, and_16_out,
       and_17_out, and_18_out, and_19_out, and_20_out, and_21_out, and_22_out, and_23_out, and_24_out,
       or_1_out, or_2_out, or_3_out, or_4_out, or_5_out, or_6_out, or_7_out, or_8_out, or_9_out, or_10_out,
       or_11_out, or_12_out, or_14_out;

  and and_1 (DX_INC, M220, E3, T3);
  and and_2 (DX_DEC, M221, E3, T3);
  and and_3 (CX_SHL, M216, E3, T3);
  and and_4 (DX_SHR, M217, E3, T3);
  and and_5 (DX_CIL, M218, E3, T3);
  and and_6 (DX_CIR, M219, E3, T3);
  and and_7 (DX_CML, M215, E3, T3);
  and and_8 (DX_CLR, M214, E3, T3);
  or or_1 (or_1_out, E19, E18, E17, E16, E15);
  or or_2 (or_2_out, M118, M101, M84, M67, M50, M33, M16);
  or or_3 (or_3_out, M152, M135);
  or or_4 (or_4_out, E15, E14, E13, E12);
  or or_5 (or_5_out, M193, M149, M148, M132, M131, M115, M98, M81, M64, M47, M30, M13);
  or or_6 (or_6_out, M117, M100, M83, M66, M49, M32, M15);
  or or_7 (or_7_out, M151, M134);
  or or_8 (or_8_out, M178, M144, M143, M127, M126, M110, M93, M76, M59, M42, M25, M8);
  or or_9 (or_9_out, M173, M139, M138, M122, M121, M105, M88, M71, M54, M37, M20, M3);
  and and_9 (and_9_out, M183, T4);
  and and_10 (and_10_out, M198, E3);
  and and_11 (and_11_out, M201, E3, Z);
  and and_12 (and_12_out, M204, E3, ~Z);  // AND_Gate
  and and_13 (and_13_out, M207, E3, ~Z, C);  // AND_Gate
  and and_14 (and_14_out, M210, E3, Z, ~C);  // AND_Gate
  and and_15 (and_15_out, M213, E3, Z, C);
  and and_16 (and_16_out, or_1_out, or_6_out);
  and and_17 (and_17_out, or_9_out, T5);
  or or_10 (or_10_out, M188, and_10_out, and_11_out, and_12_out, and_13_out, and_14_out, and_15_out);
  and and_18 (and_18_out, or_1_out, or_2_out);
  or or_11 (or_11_out, or_1_out, E14, E13, E12, E11, E10);
  and and_19 (and_19_out, or_11_out, or_3_out);
  and and_20 (and_20_out, or_4_out, M195);
  and and_21 (and_21_out, or_11_out, or_7_out);
  and and_22 (and_22_out, or_10_out, T3);
  or or_12 (or_12_out, and_16_out, and_21_out, or_8_out);
  or or_13 (DX_BUS, and_9_out, and_22_out);
  or or_14 (or_14_out, and_18_out, and_19_out, and_20_out, or_5_out);
  and and_23 (and_23_out, or_12_out, T4);
  and and_24 (and_24_out, or_14_out, T3);
  or or_15 (DX_LOAD, and_24_out, and_23_out, and_17_out);
endmodule

module EX (
  input  C,
  input  Z,
  input  T3,
  input  T4,
  input  T5,
  input  E4,
  input  E15,
  input  E16,
  input  E17,
  input  E18,
  input  E19,
  input  E20,
  input  E21,
  input  E22,
  input  E23,
  input  E24,
  input  M4,
  input  M9,
  input  M14,
  input  M15,
  input  M16,
  input  M21,
  input  M26,
  input  M31,
  input  M32,
  input  M33,
  input  M38,
  input  M43,
  input  M48,
  input  M49,
  input  M50,
  input  M55,
  input  M60,
  input  M65,
  input  M66,
  input  M67,
  input  M72,
  input  M77,
  input  M82,
  input  M83,
  input  M84,
  input  M89,
  input  M94,
  input  M99,
  input  M100,
  input  M101,
  input  M106,
  input  M111,
  input  M116,
  input  M117,
  input  M118,
  input  M122,
  input  M123,
  input  M127,
  input  M128,
  input  M132,
  input  M133,
  input  M134,
  input  M135,
  input  M139,
  input  M140,
  input  M144,
  input  M145,
  input  M149,
  input  M150,
  input  M151,
  input  M152,
  input  M174,
  input  M179,
  input  M184,
  input  M189,
  input  M194,
  input  M195,
  input  M198,
  input  M201,
  input  M204,
  input  M207,
  input  M210,
  input  M213,
  input  M214,
  input  M215,
  input  M216,
  input  M217,
  input  M218,
  input  M219,
  input  M220,
  input  M221,
  output EX_INC,
  output EX_DEC,
  output EX_SHL,
  output EX_SHR,
  output EX_CIL,
  output EX_CIR,
  output EX_CML,
  output EX_CLR,
  output EX_LOAD,
  output EX_BUS
);

  wire and_9_out, and_10_out, and_11_out, and_12_out, and_13_out, and_14_out, and_15_out, and_16_out,
       and_17_out, and_18_out, and_19_out, and_20_out, and_21_out, and_22_out, and_23_out, and_24_out,
       or_1_out, or_2_out, or_3_out, or_4_out, or_5_out, or_6_out, or_7_out, or_8_out, or_9_out, or_10_out,
       or_11_out, or_12_out, or_14_out;

  and and_1 (EX_INC, M220, E4, T3);
  and and_2 (EX_DEC, M221, E4, T3);
  and and_3 (EX_SHL, M216, E4, T3);
  and and_4 (EX_SHR, M217, E4, T3);
  and and_5 (EX_CIL, M218, E4, T3);
  and and_6 (EX_CIR, M219, E4, T3);
  and and_7 (EX_CML, M215, E4, T3);
  and and_8 (EX_CLR, M214, E4, T3);
  or or_1 (or_1_out, E24, E23, E22, E21, E20);
  or or_2 (or_2_out, M118, M101, M84, M67, M50, M33, M16);
  or or_3 (or_3_out, M152, M135);
  or or_4 (or_4_out, E19, E18, E17, E16);
  or or_5 (or_5_out, M194, M150, M149, M133, M132, M116, M99, M82, M65, M48, M31, M14);
  or or_6 (or_6_out, M117, M100, M83, M66, M49, M32, M15);
  or or_7 (or_7_out, M151, M134);
  or or_8 (or_8_out, M179, M145, M144, M128, M127, M111, M94, M77, M60, M43, M26, M9);
  or or_9 (or_9_out, M174, M140, M139, M123, M122, M106, M89, M72, M55, M38, M21, M4);
  and and_9 (and_9_out, M184, T4);
  and and_10 (and_10_out, M198, E4);
  and and_11 (and_11_out, M201, E4, Z);
  and and_12 (and_12_out, M204, E4, ~Z);  // AND_Gate
  and and_13 (and_13_out, M207, E4, ~Z, C);  // AND_Gate
  and and_14 (and_14_out, M210, E4, Z, ~C);  // AND_Gate
  and and_15 (and_15_out, M213, E4, Z, C);
  and and_16 (and_16_out, or_1_out, or_6_out);
  and and_17 (and_17_out, or_9_out, T5);
  or or_10 (or_10_out, M189, and_10_out, and_11_out, and_12_out, and_13_out, and_14_out, and_15_out);
  and and_18 (and_18_out, or_1_out, or_2_out);
  or or_11 (or_11_out, or_1_out, E19, E18, E17, E16, E15);
  and and_19 (and_19_out, or_11_out, or_3_out);
  and and_20 (and_20_out, or_4_out, M195);
  and and_21 (and_21_out, or_11_out, or_7_out);
  and and_22 (and_22_out, or_10_out, T3);
  or or_12 (or_12_out, and_16_out, and_21_out, or_8_out);
  or or_13 (EX_BUS, and_9_out, and_22_out);
  or or_14 (or_14_out, and_18_out, and_19_out, and_20_out, or_5_out);
  and and_23 (and_23_out, or_12_out, T4);
  and and_24 (and_24_out, or_14_out, T3);
  or or_15 (EX_LOAD, and_24_out, and_23_out, and_17_out);
endmodule

module GENERAL_PURPOSE (
  input  E0,
  input  E1,
  input  E2,
  input  M0,
  input  M1,
  input  M2,
  input  M3,
  input  M4,
  input  M5,
  input  M6,
  input  M7,
  input  M8,
  input  M9,
  input  M10,
  input  M11,
  input  M12,
  input  M13,
  input  M14,
  input  M15,
  input  M16,
  input  M17,
  input  M18,
  input  M19,
  input  M20,
  input  M21,
  input  M22,
  input  M23,
  input  M24,
  input  M25,
  input  M26,
  input  M27,
  input  M28,
  input  M29,
  input  M30,
  input  M31,
  input  M32,
  input  M33,
  input  M34,
  input  M35,
  input  M36,
  input  M37,
  input  M38,
  input  M39,
  input  M40,
  input  M41,
  input  M42,
  input  M43,
  input  M44,
  input  M45,
  input  M46,
  input  M47,
  input  M48,
  input  M49,
  input  M50,
  input  M51,
  input  M52,
  input  M53,
  input  M54,
  input  M55,
  input  M56,
  input  M57,
  input  M58,
  input  M59,
  input  M60,
  input  M61,
  input  M62,
  input  M63,
  input  M64,
  input  M65,
  input  M66,
  input  M67,
  input  M68,
  input  M69,
  input  M70,
  input  M71,
  input  M72,
  input  M73,
  input  M74,
  input  M75,
  input  M76,
  input  M77,
  input  M78,
  input  M79,
  input  M80,
  input  M81,
  input  M82,
  input  M83,
  input  M84,
  input  M85,
  input  M86,
  input  M87,
  input  M88,
  input  M89,
  input  M90,
  input  M91,
  input  M92,
  input  M93,
  input  M94,
  input  M95,
  input  M96,
  input  M97,
  input  M98,
  input  M99,
  input  M100,
  input  M101,
  input  M102,
  input  M103,
  input  M104,
  input  M105,
  input  M106,
  input  M107,
  input  M108,
  input  M109,
  input  M110,
  input  M111,
  input  M112,
  input  M113,
  input  M114,
  input  M115,
  input  M116,
  input  M117,
  input  M118,
  input  M119,
  input  M120,
  input  M121,
  input  M122,
  input  M123,
  input  M124,
  input  M125,
  input  M126,
  input  M127,
  input  M128,
  input  M129,
  input  M130,
  input  M131,
  input  M132,
  input  M133,
  input  M134,
  input  M135,
  input  M136,
  input  M137,
  input  M138,
  input  M139,
  input  M140,
  input  M141,
  input  M142,
  input  M143,
  input  M144,
  input  M145,
  input  M146,
  input  M147,
  input  M148,
  input  M149,
  input  M150,
  input  M151,
  input  M152,
  input  M170,
  input  M171,
  input  M172,
  input  M173,
  input  M174,
  input  M175,
  input  M176,
  input  M177,
  input  M178,
  input  M179,
  input  M180,
  input  M181,
  input  M182,
  input  M183,
  input  M184,
  input  M185,
  input  M186,
  input  M187,
  input  M188,
  input  M189,
  input  M190,
  input  M191,
  input  M192,
  input  M193,
  input  M194,
  input  M195,
  input  M198,
  input  M201,
  input  M204,
  input  M207,
  input  M210,
  input  M213,
  input  M214,
  input  M215,
  input  M216,
  input  M217,
  input  M218,
  input  M219,
  input  M220,
  input  M221,
  input  E3,
  input  E4,
  input  E5,
  input  E6,
  input  E7,
  input  E8,
  input  E9,
  input  E10,
  input  E11,
  input  E12,
  input  E13,
  input  E14,
  input  E15,
  input  E16,
  input  E17,
  input  E18,
  input  E19,
  input  E20,
  input  E21,
  input  E22,
  input  E23,
  input  E24,
  input  T3,
  input  T4,
  input  T5,
  input  C,
  input  Z,
  output AX_INC,
  output AX_DEX,
  output AX_SHL,
  output AX_SHR,
  output AX_CIL,
  output AX_CIR,
  output AX_CML,
  output AX_CLR,
  output AX_LOAD,
  output AX_BUS,
  output BX_INC,
  output BX_DEX,
  output BX_SHL,
  output BX_SHR,
  output BX_CIL,
  output BX_CIR,
  output BX_CML,
  output BX_CLR,
  output BX_LOAD,
  output BX_BUS,
  output CX_INC,
  output CX_DEX,
  output CX_SHL,
  output CX_SHR,
  output CX_CIL,
  output CX_CIR,
  output CX_CML,
  output CX_CLR,
  output CX_LOAD,
  output CX_BUS,
  output DX_INC,
  output DX_DEX,
  output DX_SHL,
  output DX_SHR,
  output DX_CIL,
  output DX_CIR,
  output DX_CML,
  output DX_CLR,
  output DX_LOAD,
  output DX_BUS,
  output EX_INC,
  output EX_DEX,
  output EX_SHL,
  output EX_SHR,
  output EX_CIL,
  output EX_CIR,
  output EX_CML,
  output EX_CLR,
  output EX_LOAD,
  output EX_BUS
);

  AX ax_1 (
    .C(C), .Z(Z), .T3(T3), .T4(T4), .T5(T5), .E0(E0), .E1(E1), .E2(E2), .E3(E3), .E4(E4), .E20(E20),
    .E21(E21), .E22(E22), .E23(E23), .E24(E24), .M0(M0), .M5(M5), .M10(M10), .M15(M15), .M16(M16), .M17(M17),
    .M22(M22), .M27(M27), .M32(M32), .M33(M33), .M34(M34), .M39(M39), .M44(M44), .M49(M49), .M50(M50),
    .M51(M51), .M56(M56), .M61(M61), .M66(M66), .M67(M67), .M68(M68), .M73(M73), .M78(M78), .M83(M83),
    .M84(M84), .M85(M85), .M90(M90), .M95(M95), .M100(M100), .M101(M101), .M102(M102), .M107(M107),
    .M112(M112), .M117(M117), .M118(M118), .M119(M119), .M123(M123), .M124(M124), .M128(M128), .M129(M129),
    .M133(M133), .M134(M134), .M135(M135), .M136(M136), .M140(M140), .M141(M141), .M145(M145), .M146(M146),
    .M150(M150), .M151(M151), .M152(M152), .M170(M170), .M175(M175), .M180(M180), .M185(M185), .M190(M190),
    .M195(M195), .M198(M198), .M201(M201), .M204(M204), .M207(M207), .M210(M210), .M213(M213), .M214(M214),
    .M215(M215), .M216(M216), .M217(M217), .M218(M218), .M219(M219), .M220(M220), .M221(M221),
    .AX_INC(AX_INC), .AX_DEC(AX_DEX), .AX_SHL(AX_SHL), .AX_SHR(AX_SHR), .AX_CIL(AX_CIL), .AX_CIR(AX_CIR),
    .AX_CML(AX_CML), .AX_CLR(AX_CLR), .AX_LOAD(AX_LOAD), .AX_BUS(AX_BUS));
  BX bx_1 (
    .C(C), .Z(Z), .T3(T3), .T4(T4), .T5(T5), .E0(E0), .E1(E1), .E2(E2), .E3(E3), .E4(E4), .E5(E5), .E6(E6),
    .E7(E7), .E8(E8), .E9(E9), .M1(M1), .M6(M6), .M11(M11), .M15(M15), .M16(M16), .M18(M18), .M23(M23),
    .M28(M28), .M32(M32), .M33(M33), .M35(M35), .M40(M40), .M45(M45), .M49(M49), .M50(M50), .M52(M52),
    .M57(M57), .M62(M62), .M66(M66), .M67(M67), .M69(M69), .M74(M74), .M79(M79), .M83(M83), .M84(M84),
    .M86(M86), .M91(M91), .M96(M96), .M100(M100), .M101(M101), .M103(M103), .M108(M108), .M113(M113),
    .M117(M117), .M118(M118), .M119(M119), .M120(M120), .M124(M124), .M125(M125), .M129(M129), .M130(M130),
    .M134(M134), .M135(M135), .M136(M136), .M137(M137), .M141(M141), .M142(M142), .M146(M146), .M147(M147),
    .M151(M151), .M152(M152), .M171(M171), .M176(M176), .M181(M181), .M186(M186), .M191(M191), .M195(M195),
    .M198(M198), .M201(M201), .M204(M204), .M207(M207), .M210(M210), .M213(M213), .M214(M214), .M215(M215),
    .M216(M216), .M217(M217), .M218(M218), .M219(M219), .M220(M220), .M221(M221), .BX_INC(BX_INC),
    .BX_DEC(BX_DEX), .BX_SHL(BX_SHL), .BX_SHR(BX_SHR), .BX_CIL(BX_CIL), .BX_CIR(BX_CIR), .BX_CML(BX_CML),
    .BX_CLR(BX_CLR), .BX_LOAD(BX_LOAD), .BX_BUS(BX_BUS));
  CX cx_1 (
    .C(C), .Z(Z), .T3(T3), .T4(T4), .T5(T5), .E2(E2), .E5(E5), .E6(E6), .E7(E7), .E8(E8), .E9(E9), .E10(E10),
    .E11(E11), .E12(E12), .E13(E13), .E14(E14), .M2(M2), .M7(M7), .M12(M12), .M15(M15), .M16(M16), .M19(M19),
    .M24(M24), .M29(M29), .M32(M32), .M33(M33), .M36(M36), .M41(M41), .M46(M46), .M49(M49), .M50(M50),
    .M53(M53), .M58(M58), .M63(M63), .M66(M66), .M67(M67), .M70(M70), .M75(M75), .M80(M80), .M83(M83),
    .M84(M84), .M87(M87), .M92(M92), .M97(M97), .M100(M100), .M101(M101), .M104(M104), .M109(M109),
    .M114(M114), .M117(M117), .M118(M118), .M120(M120), .M121(M121), .M125(M125), .M126(M126), .M130(M130),
    .M131(M131), .M134(M134), .M135(M135), .M137(M137), .M138(M138), .M142(M142), .M143(M143), .M147(M147),
    .M148(M148), .M151(M151), .M152(M152), .M172(M172), .M177(M177), .M182(M182), .M187(M187), .M192(M192),
    .M195(M195), .M198(M198), .M201(M201), .M204(M204), .M207(M207), .M210(M210), .M213(M213), .M214(M214),
    .M215(M215), .M216(M216), .M217(M217), .M218(M218), .M219(M219), .M220(M220), .M221(M221),
    .CX_INC(CX_INC), .CX_DEC(CX_DEX), .CX_SHL(CX_SHL), .CX_SHR(CX_SHR), .CX_CIL(CX_CIL), .CX_CIR(CX_CIR),
    .CX_CML(CX_CML), .CX_CLR(CX_CLR), .CX_LOAD(CX_LOAD), .CX_BUS(CX_BUS));
  DX dx_1 (
    .C(C), .Z(Z), .T3(T3), .T4(T4), .T5(T5), .E3(E3), .E10(E10), .E11(E11), .E12(E12), .E13(E13), .E14(E14),
    .E15(E15), .E16(E16), .E17(E17), .E18(E18), .E19(E19), .M3(M3), .M8(M8), .M13(M13), .M15(M15), .M16(M16),
    .M20(M20), .M25(M25), .M30(M30), .M32(M32), .M33(M33), .M37(M37), .M42(M42), .M47(M47), .M49(M49),
    .M50(M50), .M54(M54), .M59(M59), .M64(M64), .M66(M66), .M67(M67), .M71(M71), .M76(M76), .M81(M81),
    .M83(M83), .M84(M84), .M88(M88), .M93(M93), .M98(M98), .M100(M100), .M101(M101), .M105(M105),
    .M110(M110), .M115(M115), .M117(M117), .M118(M118), .M121(M121), .M122(M122), .M126(M126), .M127(M127),
    .M131(M131), .M132(M132), .M134(M134), .M135(M135), .M138(M138), .M139(M139), .M143(M143), .M144(M144),
    .M148(M148), .M149(M149), .M151(M151), .M152(M152), .M173(M173), .M178(M178), .M183(M183), .M188(M188),
    .M193(M193), .M195(M195), .M198(M198), .M201(M201), .M204(M204), .M207(M207), .M210(M210), .M213(M213),
    .M214(M214), .M215(M215), .M216(M216), .M217(M217), .M218(M218), .M219(M219), .M220(M220), .M221(M221),
    .DX_INC(DX_INC), .DX_DEC(DX_DEX), .CX_SHL(DX_SHL), .DX_SHR(DX_SHR), .DX_CIL(DX_CIL), .DX_CIR(DX_CIR),
    .DX_CML(DX_CML), .DX_CLR(DX_CLR), .DX_LOAD(DX_LOAD), .DX_BUS(DX_BUS));
  EX ex_1 (
    .C(C), .Z(Z), .T3(T3), .T4(T4), .T5(T5), .E4(E4), .E15(E15), .E16(E16), .E17(E17), .E18(E18), .E19(E19),
    .E20(E20), .E21(E21), .E22(E22), .E23(E23), .E24(E24), .M4(M4), .M9(M9), .M14(M14), .M15(M15), .M16(M16),
    .M21(M21), .M26(M26), .M31(M31), .M32(M32), .M33(M33), .M38(M38), .M43(M43), .M48(M48), .M49(M49),
    .M50(M50), .M55(M55), .M60(M60), .M65(M65), .M66(M66), .M67(M67), .M72(M72), .M77(M77), .M82(M82),
    .M83(M83), .M84(M84), .M89(M89), .M94(M94), .M99(M99), .M100(M100), .M101(M101), .M106(M106),
    .M111(M111), .M116(M116), .M117(M117), .M118(M118), .M122(M122), .M123(M123), .M127(M127), .M128(M128),
    .M132(M132), .M133(M133), .M134(M134), .M135(M135), .M139(M139), .M140(M140), .M144(M144), .M145(M145),
    .M149(M149), .M150(M150), .M151(M151), .M152(M152), .M174(M174), .M179(M179), .M184(M184), .M189(M189),
    .M194(M194), .M195(M195), .M198(M198), .M201(M201), .M204(M204), .M207(M207), .M210(M210), .M213(M213),
    .M214(M214), .M215(M215), .M216(M216), .M217(M217), .M218(M218), .M219(M219), .M220(M220), .M221(M221),
    .EX_INC(EX_INC), .EX_DEC(EX_DEX), .EX_SHL(EX_SHL), .EX_SHR(EX_SHR), .EX_CIL(EX_CIL), .EX_CIR(EX_CIR),
    .EX_CML(EX_CML), .EX_CLR(EX_CLR), .EX_LOAD(EX_LOAD), .EX_BUS(EX_BUS));
endmodule

module MEMORY (
  input  T3,
  input  T4,
  input  E0,
  input  E1,
  input  E2,
  input  E3,
  input  E4,
  input  E5,
  input  E6,
  input  E7,
  input  E8,
  input  E9,
  input  E10,
  input  E11,
  input  E12,
  input  E13,
  input  E14,
  input  E15,
  input  E16,
  input  E17,
  input  E18,
  input  E19,
  input  E20,
  input  E21,
  input  E22,
  input  E23,
  input  E24,
  input  M0,
  input  M1,
  input  M2,
  input  M3,
  input  M4,
  input  M5,
  input  M6,
  input  M7,
  input  M8,
  input  M9,
  input  M15,
  input  M17,
  input  M18,
  input  M19,
  input  M20,
  input  M21,
  input  M22,
  input  M23,
  input  M24,
  input  M25,
  input  M26,
  input  M32,
  input  M34,
  input  M35,
  input  M36,
  input  M37,
  input  M38,
  input  M39,
  input  M40,
  input  M41,
  input  M42,
  input  M43,
  input  M49,
  input  M51,
  input  M52,
  input  M53,
  input  M54,
  input  M55,
  input  M56,
  input  M57,
  input  M58,
  input  M59,
  input  M60,
  input  M66,
  input  M68,
  input  M69,
  input  M70,
  input  M71,
  input  M72,
  input  M73,
  input  M74,
  input  M75,
  input  M76,
  input  M77,
  input  M83,
  input  M85,
  input  M86,
  input  M87,
  input  M88,
  input  M89,
  input  M90,
  input  M91,
  input  M92,
  input  M93,
  input  M94,
  input  M100,
  input  M102,
  input  M103,
  input  M104,
  input  M105,
  input  M106,
  input  M107,
  input  M108,
  input  M109,
  input  M110,
  input  M111,
  input  M117,
  input  M119,
  input  M120,
  input  M121,
  input  M122,
  input  M123,
  input  M124,
  input  M125,
  input  M126,
  input  M127,
  input  M128,
  input  M134,
  input  M136,
  input  M137,
  input  M138,
  input  M139,
  input  M140,
  input  M141,
  input  M142,
  input  M143,
  input  M144,
  input  M145,
  input  M151,
  input  M153,
  input  M154,
  input  M155,
  input  M156,
  input  M157,
  input  M158,
  input  M159,
  input  M160,
  input  M161,
  input  M162,
  input  M168,
  input  M170,
  input  M171,
  input  M172,
  input  M173,
  input  M174,
  input  M175,
  input  M176,
  input  M177,
  input  M178,
  input  M179,
  input  M180,
  input  M181,
  input  M182,
  input  M183,
  input  M184,
  input  M185,
  input  M186,
  input  M187,
  input  M188,
  input  M189,
  input  M196,
  input  M199,
  input  M202,
  input  M205,
  input  M208,
  input  M211,
  output STR,
  output BUS,
  output [2:0] MUX
);

  wire and_1_out, and_2_out, and_3_out, and_4_out, and_5_out, and_6_out, and_7_out, and_8_out, and_9_out,
       and_10_out, and_11_out, and_12_out, or_1_out, or_2_out, or_3_out, or_4_out, or_5_out, or_6_out,
       or_7_out, or_8_out, or_9_out, or_10_out, or_11_out, or_12_out, or_13_out, or_14_out, or_15_out,
       or_16_out, or_17_out, or_18_out, or_19_out, or_20_out, or_21_out, or_22_out, or_23_out, or_24_out,
       or_25_out, or_27_out, or_28_out;

  or or_1 (or_1_out, M189, M188, M187, M186, M185);
  or or_2 (or_2_out, M184, M183, M182, M181, M180);
  or or_3 (or_3_out, E24, E23, E22, E21, E20, E19, E18, E17, E16, E15, E14, E13, E12, E11, E10, E9, E8, E7, E6, E5, E4, E3, E2, E1, E0);
  or or_4 (or_4_out, M168, M151, M134, M117, M100, M83, M66, M49, M32, M15);
  or or_5 (or_5_out, M211, M208, M205, M202, M199, M196, M184, M183, M182, M181, M180, M179, M178, M177, M176, M175, M174, M173, M172, M171, M170, M162, M161, M160, M159, M158, M157, M156, M155, M154, M153, M145);
  or or_6 (or_6_out, or_5_out, M144, M143, M142, M141, M140, M139, M138, M137, M136, M128, M127, M126, M125, M124, M123, M122, M121, M120, M119, M111, M110, M109, M108, M107, M106, M105, M104, M103, M102, M94, M93);
  or or_7 (or_7_out, or_6_out, M92, M91, M90, M89, M88, M87, M86, M85, M77, M76, M75, M74, M73, M72, M71, M70, M69, M68, M60, M59, M58, M57, M56, M55, M54, M53, M52, M51, M43, M42, M41);
  or or_8 (or_8_out, or_7_out, M40, M39, M38, M37, M36, M35, M34, M26, M25, M24, M23, M22, M21, M20, M19, M18, M17, M9, M8, M7, M6, M5, M4, M3, M2, M1, M0);
  or or_9 (or_9_out, M174, M173, M172, M171, M170, M157, M156, M155, M154, M153, M140, M139, M138, M137, M136, M123, M122, M121, M120, M119, M106, M105);
  or or_10 (or_10_out, or_9_out, M104, M103, M102, M89, M88, M87, M86, M85, M72, M71, M70, M69, M68, M55, M54, M53, M52, M51, M38, M37, M36);
  or or_11 (or_11_out, or_10_out, M35, M34, M21, M20, M19, M18, M17, M4, M3, M2, M1, M0);
  or or_12 (or_12_out, M211, M208, M205, M202, M199, M196, M189, M188, M187, M186, M185, M184, M183, M182, M181, M180, M179, M178, M177, M176, M175, M174);
  or or_13 (or_13_out, or_12_out, M173, M172, M171, M170, M162, M161, M160, M159, M158, M157, M156, M155, M154, M153, M145, M144, M143, M142, M141, M140, M139);
  or or_14 (or_14_out, or_13_out, M138, M137, M136, M128, M127, M126, M125, M124, M123, M122, M121, M120, M119, M111, M110, M109, M108, M107, M106, M105, M104);
  or or_15 (or_15_out, or_14_out, M103, M102, M94, M93, M92, M91, M90, M89, M88, M87, M86, M85, M77, M76, M75, M74, M73, M72, M71, M70, M69);
  or or_16 (or_16_out, or_15_out, M68, M60, M59, M58, M57, M56, M55, M54, M53, M52, M51, M43, M42, M41, M40, M39, M38, M37, M36, M35, M34);
  or or_17 (or_17_out, or_16_out, M26, M25, M24, M23, M22, M21, M20, M19, M18, M17, M9, M8, M7, M6, M5, M4, M3, M2, M1, M0);
  or or_18 (or_18_out, M184, M183, M182, M181, M180, M174, M173, M172, M171, M170, M157, M156, M155, M154, M153, M140, M139, M138, M137, M136, M123, M122, M121, M120, M119, M106, M105, M104, M103, M102, M89, M88);
  or or_19 (or_19_out, or_18_out, M87, M86, M85, M72, M71, M70, M69, M68, M55, M54, M53, M52, M51, M38, M37, M36, M35, M34, M21, M20, M19, M18, M17, M4, M3, M2, M1, M0);
  or or_20 (or_20_out, E20, E15, E10, E5, E0);
  or or_21 (or_21_out, E21, E16, E11, E6, E1);
  or or_22 (or_22_out, E22, E17, E12, E7, E2);
  or or_23 (or_23_out, E23, E18, E13, E8, E3);
  or or_24 (or_24_out, E24, E19, E14, E9, E4);
  and and_1 (and_1_out, or_1_out, T3);
  and and_2 (and_2_out, T4, or_2_out);
  and and_3 (and_3_out, or_11_out, T4);
  or or_25 (or_25_out, M168, M151, M134, M117, M100, M83, M66, M49, M32, M15);
  or or_26 (STR, and_1_out, and_2_out);
  and and_4 (and_4_out, or_3_out, or_4_out);
  and and_5 (and_5_out, or_17_out, T3);
  and and_6 (and_6_out, or_19_out, T4);
  or or_27 (or_27_out, and_4_out, or_8_out);
  and and_7 (and_7_out, or_27_out, T3);
  or or_28 (or_28_out, and_5_out, and_6_out);
  and and_8 (and_8_out, or_25_out, or_20_out, T3);
  and and_9 (and_9_out, or_25_out, or_21_out, T3);
  and and_10 (and_10_out, or_25_out, or_22_out, T3);
  and and_11 (and_11_out, or_25_out, or_23_out, T3);
  and and_12 (and_12_out, or_25_out, or_24_out, T3);
  or or_29 (BUS, and_7_out, and_3_out);
  assign MUX = or_28_out ? 3'b000 : 3'bz;  // Controlled_Buffer controlled_buffer_1
  assign MUX = and_8_out ? 3'b001 : 3'bz;  // Controlled_Buffer controlled_buffer_2
  assign MUX = and_9_out ? 3'b010 : 3'bz;  // Controlled_Buffer controlled_buffer_3
  assign MUX = and_10_out ? 3'b011 : 3'bz;  // Controlled_Buffer controlled_buffer_4
  assign MUX = and_11_out ? 3'b100 : 3'bz;  // Controlled_Buffer controlled_buffer_5
  assign MUX = and_12_out ? 3'b101 : 3'bz;  // Controlled_Buffer controlled_buffer_6
endmodule

module ALU (
  input  T3,
  input  T4,
  input  T5,
  input  E0,
  input  E1,
  input  E2,
  input  E3,
  input  E4,
  input  E5,
  input  E6,
  input  E7,
  input  E8,
  input  E9,
  input  E10,
  input  E11,
  input  E12,
  input  E13,
  input  E14,
  input  E15,
  input  E16,
  input  E17,
  input  E18,
  input  E19,
  input  E20,
  input  E21,
  input  E22,
  input  E23,
  input  E24,
  input  M0,
  input  M1,
  input  M2,
  input  M3,
  input  M4,
  input  M5,
  input  M6,
  input  M7,
  input  M8,
  input  M9,
  input  M10,
  input  M11,
  input  M12,
  input  M13,
  input  M14,
  input  M15,
  input  M16,
  input  M17,
  input  M18,
  input  M19,
  input  M20,
  input  M21,
  input  M22,
  input  M23,
  input  M24,
  input  M25,
  input  M26,
  input  M27,
  input  M28,
  input  M29,
  input  M30,
  input  M31,
  input  M32,
  input  M33,
  input  M34,
  input  M35,
  input  M36,
  input  M37,
  input  M38,
  input  M39,
  input  M40,
  input  M41,
  input  M42,
  input  M43,
  input  M44,
  input  M45,
  input  M46,
  input  M47,
  input  M48,
  input  M49,
  input  M50,
  input  M51,
  input  M52,
  input  M53,
  input  M54,
  input  M55,
  input  M56,
  input  M57,
  input  M58,
  input  M59,
  input  M60,
  input  M61,
  input  M62,
  input  M63,
  input  M64,
  input  M65,
  input  M66,
  input  M67,
  input  M68,
  input  M69,
  input  M70,
  input  M71,
  input  M72,
  input  M73,
  input  M74,
  input  M75,
  input  M76,
  input  M77,
  input  M78,
  input  M79,
  input  M80,
  input  M81,
  input  M82,
  input  M83,
  input  M84,
  input  M85,
  input  M86,
  input  M87,
  input  M88,
  input  M89,
  input  M90,
  input  M91,
  input  M92,
  input  M93,
  input  M94,
  input  M95,
  input  M96,
  input  M97,
  input  M98,
  input  M99,
  input  M100,
  input  M101,
  input  M102,
  input  M103,
  input  M104,
  input  M105,
  input  M106,
  input  M107,
  input  M108,
  input  M109,
  input  M110,
  input  M111,
  input  M112,
  input  M113,
  input  M114,
  input  M115,
  input  M116,
  input  M117,
  input  M118,
  input  M119,
  input  M120,
  input  M121,
  input  M122,
  input  M123,
  input  M124,
  input  M125,
  input  M126,
  input  M127,
  input  M128,
  input  M129,
  input  M130,
  input  M131,
  input  M132,
  input  M133,
  input  M134,
  input  M135,
  input  M136,
  input  M137,
  input  M138,
  input  M139,
  input  M140,
  input  M141,
  input  M142,
  input  M143,
  input  M144,
  input  M145,
  input  M146,
  input  M147,
  input  M148,
  input  M149,
  input  M150,
  input  M151,
  input  M152,
  input  M153,
  input  M154,
  input  M155,
  input  M156,
  input  M157,
  input  M158,
  input  M159,
  input  M160,
  input  M161,
  input  M162,
  input  M163,
  input  M164,
  input  M165,
  input  M166,
  input  M167,
  input  M168,
  input  M169,
  input  M170,
  input  M171,
  input  M172,
  input  M173,
  input  M174,
  input  M175,
  input  M176,
  input  M177,
  input  M178,
  input  M179,
  input  M190,
  input  M191,
  input  M192,
  input  M193,
  input  M194,
  input  M195,
  output AX_1,
  output BX_1,
  output CX_1,
  output DX_1,
  output EX_1,
  output AND,
  output OR,
  output XOR,
  output ADD,
  output ADC,
  output SUB,
  output SBB,
  output MUL,
  output DIV,
  output CMP,
  output LOAD,
  output AX_2,
  output BX_2,
  output CX_2,
  output DX_2,
  output EX_2,
  output DR_2,
  output IR_2
);

  INSTRUCTION instruction_1 (
    .T3(T3), .T4(T4), .T5(T5), .M0(M0), .M1(M1), .M2(M2), .M3(M3), .M4(M4), .M5(M5), .M6(M6), .M7(M7),
    .M8(M8), .M9(M9), .M10(M10), .M11(M11), .M12(M12), .M13(M13), .M14(M14), .M15(M15), .M16(M16), .M17(M17),
    .M18(M18), .M19(M19), .M20(M20), .M21(M21), .M22(M22), .M23(M23), .M24(M24), .M25(M25), .M26(M26),
    .M27(M27), .M28(M28), .M29(M29), .M30(M30), .M31(M31), .M32(M32), .M33(M33), .M34(M34), .M35(M35),
    .M36(M36), .M37(M37), .M38(M38), .M39(M39), .M40(M40), .M41(M41), .M42(M42), .M43(M43), .M44(M44),
    .M45(M45), .M46(M46), .M47(M47), .M48(M48), .M49(M49), .M50(M50), .M51(M51), .M52(M52), .M53(M53),
    .M54(M54), .M55(M55), .M56(M56), .M57(M57), .M58(M58), .M59(M59), .M60(M60), .M61(M61), .M62(M62),
    .M63(M63), .M64(M64), .M65(M65), .M66(M66), .M67(M67), .M68(M68), .M69(M69), .M70(M70), .M71(M71),
    .M72(M72), .M73(M73), .M74(M74), .M75(M75), .M76(M76), .M77(M77), .M78(M78), .M79(M79), .M80(M80),
    .M81(M81), .M82(M82), .M83(M83), .M84(M84), .M85(M85), .M86(M86), .M87(M87), .M88(M88), .M89(M89),
    .M90(M90), .M91(M91), .M92(M92), .M93(M93), .M94(M94), .M95(M95), .M96(M96), .M97(M97), .M98(M98),
    .M99(M99), .M100(M100), .M101(M101), .M102(M102), .M103(M103), .M104(M104), .M105(M105), .M106(M106),
    .M107(M107), .M108(M108), .M109(M109), .M110(M110), .M111(M111), .M112(M112), .M113(M113), .M114(M114),
    .M115(M115), .M116(M116), .M117(M117), .M118(M118), .M119(M119), .M120(M120), .M121(M121), .M122(M122),
    .M123(M123), .M124(M124), .M125(M125), .M126(M126), .M127(M127), .M128(M128), .M129(M129), .M130(M130),
    .M131(M131), .M132(M132), .M133(M133), .M134(M134), .M135(M135), .M136(M136), .M137(M137), .M138(M138),
    .M139(M139), .M140(M140), .M141(M141), .M142(M142), .M143(M143), .M144(M144), .M145(M145), .M146(M146),
    .M147(M147), .M148(M148), .M149(M149), .M150(M150), .M151(M151), .M152(M152), .M153(M153), .M154(M154),
    .M155(M155), .M156(M156), .M157(M157), .M158(M158), .M159(M159), .M160(M160), .M161(M161), .M162(M162),
    .M163(M163), .M164(M164), .M165(M165), .M166(M166), .M167(M167), .M168(M168), .M169(M169), .M170(M170),
    .M171(M171), .M172(M172), .M173(M173), .M174(M174), .M175(M175), .M176(M176), .M177(M177), .M178(M178),
    .M179(M179), .M190(M190), .M191(M191), .M192(M192), .M193(M193), .M194(M194), .M195(M195), .AND(AND),
    .OR(OR), .XOR(XOR), .ADD(ADD), .ADC(ADC), .SUB(SUB), .SBB(SBB), .MUL(MUL), .DIV(DIV), .CMP(CMP),
    .LOAD(LOAD));
  FIRST_REGISTER first_register_1 (
    .T3(T3), .T4(T4), .T5(T5), .E0(E0), .E1(E1), .E2(E2), .E3(E3), .E4(E4), .E5(E5), .E6(E6), .E7(E7),
    .E8(E8), .E9(E9), .E10(E10), .E11(E11), .E12(E12), .E13(E13), .E14(E14), .E15(E15), .E16(E16), .E17(E17),
    .E18(E18), .E19(E19), .E20(E20), .E21(E21), .E22(E22), .E23(E23), .E24(E24), .M0(M0), .M1(M1), .M2(M2),
    .M3(M3), .M4(M4), .M5(M5), .M6(M6), .M7(M7), .M8(M8), .M9(M9), .M10(M10), .M11(M11), .M12(M12),
    .M13(M13), .M14(M14), .M15(M15), .M16(M16), .M17(M17), .M18(M18), .M19(M19), .M20(M20), .M21(M21),
    .M22(M22), .M23(M23), .M24(M24), .M25(M25), .M26(M26), .M27(M27), .M28(M28), .M29(M29), .M30(M30),
    .M31(M31), .M32(M32), .M33(M33), .M34(M34), .M35(M35), .M36(M36), .M37(M37), .M38(M38), .M39(M39),
    .M40(M40), .M41(M41), .M42(M42), .M43(M43), .M44(M44), .M45(M45), .M46(M46), .M47(M47), .M48(M48),
    .M49(M49), .M50(M50), .M51(M51), .M52(M52), .M53(M53), .M54(M54), .M55(M55), .M56(M56), .M57(M57),
    .M58(M58), .M59(M59), .M60(M60), .M61(M61), .M62(M62), .M63(M63), .M64(M64), .M65(M65), .M66(M66),
    .M67(M67), .M68(M68), .M69(M69), .M70(M70), .M71(M71), .M72(M72), .M73(M73), .M74(M74), .M75(M75),
    .M76(M76), .M77(M77), .M78(M78), .M79(M79), .M80(M80), .M81(M81), .M82(M82), .M83(M83), .M84(M84),
    .M85(M85), .M86(M86), .M87(M87), .M88(M88), .M89(M89), .M90(M90), .M91(M91), .M92(M92), .M93(M93),
    .M94(M94), .M95(M95), .M96(M96), .M97(M97), .M98(M98), .M99(M99), .M100(M100), .M101(M101), .M102(M102),
    .M103(M103), .M104(M104), .M105(M105), .M106(M106), .M107(M107), .M108(M108), .M109(M109), .M110(M110),
    .M111(M111), .M112(M112), .M113(M113), .M114(M114), .M115(M115), .M116(M116), .M117(M117), .M118(M118),
    .M119(M119), .M120(M120), .M121(M121), .M122(M122), .M123(M123), .M124(M124), .M125(M125), .M126(M126),
    .M127(M127), .M128(M128), .M129(M129), .M130(M130), .M131(M131), .M132(M132), .M133(M133), .M134(M134),
    .M135(M135), .M136(M136), .M137(M137), .M138(M138), .M139(M139), .M140(M140), .M141(M141), .M142(M142),
    .M143(M143), .M144(M144), .M145(M145), .M146(M146), .M147(M147), .M148(M148), .M149(M149), .M150(M150),
    .M151(M151), .M152(M152), .M153(M153), .M154(M154), .M155(M155), .M156(M156), .M157(M157), .M158(M158),
    .M159(M159), .M160(M160), .M161(M161), .M162(M162), .M163(M163), .M164(M164), .M165(M165), .M166(M166),
    .M167(M167), .M168(M168), .M169(M169), .M170(M170), .M171(M171), .M172(M172), .M173(M173), .M174(M174),
    .M175(M175), .M176(M176), .M177(M177), .M178(M178), .M179(M179), .M190(M190), .M191(M191), .M192(M192),
    .M193(M193), .M194(M194), .M195(M195), .AX(AX_1), .BX(BX_1), .CX(CX_1), .DX(DX_1), .EX(EX_1));
  SECOND_REGISTER second_register_1 (
    .T3(T3), .T4(T4), .T5(T5), .E0(E0), .E1(E1), .E2(E2), .E3(E3), .E4(E4), .E5(E5), .E6(E6), .E7(E7),
    .E8(E8), .E9(E9), .E10(E10), .E11(E11), .E12(E12), .E13(E13), .E14(E14), .E15(E15), .E16(E16), .E17(E17),
    .E18(E18), .E19(E19), .E20(E20), .E21(E21), .E22(E22), .E23(E23), .E24(E24), .M0(M0), .M1(M1), .M2(M2),
    .M3(M3), .M4(M4), .M5(M5), .M6(M6), .M7(M7), .M8(M8), .M9(M9), .M10(M10), .M11(M11), .M12(M12),
    .M13(M13), .M14(M14), .M15(M15), .M16(M16), .M17(M17), .M18(M18), .M19(M19), .M20(M20), .M21(M21),
    .M22(M22), .M23(M23), .M24(M24), .M25(M25), .M26(M26), .M27(M27), .M28(M28), .M29(M29), .M30(M30),
    .M31(M31), .M32(M32), .M33(M33), .M34(M34), .M35(M35), .M36(M36), .M37(M37), .M38(M38), .M39(M39),
    .M40(M40), .M41(M41), .M42(M42), .M43(M43), .M44(M44), .M45(M45), .M46(M46), .M47(M47), .M48(M48),
    .M49(M49), .M50(M50), .M51(M51), .M52(M52), .M53(M53), .M54(M54), .M55(M55), .M56(M56), .M57(M57),
    .M58(M58), .M59(M59), .M60(M60), .M61(M61), .M62(M62), .M63(M63), .M64(M64), .M65(M65), .M66(M66),
    .M67(M67), .M68(M68), .M69(M69), .M70(M70), .M71(M71), .M72(M72), .M73(M73), .M74(M74), .M75(M75),
    .M76(M76), .M77(M77), .M78(M78), .M79(M79), .M80(M80), .M81(M81), .M82(M82), .M83(M83), .M84(M84),
    .M85(M85), .M86(M86), .M87(M87), .M88(M88), .M89(M89), .M90(M90), .M91(M91), .M92(M92), .M93(M93),
    .M94(M94), .M95(M95), .M96(M96), .M97(M97), .M98(M98), .M99(M99), .M100(M100), .M101(M101), .M102(M102),
    .M103(M103), .M104(M104), .M105(M105), .M106(M106), .M107(M107), .M108(M108), .M109(M109), .M110(M110),
    .M111(M111), .M112(M112), .M113(M113), .M114(M114), .M115(M115), .M116(M116), .M117(M117), .M118(M118),
    .M119(M119), .M120(M120), .M121(M121), .M122(M122), .M123(M123), .M124(M124), .M125(M125), .M126(M126),
    .M127(M127), .M128(M128), .M129(M129), .M130(M130), .M131(M131), .M132(M132), .M133(M133), .M134(M134),
    .M135(M135), .M136(M136), .M137(M137), .M138(M138), .M139(M139), .M140(M140), .M141(M141), .M142(M142),
    .M143(M143), .M144(M144), .M145(M145), .M146(M146), .M147(M147), .M148(M148), .M149(M149), .M150(M150),
    .M151(M151), .M152(M152), .M153(M153), .M154(M154), .M155(M155), .M156(M156), .M157(M157), .M158(M158),
    .M159(M159), .M160(M160), .M161(M161), .M162(M162), .M163(M163), .M164(M164), .M165(M165), .M166(M166),
    .M167(M167), .M168(M168), .M169(M169), .M170(M170), .M171(M171), .M172(M172), .M173(M173), .M174(M174),
    .M175(M175), .M176(M176), .M177(M177), .M178(M178), .M179(M179), .M190(M190), .M191(M191), .M192(M192),
    .M193(M193), .M194(M194), .M195(M195), .AX(AX_2), .BX(BX_2), .CX(CX_2), .DX(DX_2), .EX(EX_2), .DR(DR_2),
    .IR(IR_2));
endmodule

// FIRST_REGISTER_SELECTOR
module FIRST_REGISTER (
  input  T3,
  input  T4,
  input  T5,
  input  E0,
  input  E1,
  input  E2,
  input  E3,
  input  E4,
  input  E5,
  input  E6,
  input  E7,
  input  E8,
  input  E9,
  input  E10,
  input  E11,
  input  E12,
  input  E13,
  input  E14,
  input  E15,
  input  E16,
  input  E17,
  input  E18,
  input  E19,
  input  E20,
  input  E21,
  input  E22,
  input  E23,
  input  E24,
  input  M0,
  input  M1,
  input  M2,
  input  M3,
  input  M4,
  input  M5,
  input  M6,
  input  M7,
  input  M8,
  input  M9,
  input  M10,
  input  M11,
  input  M12,
  input  M13,
  input  M14,
  input  M15,
  input  M16,
  input  M17,
  input  M18,
  input  M19,
  input  M20,
  input  M21,
  input  M22,
  input  M23,
  input  M24,
  input  M25,
  input  M26,
  input  M27,
  input  M28,
  input  M29,
  input  M30,
  input  M31,
  input  M32,
  input  M33,
  input  M34,
  input  M35,
  input  M36,
  input  M37,
  input  M38,
  input  M39,
  input  M40,
  input  M41,
  input  M42,
  input  M43,
  input  M44,
  input  M45,
  input  M46,
  input  M47,
  input  M48,
  input  M49,
  input  M50,
  input  M51,
  input  M52,
  input  M53,
  input  M54,
  input  M55,
  input  M56,
  input  M57,
  input  M58,
  input  M59,
  input  M60,
  input  M61,
  input  M62,
  input  M63,
  input  M64,
  input  M65,
  input  M66,
  input  M67,
  input  M68,
  input  M69,
  input  M70,
  input  M71,
  input  M72,
  input  M73,
  input  M74,
  input  M75,
  input  M76,
  input  M77,
  input  M78,
  input  M79,
  input  M80,
  input  M81,
  input  M82,
  input  M83,
  input  M84,
  input  M85,
  input  M86,
  input  M87,
  input  M88,
  input  M89,
  input  M90,
  input  M91,
  input  M92,
  input  M93,
  input  M94,
  input  M95,
  input  M96,
  input  M97,
  input  M98,
  input  M99,
  input  M100,
  input  M101,
  input  M102,
  input  M103,
  input  M104,
  input  M105,
  input  M106,
  input  M107,
  input  M108,
  input  M109,
  input  M110,
  input  M111,
  input  M112,
  input  M113,
  input  M114,
  input  M115,
  input  M116,
  input  M117,
  input  M118,
  input  M119,
  input  M120,
  input  M121,
  input  M122,
  input  M123,
  input  M124,
  input  M125,
  input  M126,
  input  M127,
  input  M128,
  input  M129,
  input  M130,
  input  M131,
  input  M132,
  input  M133,
  input  M134,
  input  M135,
  input  M136,
  input  M137,
  input  M138,
  input  M139,
  input  M140,
  input  M141,
  input  M142,
  input  M143,
  input  M144,
  input  M145,
  input  M146,
  input  M147,
  input  M148,
  input  M149,
  input  M150,
  input  M151,
  input  M152,
  input  M153,
  input  M154,
  input  M155,
  input  M156,
  input  M157,
  input  M158,
  input  M159,
  input  M160,
  input  M161,
  input  M162,
  input  M163,
  input  M164,
  input  M165,
  input  M166,
  input  M167,
  input  M168,
  input  M169,
  input  M170,
  input  M171,
  input  M172,
  input  M173,
  input  M174,
  input  M175,
  input  M176,
  input  M177,
  input  M178,
  input  M179,
  input  M190,
  input  M191,
  input  M192,
  input  M193,
  input  M194,
  input  M195,
  output AX,
  output BX,
  output CX,
  output DX,
  output EX
);

  wire and_1_out, and_2_out, and_3_out, and_4_out, and_5_out, and_6_out, and_7_out, and_8_out, and_9_out,
       and_10_out, and_11_out, and_12_out, and_13_out, and_14_out, and_15_out, and_16_out, and_17_out,
       and_18_out, and_19_out, and_20_out, and_21_out, and_22_out, and_23_out, and_24_out, and_25_out,
       and_26_out, and_27_out, and_28_out, and_29_out, and_30_out, or_1_out, or_2_out, or_3_out, or_4_out,
       or_5_out, or_6_out, or_7_out, or_8_out, or_9_out, or_10_out, or_11_out, or_12_out, or_13_out,
       or_14_out, or_15_out, or_16_out, or_17_out, or_18_out, or_19_out, or_20_out, or_21_out, or_22_out,
       or_23_out, or_24_out, or_25_out, or_26_out, or_27_out, or_28_out, or_29_out, or_30_out, or_31_out,
       or_32_out, or_33_out, or_34_out, or_35_out, or_36_out, or_37_out, or_38_out, or_39_out, or_40_out,
       T3_out, T4_out;

  or u_T3 (T3_out, M152, M135, M118, M101, M84, M67, M50, M33, M16);
  or u_T4 (T4_out, M168, M151, M134, M117, M100, M83, M66, M49, M32, M15);
  or or_1 (or_1_out, E4, E3, E2, E1, E0);
  or or_2 (or_2_out, M190, M163, M146, M129, M112, M95, M78, M61, M44, M27, M10);
  or or_3 (or_3_out, E3, E2, E1, E0);
  or or_4 (or_4_out, M195, M169);
  or or_5 (or_5_out, M175, M158, M141, M124, M107, M90, M73, M56, M39, M22, M5);
  or or_6 (or_6_out, M170, M153, M136, M119, M102, M85, M68, M51, M34, M17, M0);
  or or_7 (or_7_out, E9, E8, E7, E6, E5);
  or or_8 (or_8_out, M191, M164, M147, M130, M113, M96, M79, M62, M45, M28, M11);
  or or_9 (or_9_out, E7, E6, E5, E4);
  or or_10 (or_10_out, M195, M169);
  or or_11 (or_11_out, M176, M159, M142, M125, M108, M91, M74, M57, M40, M23, M6);
  or or_12 (or_12_out, M171, M154, M137, M120, M103, M86, M69, M52, M35, M18, M1);
  or or_13 (or_13_out, E14, E13, E12, E11, E10);
  or or_14 (or_14_out, M192, M165, M148, M131, M114, M97, M80, M63, M46, M29, M12);
  or or_15 (or_15_out, E11, E10, E9, E8);
  or or_16 (or_16_out, M195, M169);
  or or_17 (or_17_out, M177, M160, M143, M126, M109, M92, M75, M58, M41, M24, M7);
  or or_18 (or_18_out, M172, M155, M138, M121, M104, M87, M70, M53, M36, M19, M2);
  or or_19 (or_19_out, E19, E18, E17, E16, E15);
  or or_20 (or_20_out, M193, M166, M149, M132, M115, M98, M81, M64, M47, M30, M13);
  or or_21 (or_21_out, E15, E14, E13, E12);
  or or_22 (or_22_out, M195, M169);
  or or_23 (or_23_out, M178, M161, M144, M127, M110, M93, M76, M59, M42, M25, M8);
  or or_24 (or_24_out, M173, M156, M139, M122, M105, M88, M71, M54, M37, M20, M3);
  or or_25 (or_25_out, E24, E23, E22, E21, E20);
  or or_26 (or_26_out, M194, M167, M150, M133, M116, M99, M82, M65, M48, M31, M14);
  or or_27 (or_27_out, E19, E18, E17, E16);
  or or_28 (or_28_out, M195, M169);
  or or_29 (or_29_out, M179, M162, M145, M128, M111, M94, M77, M60, M43, M26, M9);
  or or_30 (or_30_out, M174, M157, M140, M123, M106, M89, M72, M55, M38, M21, M4);
  and and_1 (and_1_out, or_1_out, T3_out);
  and and_2 (and_2_out, or_3_out, or_4_out);
  and and_3 (and_3_out, or_1_out, T4_out);
  and and_4 (and_4_out, or_6_out, T5);
  and and_5 (and_5_out, or_7_out, T3_out);
  and and_6 (and_6_out, or_9_out, or_10_out);
  and and_7 (and_7_out, or_7_out, T4_out);
  and and_8 (and_8_out, or_12_out, T5);
  and and_9 (and_9_out, or_13_out, T3_out);
  and and_10 (and_10_out, or_15_out, or_16_out);
  and and_11 (and_11_out, or_13_out, T4_out);
  and and_12 (and_12_out, or_18_out, T5);
  and and_13 (and_13_out, or_19_out, T3_out);
  and and_14 (and_14_out, or_21_out, or_22_out);
  and and_15 (and_15_out, or_19_out, T4_out);
  and and_16 (and_16_out, or_24_out, T5);
  and and_17 (and_17_out, or_25_out, T3_out);
  and and_18 (and_18_out, or_27_out, or_28_out);
  and and_19 (and_19_out, or_25_out, T4_out);
  and and_20 (and_20_out, or_30_out, T5);
  or or_31 (or_31_out, and_1_out, or_2_out, and_2_out);
  or or_32 (or_32_out, and_3_out, or_5_out);
  or or_33 (or_33_out, and_5_out, or_8_out, and_6_out);
  or or_34 (or_34_out, and_7_out, or_11_out);
  or or_35 (or_35_out, and_9_out, or_14_out, and_10_out);
  or or_36 (or_36_out, and_11_out, or_17_out);
  or or_37 (or_37_out, and_13_out, or_20_out, and_14_out);
  or or_38 (or_38_out, and_15_out, or_23_out);
  or or_39 (or_39_out, and_17_out, or_26_out, and_18_out);
  or or_40 (or_40_out, and_19_out, or_29_out);
  and and_21 (and_21_out, or_31_out, T3);
  and and_22 (and_22_out, or_32_out, T4);
  and and_23 (and_23_out, or_33_out, T3);
  and and_24 (and_24_out, or_34_out, T4);
  and and_25 (and_25_out, or_35_out, T3);
  and and_26 (and_26_out, or_36_out, T4);
  and and_27 (and_27_out, or_37_out, T3);
  and and_28 (and_28_out, or_38_out, T4);
  and and_29 (and_29_out, or_39_out, T3);
  and and_30 (and_30_out, or_40_out, T4);
  or or_41 (AX, and_21_out, and_22_out, and_4_out);
  or or_42 (BX, and_23_out, and_24_out, and_8_out);
  or or_43 (CX, and_25_out, and_26_out, and_12_out);
  or or_44 (DX, and_27_out, and_28_out, and_16_out);
  or or_45 (EX, and_29_out, and_30_out, and_20_out);
endmodule

// INSTRUCTION_SELECTOR
module INSTRUCTION (
  input  T3,
  input  T4,
  input  T5,
  input  M0,
  input  M1,
  input  M2,
  input  M3,
  input  M4,
  input  M5,
  input  M6,
  input  M7,
  input  M8,
  input  M9,
  input  M10,
  input  M11,
  input  M12,
  input  M13,
  input  M14,
  input  M15,
  input  M16,
  input  M17,
  input  M18,
  input  M19,
  input  M20,
  input  M21,
  input  M22,
  input  M23,
  input  M24,
  input  M25,
  input  M26,
  input  M27,
  input  M28,
  input  M29,
  input  M30,
  input  M31,
  input  M32,
  input  M33,
  input  M34,
  input  M35,
  input  M36,
  input  M37,
  input  M38,
  input  M39,
  input  M40,
  input  M41,
  input  M42,
  input  M43,
  input  M44,
  input  M45,
  input  M46,
  input  M47,
  input  M48,
  input  M49,
  input  M50,
  input  M51,
  input  M52,
  input  M53,
  input  M54,
  input  M55,
  input  M56,
  input  M57,
  input  M58,
  input  M59,
  input  M60,
  input  M61,
  input  M62,
  input  M63,
  input  M64,
  input  M65,
  input  M66,
  input  M67,
  input  M68,
  input  M69,
  input  M70,
  input  M71,
  input  M72,
  input  M73,
  input  M74,
  input  M75,
  input  M76,
  input  M77,
  input  M78,
  input  M79,
  input  M80,
  input  M81,
  input  M82,
  input  M83,
  input  M84,
  input  M85,
  input  M86,
  input  M87,
  input  M88,
  input  M89,
  input  M90,
  input  M91,
  input  M92,
  input  M93,
  input  M94,
  input  M95,
  input  M96,
  input  M97,
  input  M98,
  input  M99,
  input  M100,
  input  M101,
  input  M102,
  input  M103,
  input  M104,
  input  M105,
  input  M106,
  input  M107,
  input  M108,
  input  M109,
  input  M110,
  input  M111,
  input  M112,
  input  M113,
  input  M114,
  input  M115,
  input  M116,
  input  M117,
  input  M118,
  input  M119,
  input  M120,
  input  M121,
  input  M122,
  input  M123,
  input  M124,
  input  M125,
  input  M126,
  input  M127,
  input  M128,
  input  M129,
  input  M130,
  input  M131,
  input  M132,
  input  M133,
  input  M134,
  input  M135,
  input  M136,
  input  M137,
  input  M138,
  input  M139,
  input  M140,
  input  M141,
  input  M142,
  input  M143,
  input  M144,
  input  M145,
  input  M146,
  input  M147,
  input  M148,
  input  M149,
  input  M150,
  input  M151,
  input  M152,
  input  M153,
  input  M154,
  input  M155,
  input  M156,
  input  M157,
  input  M158,
  input  M159,
  input  M160,
  input  M161,
  input  M162,
  input  M163,
  input  M164,
  input  M165,
  input  M166,
  input  M167,
  input  M168,
  input  M169,
  input  M170,
  input  M171,
  input  M172,
  input  M173,
  input  M174,
  input  M175,
  input  M176,
  input  M177,
  input  M178,
  input  M179,
  input  M190,
  input  M191,
  input  M192,
  input  M193,
  input  M194,
  input  M195,
  output AND,
  output OR,
  output XOR,
  output ADD,
  output ADC,
  output SUB,
  output SBB,
  output MUL,
  output DIV,
  output CMP,
  output LOAD
);

  wire and_1_out, and_2_out, and_3_out, and_4_out, and_5_out, and_6_out, and_7_out, and_8_out, and_9_out,
       and_10_out, and_11_out, and_12_out, and_13_out, and_14_out, and_15_out, and_16_out, and_17_out,
       and_18_out, and_19_out, and_20_out, and_21_out, and_22_out, and_23_out, and_24_out, and_25_out,
       and_26_out, and_27_out, and_28_out, and_29_out, and_30_out, and_31_out, and_32_out, and_33_out,
       or_1_out, or_2_out, or_3_out, or_4_out, or_5_out, or_6_out, or_7_out, or_8_out, or_9_out, or_10_out,
       or_11_out, or_12_out, or_13_out, or_14_out, or_15_out, or_16_out, or_17_out, or_18_out, or_19_out,
       or_20_out, or_21_out, or_22_out, or_23_out, or_24_out, or_25_out, or_26_out, or_27_out, or_28_out,
       or_29_out, or_30_out, or_31_out, or_32_out, or_33_out;

  or or_1 (or_1_out, M16, M14, M13, M12, M11, M10);
  or or_2 (or_2_out, M15, M9, M8, M7, M6, M5);
  or or_3 (or_3_out, M4, M3, M2, M1, M0);
  or or_4 (or_4_out, M33, M31, M30, M29, M28, M27);
  or or_5 (or_5_out, M32, M26, M25, M24, M23, M22);
  or or_6 (or_6_out, M21, M20, M19, M18, M17);
  or or_7 (or_7_out, M50, M48, M47, M46, M45, M44);
  or or_8 (or_8_out, M49, M43, M42, M41, M40, M39);
  or or_9 (or_9_out, M38, M37, M36, M35, M34);
  or or_10 (or_10_out, M67, M65, M64, M63, M62, M61);
  or or_11 (or_11_out, M66, M60, M59, M58, M57, M56);
  or or_12 (or_12_out, M55, M54, M53, M52, M51);
  or or_13 (or_13_out, M84, M82, M81, M80, M79, M78);
  or or_14 (or_14_out, M83, M77, M76, M75, M74, M73);
  or or_15 (or_15_out, M72, M71, M70, M69, M68);
  or or_16 (or_16_out, M101, M99, M98, M97, M96, M95);
  or or_17 (or_17_out, M100, M94, M93, M92, M91, M90);
  or or_18 (or_18_out, M89, M88, M87, M86, M85);
  or or_19 (or_19_out, M118, M116, M115, M114, M113, M112);
  or or_20 (or_20_out, M117, M111, M110, M109, M108, M107);
  or or_21 (or_21_out, M106, M105, M104, M103, M102);
  or or_22 (or_22_out, M135, M133, M132, M131, M130, M129);
  or or_23 (or_23_out, M134, M128, M127, M126, M125, M124);
  or or_24 (or_24_out, M123, M122, M121, M120, M119);
  or or_25 (or_25_out, M152, M150, M149, M148, M147, M146);
  or or_26 (or_26_out, M151, M145, M144, M143, M142, M141);
  or or_27 (or_27_out, M140, M139, M138, M137, M136);
  or or_28 (or_28_out, M169, M167, M166, M165, M164, M163);
  or or_29 (or_29_out, M168, M162, M161, M160, M159, M158);
  or or_30 (or_30_out, M157, M156, M155, M154, M153);
  or or_31 (or_31_out, M195, M194, M193, M192, M191, M190);
  or or_32 (or_32_out, M179, M178, M177, M176, M175);
  or or_33 (or_33_out, M174, M173, M172, M171, M170);
  and and_1 (and_1_out, or_1_out, T3);
  and and_2 (and_2_out, or_2_out, T4);
  and and_3 (and_3_out, or_3_out, T5);
  and and_4 (and_4_out, or_4_out, T3);
  and and_5 (and_5_out, or_5_out, T4);
  and and_6 (and_6_out, or_6_out, T5);
  and and_7 (and_7_out, or_7_out, T3);
  and and_8 (and_8_out, or_8_out, T4);
  and and_9 (and_9_out, or_9_out, T5);
  and and_10 (and_10_out, or_10_out, T3);
  and and_11 (and_11_out, or_11_out, T4);
  and and_12 (and_12_out, or_12_out, T5);
  and and_13 (and_13_out, or_13_out, T3);
  and and_14 (and_14_out, or_14_out, T4);
  and and_15 (and_15_out, or_15_out, T5);
  and and_16 (and_16_out, or_16_out, T3);
  and and_17 (and_17_out, or_17_out, T4);
  and and_18 (and_18_out, or_18_out, T5);
  and and_19 (and_19_out, or_19_out, T3);
  and and_20 (and_20_out, or_20_out, T4);
  and and_21 (and_21_out, or_21_out, T5);
  and and_22 (and_22_out, or_22_out, T3);
  and and_23 (and_23_out, or_23_out, T4);
  and and_24 (and_24_out, or_24_out, T5);
  and and_25 (and_25_out, or_25_out, T3);
  and and_26 (and_26_out, or_26_out, T4);
  and and_27 (and_27_out, or_27_out, T5);
  and and_28 (and_28_out, or_28_out, T3);
  and and_29 (and_29_out, or_29_out, T4);
  and and_30 (and_30_out, or_30_out, T5);
  and and_31 (and_31_out, or_31_out, T3);
  and and_32 (and_32_out, or_32_out, T4);
  and and_33 (and_33_out, or_33_out, T5);
  or or_34 (AND, and_1_out, and_2_out, and_3_out);
  or or_35 (OR, and_4_out, and_5_out, and_6_out);
  or or_36 (XOR, and_7_out, and_8_out, and_9_out);
  or or_37 (ADD, and_10_out, and_11_out, and_12_out);
  or or_38 (ADC, and_13_out, and_14_out, and_15_out);
  or or_39 (SUB, and_16_out, and_17_out, and_18_out);
  or or_40 (SBB, and_19_out, and_20_out, and_21_out);
  or or_41 (MUL, and_22_out, and_23_out, and_24_out);
  or or_42 (DIV, and_25_out, and_26_out, and_27_out);
  or or_43 (CMP, and_28_out, and_29_out, and_30_out);
  or or_44 (LOAD, and_31_out, and_32_out, and_33_out);
endmodule

// SECOND_REGISTER_SELECTOR
module SECOND_REGISTER (
  input  T3,
  input  T4,
  input  T5,
  input  E0,
  input  E1,
  input  E2,
  input  E3,
  input  E4,
  input  E5,
  input  E6,
  input  E7,
  input  E8,
  input  E9,
  input  E10,
  input  E11,
  input  E12,
  input  E13,
  input  E14,
  input  E15,
  input  E16,
  input  E17,
  input  E18,
  input  E19,
  input  E20,
  input  E21,
  input  E22,
  input  E23,
  input  E24,
  input  M0,
  input  M1,
  input  M2,
  input  M3,
  input  M4,
  input  M5,
  input  M6,
  input  M7,
  input  M8,
  input  M9,
  input  M10,
  input  M11,
  input  M12,
  input  M13,
  input  M14,
  input  M15,
  input  M16,
  input  M17,
  input  M18,
  input  M19,
  input  M20,
  input  M21,
  input  M22,
  input  M23,
  input  M24,
  input  M25,
  input  M26,
  input  M27,
  input  M28,
  input  M29,
  input  M30,
  input  M31,
  input  M32,
  input  M33,
  input  M34,
  input  M35,
  input  M36,
  input  M37,
  input  M38,
  input  M39,
  input  M40,
  input  M41,
  input  M42,
  input  M43,
  input  M44,
  input  M45,
  input  M46,
  input  M47,
  input  M48,
  input  M49,
  input  M50,
  input  M51,
  input  M52,
  input  M53,
  input  M54,
  input  M55,
  input  M56,
  input  M57,
  input  M58,
  input  M59,
  input  M60,
  input  M61,
  input  M62,
  input  M63,
  input  M64,
  input  M65,
  input  M66,
  input  M67,
  input  M68,
  input  M69,
  input  M70,
  input  M71,
  input  M72,
  input  M73,
  input  M74,
  input  M75,
  input  M76,
  input  M77,
  input  M78,
  input  M79,
  input  M80,
  input  M81,
  input  M82,
  input  M83,
  input  M84,
  input  M85,
  input  M86,
  input  M87,
  input  M88,
  input  M89,
  input  M90,
  input  M91,
  input  M92,
  input  M93,
  input  M94,
  input  M95,
  input  M96,
  input  M97,
  input  M98,
  input  M99,
  input  M100,
  input  M101,
  input  M102,
  input  M103,
  input  M104,
  input  M105,
  input  M106,
  input  M107,
  input  M108,
  input  M109,
  input  M110,
  input  M111,
  input  M112,
  input  M113,
  input  M114,
  input  M115,
  input  M116,
  input  M117,
  input  M118,
  input  M119,
  input  M120,
  input  M121,
  input  M122,
  input  M123,
  input  M124,
  input  M125,
  input  M126,
  input  M127,
  input  M128,
  input  M129,
  input  M130,
  input  M131,
  input  M132,
  input  M133,
  input  M134,
  input  M135,
  input  M136,
  input  M137,
  input  M138,
  input  M139,
  input  M140,
  input  M141,
  input  M142,
  input  M143,
  input  M144,
  input  M145,
  input  M146,
  input  M147,
  input  M148,
  input  M149,
  input  M150,
  input  M151,
  input  M152,
  input  M153,
  input  M154,
  input  M155,
  input  M156,
  input  M157,
  input  M158,
  input  M159,
  input  M160,
  input  M161,
  input  M162,
  input  M163,
  input  M164,
  input  M165,
  input  M166,
  input  M167,
  input  M168,
  input  M169,
  input  M170,
  input  M171,
  input  M172,
  input  M173,
  input  M174,
  input  M175,
  input  M176,
  input  M177,
  input  M178,
  input  M179,
  input  M190,
  input  M191,
  input  M192,
  input  M193,
  input  M194,
  input  M195,
  output AX,
  output BX,
  output CX,
  output DX,
  output EX,
  output DR,
  output IR
);

  wire and_1_out, and_2_out, and_3_out, and_4_out, and_5_out, and_6_out, and_7_out, and_8_out, and_9_out,
       and_10_out, and_11_out, and_12_out, M_4_out, M_5_out, or_1_out, or_2_out, or_3_out, or_4_out,
       or_5_out, or_6_out, or_7_out, or_8_out, or_9_out, or_10_out, or_11_out, or_12_out, or_13_out,
       or_14_out, or_15_out, or_16_out, or_17_out, or_18_out, or_19_out, or_20_out, or_21_out, or_22_out,
       or_23_out, or_24_out;

  or M_5 (M_5_out, M152, M135, M118, M101, M84, M67, M50);
  or M_4 (M_4_out, M195, M169);
  or or_1 (or_1_out, E20, E15, E10, E5, E0);
  or or_2 (or_2_out, E16, E12, E8, E4);
  or or_3 (or_3_out, E21, E16, E11, E6, E1);
  or or_4 (or_4_out, E17, E13, E9, E0);
  or or_5 (or_5_out, E22, E17, E12, E7, E2);
  or or_6 (or_6_out, E18, E14, E5, E1);
  or or_7 (or_7_out, E23, E18, E13, E8, E3);
  or or_8 (or_8_out, E19, E10, E6, E2);
  or or_9 (or_9_out, E24, E19, E14, E9, E4);
  or or_10 (or_10_out, E15, E11, E7, E3);
  or or_11 (or_11_out, M179, M178, M177, M176, M175, M168, M162, M161, M160, M159, M158, M151, M145, M144, M143, M142, M141, M134, M128, M127, M126, M125, M124);
  or or_12 (or_12_out, or_11_out, M117, M111, M110, M109, M108, M107, M100, M94, M93, M92, M91, M90, M83, M77, M76, M75, M74, M73, M66, M60, M59);
  or or_13 (or_13_out, or_12_out, M58, M57, M56, M49, M43, M42, M41, M40, M39, M32, M26, M25, M24, M23, M22, M15, M9, M8, M7, M6, M5);
  or or_14 (or_14_out, M174, M173, M172, M171, M170, M157, M156, M155, M154, M153, M140, M139, M138, M137, M136, M123, M122, M121, M120);
  or or_15 (or_15_out, or_14_out, M119, M106, M105, M104, M103, M102, M89, M88, M87, M86, M85, M72, M71, M70, M69, M68, M55, M54);
  or or_16 (or_16_out, or_15_out, M53, M52, M51, M38, M37, M36, M35, M34, M21, M20, M19, M18, M17, M4, M3, M2, M1, M0);
  or or_17 (or_17_out, M194, M193, M192, M191, M190, M167, M166, M165, M164, M163, M150, M149, M148, M147, M146, M133, M132, M131, M130);
  or or_18 (or_18_out, or_17_out, M129, M116, M115, M114, M113, M112, M99, M98, M97, M96, M95, M82, M81, M80, M79, M78, M65, M64);
  or or_19 (or_19_out, or_18_out, M63, M62, M61, M48, M47, M46, M45, M44, M31, M30, M29, M28, M27, M14, M13, M12, M11, M10);
  and and_1 (and_1_out, or_1_out, M_5_out);
  and and_2 (and_2_out, or_2_out, M_4_out);
  and and_3 (and_3_out, or_3_out, M_5_out);
  and and_4 (and_4_out, or_4_out, M_4_out);
  and and_5 (and_5_out, or_5_out, M_5_out);
  and and_6 (and_6_out, or_6_out, M_4_out);
  and and_7 (and_7_out, or_7_out, M_5_out);
  and and_8 (and_8_out, or_8_out, M_4_out);
  and and_9 (and_9_out, or_9_out, M_5_out);
  and and_10 (and_10_out, or_10_out, M_4_out);
  and and_11 (and_11_out, or_13_out, T4);
  and and_12 (and_12_out, or_16_out, T5);
  and and_13 (IR, or_19_out, T3);
  or or_20 (or_20_out, and_1_out, and_2_out);
  or or_21 (or_21_out, and_3_out, and_4_out);
  or or_22 (or_22_out, and_5_out, and_6_out);
  or or_23 (or_23_out, and_7_out, and_8_out);
  or or_24 (or_24_out, and_9_out, and_10_out);
  or or_25 (DR, and_11_out, and_12_out);
  and and_14 (AX, or_20_out, T3);
  and and_15 (BX, or_21_out, T3);
  and and_16 (CX, or_22_out, T3);
  and and_17 (DX, or_23_out, T3);
  and and_18 (EX, or_24_out, T3);
endmodule

module SIGNAL_PRODUCER (
  input  [23:0] IR,
  input  C,
  input  Z
);

  E_SIGNAL_DECODER e_signal_decoder_1 (.IR_4_0(IR[4:0]));  // open: _0, _1, _2, _3, _4, _5, _6, _7, _8, _9, _10, _11, _12, _13, _14, _15, _16, _17, _18, _19, _20, _21, _22, _23, _24
  M_SIGNAL_DECODER m_signal_decoder_1 (.IR_23_16(IR[23:16]));  // open: _0, _1, _2, _3, _4, _5, _6, _7, _8, _9, _10, _11, _12, _13, _14, _15, _16, _17, _18, _19, _20, _21, _22, _23, _24, _25, _26, _27, _28, _29, _30, _31, _32, _33, _34, _35, _36, _37, _38, _39, _40, _41, _42, _43, _44, _45, _46, _47, _48, _49, _50, _51, _52, _53, _54, _55, _56, _57, _58, _59, _60, _61, _62, _63, _64, _65, _66, _67, _68, _69, _70, _71, _72, _73, _74, _75, _76, _77, _78, _79, _80, _81, _82, _83, _84, _85, _86, _87, _88, _89, _90, _91, _92, _93, _94, _95, _96, _97, _98, _99, _100, _101, _102, _103, _104, _105, _106, _107, _108, _109, _110, _111, _112, _113, _114, _115, _116, _117, _118, _119, _120, _121, _122, _123, _124, _125, _126, _127, _128, _129, _130, _131, _132, _133, _134, _135, _136, _137, _138, _139, _140, _141, _142, _143, _144, _145, _146, _147, _148, _149, _150, _151, _152, _153, _154, _155, _156, _157, _158, _159, _160, _161, _162, _163, _164, _165, _166, _167, _168, _169, _170, _171, _172, _173, _174, _175, _176, _177, _178, _179, _180, _181, _182, _183, _184, _185, _186, _187, _188, _189, _190, _191, _192, _193, _194, _195, _196, _197, _198, _199, _200, _201, _202, _203, _204, _205, _206, _207, _208, _209, _210, _211, _212, _213, _214, _215, _216, _217, _218, _219, _220, _221, _222, _223, _224, _225, _226
endmodule

module E_SIGNAL_DECODER (
  input  [4:0] IR_4_0,
  output _0,
  output _1,
  output _2,
  output _3,
  output _4,
  output _5,
  output _6,
  output _7,
  output _8,
  output _9,
  output _10,
  output _11,
  output _12,
  output _13,
  output _14,
  output _15,
  output _16,
  output _17,
  output _18,
  output _19,
  output _20,
  output _21,
  output _22,
  output _23,
  output _24
);

  and and_1 (_0, ~IR_4_0[0], ~IR_4_0[1], ~IR_4_0[2], ~IR_4_0[3], ~IR_4_0[4]);  // AND_Gate
  and and_2 (_1, IR_4_0[0], ~IR_4_0[1], ~IR_4_0[2], ~IR_4_0[3], ~IR_4_0[4]);  // AND_Gate
  and and_3 (_2, ~IR_4_0[0], IR_4_0[1], ~IR_4_0[2], ~IR_4_0[3], ~IR_4_0[4]);  // AND_Gate
  and and_4 (_3, IR_4_0[0], IR_4_0[1], ~IR_4_0[2], ~IR_4_0[3], ~IR_4_0[4]);  // AND_Gate
  and and_5 (_4, ~IR_4_0[0], ~IR_4_0[1], IR_4_0[2], ~IR_4_0[3], ~IR_4_0[4]);  // AND_Gate
  and and_6 (_5, IR_4_0[0], ~IR_4_0[1], IR_4_0[2], ~IR_4_0[3], ~IR_4_0[4]);  // AND_Gate
  and and_7 (_6, ~IR_4_0[0], IR_4_0[1], IR_4_0[2], ~IR_4_0[3], ~IR_4_0[4]);  // AND_Gate
  and and_8 (_7, IR_4_0[0], IR_4_0[1], IR_4_0[2], ~IR_4_0[3], ~IR_4_0[4]);  // AND_Gate
  and and_9 (_8, ~IR_4_0[0], ~IR_4_0[1], ~IR_4_0[2], IR_4_0[3], ~IR_4_0[4]);  // AND_Gate
  and and_10 (_9, IR_4_0[0], ~IR_4_0[1], ~IR_4_0[2], IR_4_0[3], ~IR_4_0[4]);  // AND_Gate
  and and_11 (_10, ~IR_4_0[0], IR_4_0[1], ~IR_4_0[2], IR_4_0[3], ~IR_4_0[4]);  // AND_Gate
  and and_12 (_11, IR_4_0[0], IR_4_0[1], ~IR_4_0[2], IR_4_0[3], ~IR_4_0[4]);  // AND_Gate
  and and_13 (_12, ~IR_4_0[0], ~IR_4_0[1], IR_4_0[2], IR_4_0[3], ~IR_4_0[4]);  // AND_Gate
  and and_14 (_13, IR_4_0[0], ~IR_4_0[1], IR_4_0[2], IR_4_0[3], ~IR_4_0[4]);  // AND_Gate
  and and_15 (_14, ~IR_4_0[0], IR_4_0[1], IR_4_0[2], IR_4_0[3], ~IR_4_0[4]);  // AND_Gate
  and and_16 (_15, IR_4_0[0], IR_4_0[1], IR_4_0[2], IR_4_0[3], ~IR_4_0[4]);  // AND_Gate
  and and_17 (_16, ~IR_4_0[0], ~IR_4_0[1], ~IR_4_0[2], ~IR_4_0[3], IR_4_0[4]);  // AND_Gate
  and and_18 (_17, IR_4_0[0], ~IR_4_0[1], ~IR_4_0[2], ~IR_4_0[3], IR_4_0[4]);  // AND_Gate
  and and_19 (_18, ~IR_4_0[0], IR_4_0[1], ~IR_4_0[2], ~IR_4_0[3], IR_4_0[4]);  // AND_Gate
  and and_20 (_19, IR_4_0[0], IR_4_0[1], ~IR_4_0[2], ~IR_4_0[3], IR_4_0[4]);  // AND_Gate
  and and_21 (_20, ~IR_4_0[0], ~IR_4_0[1], IR_4_0[2], ~IR_4_0[3], IR_4_0[4]);  // AND_Gate
  and and_22 (_21, IR_4_0[0], ~IR_4_0[1], IR_4_0[2], ~IR_4_0[3], IR_4_0[4]);  // AND_Gate
  and and_23 (_22, ~IR_4_0[0], IR_4_0[1], IR_4_0[2], ~IR_4_0[3], IR_4_0[4]);  // AND_Gate
  and and_24 (_23, IR_4_0[0], IR_4_0[1], IR_4_0[2], ~IR_4_0[3], IR_4_0[4]);  // AND_Gate
  and and_25 (_24, ~IR_4_0[0], ~IR_4_0[1], ~IR_4_0[2], IR_4_0[3], IR_4_0[4]);  // AND_Gate
endmodule
module M_SIGNAL_DECODER (
  input  [7:0] IR_23_16,
  output _0,
  output _1,
  output _2,
  output _3,
  output _4,
  output _5,
  output _6,
  output _7,
  output _8,
  output _9,
  output _10,
  output _11,
  output _12,
  output _13,
  output _14,
  output _15,
  output _16,
  output _17,
  output _18,
  output _19,
  output _20,
  output _21,
  output _22,
  output _23,
  output _24,
  output _25,
  output _26,
  output _27,
  output _28,
  output _29,
  output _30,
  output _31,
  output _32,
  output _33,
  output _34,
  output _35,
  output _36,
  output _37,
  output _38,
  output _39,
  output _40,
  output _41,
  output _42,
  output _43,
  output _44,
  output _45,
  output _46,
  output _47,
  output _48,
  output _49,
  output _50,
  output _51,
  output _52,
  output _53,
  output _54,
  output _55,
  output _56,
  output _57,
  output _58,
  output _59,
  output _60,
  output _61,
  output _62,
  output _63,
  output _64,
  output _65,
  output _66,
  output _67,
  output _68,
  output _69,
  output _70,
  output _71,
  output _72,
  output _73,
  output _74,
  output _75,
  output _76,
  output _77,
  output _78,
  output _79,
  output _80,
  output _81,
  output _82,
  output _83,
  output _84,
  output _85,
  output _86,
  output _87,
  output _88,
  output _89,
  output _90,
  output _91,
  output _92,
  output _93,
  output _94,
  output _95,
  output _96,
  output _97,
  output _98,
  output _99,
  output _100,
  output _101,
  output _102,
  output _103,
  output _104,
  output _105,
  output _106,
  output _107,
  output _108,
  output _109,
  output _110,
  output _111,
  output _112,
  output _113,
  output _114,
  output _115,
  output _116,
  output _117,
  output _118,
  output _119,
  output _120,
  output _121,
  output _122,
  output _123,
  output _124,
  output _125,
  output _126,
  output _127,
  output _128,
  output _129,
  output _130,
  output _131,
  output _132,
  output _133,
  output _134,
  output _135,
  output _136,
  output _137,
  output _138,
  output _139,
  output _140,
  output _141,
  output _142,
  output _143,
  output _144,
  output _145,
  output _146,
  output _147,
  output _148,
  output _149,
  output _150,
  output _151,
  output _152,
  output _153,
  output _154,
  output _155,
  output _156,
  output _157,
  output _158,
  output _159,
  output _160,
  output _161,
  output _162,
  output _163,
  output _164,
  output _165,
  output _166,
  output _167,
  output _168,
  output _169,
  output _170,
  output _171,
  output _172,
  output _173,
  output _174,
  output _175,
  output _176,
  output _177,
  output _178,
  output _179,
  output _180,
  output _181,
  output _182,
  output _183,
  output _184,
  output _185,
  output _186,
  output _187,
  output _188,
  output _189,
  output _190,
  output _191,
  output _192,
  output _193,
  output _194,
  output _195,
  output _196,
  output _197,
  output _198,
  output _199,
  output _200,
  output _201,
  output _202,
  output _203,
  output _204,
  output _205,
  output _206,
  output _207,
  output _208,
  output _209,
  output _210,
  output _211,
  output _212,
  output _213,
  output _214,
  output _215,
  output _216,
  output _217,
  output _218,
  output _219,
  output _220,
  output _221,
  output _222,
  output _223,
  output _224,
  output _225,
  output _226
);

  and u__0 (_0, ~IR_23_16[0], ~IR_23_16[1], ~IR_23_16[2], ~IR_23_16[3], ~IR_23_16[4], ~IR_23_16[5], ~IR_23_16[6], ~IR_23_16[7]);  // AND_Gate
  and u__1 (_1, IR_23_16[0], ~IR_23_16[1], ~IR_23_16[2], ~IR_23_16[3], ~IR_23_16[4], ~IR_23_16[5], ~IR_23_16[6], ~IR_23_16[7]);  // AND_Gate
  and u__2 (_2, ~IR_23_16[0], IR_23_16[1], ~IR_23_16[2], ~IR_23_16[3], ~IR_23_16[4], ~IR_23_16[5], ~IR_23_16[6], ~IR_23_16[7]);  // AND_Gate
  and u__3 (_3, IR_23_16[0], IR_23_16[1], ~IR_23_16[2], ~IR_23_16[3], ~IR_23_16[4], ~IR_23_16[5], ~IR_23_16[6], ~IR_23_16[7]);  // AND_Gate
  and u__4 (_4, ~IR_23_16[0], ~IR_23_16[1], IR_23_16[2], ~IR_23_16[3], ~IR_23_16[4], ~IR_23_16[5], ~IR_23_16[6], ~IR_23_16[7]);  // AND_Gate
  and u__5 (_5, IR_23_16[0], ~IR_23_16[1], IR_23_16[2], ~IR_23_16[3], ~IR_23_16[4], ~IR_23_16[5], ~IR_23_16[6], ~IR_23_16[7]);  // AND_Gate
  and u__6 (_6, ~IR_23_16[0], IR_23_16[1], IR_23_16[2], ~IR_23_16[3], ~IR_23_16[4], ~IR_23_16[5], ~IR_23_16[6], ~IR_23_16[7]);  // AND_Gate
  and u__7 (_7, IR_23_16[0], IR_23_16[1], IR_23_16[2], ~IR_23_16[3], ~IR_23_16[4], ~IR_23_16[5], ~IR_23_16[6], ~IR_23_16[7]);  // AND_Gate
  and u__8 (_8, ~IR_23_16[0], ~IR_23_16[1], ~IR_23_16[2], IR_23_16[3], ~IR_23_16[4], ~IR_23_16[5], ~IR_23_16[6], ~IR_23_16[7]);  // AND_Gate
  and u__9 (_9, IR_23_16[0], ~IR_23_16[1], ~IR_23_16[2], IR_23_16[3], ~IR_23_16[4], ~IR_23_16[5], ~IR_23_16[6], ~IR_23_16[7]);  // AND_Gate
  and u__10 (_10, ~IR_23_16[0], IR_23_16[1], ~IR_23_16[2], IR_23_16[3], ~IR_23_16[4], ~IR_23_16[5], ~IR_23_16[6], ~IR_23_16[7]);  // AND_Gate
  and u__11 (_11, IR_23_16[0], IR_23_16[1], ~IR_23_16[2], IR_23_16[3], ~IR_23_16[4], ~IR_23_16[5], ~IR_23_16[6], ~IR_23_16[7]);  // AND_Gate
  and u__12 (_12, ~IR_23_16[0], ~IR_23_16[1], IR_23_16[2], IR_23_16[3], ~IR_23_16[4], ~IR_23_16[5], ~IR_23_16[6], ~IR_23_16[7]);  // AND_Gate
  and u__13 (_13, IR_23_16[0], ~IR_23_16[1], IR_23_16[2], IR_23_16[3], ~IR_23_16[4], ~IR_23_16[5], ~IR_23_16[6], ~IR_23_16[7]);  // AND_Gate
  and u__14 (_14, ~IR_23_16[0], IR_23_16[1], IR_23_16[2], IR_23_16[3], ~IR_23_16[4], ~IR_23_16[5], ~IR_23_16[6], ~IR_23_16[7]);  // AND_Gate
  and u__15 (_15, IR_23_16[0], IR_23_16[1], IR_23_16[2], IR_23_16[3], ~IR_23_16[4], ~IR_23_16[5], ~IR_23_16[6], ~IR_23_16[7]);  // AND_Gate
  and u__16 (_16, ~IR_23_16[0], ~IR_23_16[1], ~IR_23_16[2], ~IR_23_16[3], IR_23_16[4], ~IR_23_16[5], ~IR_23_16[6], ~IR_23_16[7]);  // AND_Gate
  and u__17 (_17, IR_23_16[0], ~IR_23_16[1], ~IR_23_16[2], ~IR_23_16[3], IR_23_16[4], ~IR_23_16[5], ~IR_23_16[6], ~IR_23_16[7]);  // AND_Gate
  and u__18 (_18, ~IR_23_16[0], IR_23_16[1], ~IR_23_16[2], ~IR_23_16[3], IR_23_16[4], ~IR_23_16[5], ~IR_23_16[6], ~IR_23_16[7]);  // AND_Gate
  and u__19 (_19, IR_23_16[0], IR_23_16[1], ~IR_23_16[2], ~IR_23_16[3], IR_23_16[4], ~IR_23_16[5], ~IR_23_16[6], ~IR_23_16[7]);  // AND_Gate
  and u__20 (_20, ~IR_23_16[0], ~IR_23_16[1], IR_23_16[2], ~IR_23_16[3], IR_23_16[4], ~IR_23_16[5], ~IR_23_16[6], ~IR_23_16[7]);  // AND_Gate
  and u__21 (_21, IR_23_16[0], ~IR_23_16[1], IR_23_16[2], ~IR_23_16[3], IR_23_16[4], ~IR_23_16[5], ~IR_23_16[6], ~IR_23_16[7]);  // AND_Gate
  and u__22 (_22, ~IR_23_16[0], IR_23_16[1], IR_23_16[2], ~IR_23_16[3], IR_23_16[4], ~IR_23_16[5], ~IR_23_16[6], ~IR_23_16[7]);  // AND_Gate
  and u__23 (_23, IR_23_16[0], IR_23_16[1], IR_23_16[2], ~IR_23_16[3], IR_23_16[4], ~IR_23_16[5], ~IR_23_16[6], ~IR_23_16[7]);  // AND_Gate
  and u__24 (_24, ~IR_23_16[0], ~IR_23_16[1], ~IR_23_16[2], IR_23_16[3], IR_23_16[4], ~IR_23_16[5], ~IR_23_16[6], ~IR_23_16[7]);  // AND_Gate
  and u__25 (_25, IR_23_16[0], ~IR_23_16[1], ~IR_23_16[2], IR_23_16[3], IR_23_16[4], ~IR_23_16[5], ~IR_23_16[6], ~IR_23_16[7]);  // AND_Gate
  and u__26 (_26, ~IR_23_16[0], IR_23_16[1], ~IR_23_16[2], IR_23_16[3], IR_23_16[4], ~IR_23_16[5], ~IR_23_16[6], ~IR_23_16[7]);  // AND_Gate
  and u__27 (_27, IR_23_16[0], IR_23_16[1], ~IR_23_16[2], IR_23_16[3], IR_23_16[4], ~IR_23_16[5], ~IR_23_16[6], ~IR_23_16[7]);  // AND_Gate
  and u__28 (_28, ~IR_23_16[0], ~IR_23_16[1], IR_23_16[2], IR_23_16[3], IR_23_16[4], ~IR_23_16[5], ~IR_23_16[6], ~IR_23_16[7]);  // AND_Gate
  and u__29 (_29, IR_23_16[0], ~IR_23_16[1], IR_23_16[2], IR_23_16[3], IR_23_16[4], ~IR_23_16[5], ~IR_23_16[6], ~IR_23_16[7]);  // AND_Gate
  and u__30 (_30, ~IR_23_16[0], IR_23_16[1], IR_23_16[2], IR_23_16[3], IR_23_16[4], ~IR_23_16[5], ~IR_23_16[6], ~IR_23_16[7]);  // AND_Gate
  and u__31 (_31, IR_23_16[0], IR_23_16[1], IR_23_16[2], IR_23_16[3], IR_23_16[4], ~IR_23_16[5], ~IR_23_16[6], ~IR_23_16[7]);  // AND_Gate
  and u__32 (_32, ~IR_23_16[0], ~IR_23_16[1], ~IR_23_16[2], ~IR_23_16[3], ~IR_23_16[4], IR_23_16[5], ~IR_23_16[6], ~IR_23_16[7]);  // AND_Gate
  and u__33 (_33, IR_23_16[0], ~IR_23_16[1], ~IR_23_16[2], ~IR_23_16[3], ~IR_23_16[4], IR_23_16[5], ~IR_23_16[6], ~IR_23_16[7]);  // AND_Gate
  and u__34 (_34, ~IR_23_16[0], IR_23_16[1], ~IR_23_16[2], ~IR_23_16[3], ~IR_23_16[4], IR_23_16[5], ~IR_23_16[6], ~IR_23_16[7]);  // AND_Gate
  and u__35 (_35, IR_23_16[0], IR_23_16[1], ~IR_23_16[2], ~IR_23_16[3], ~IR_23_16[4], IR_23_16[5], ~IR_23_16[6], ~IR_23_16[7]);  // AND_Gate
  and u__36 (_36, ~IR_23_16[0], ~IR_23_16[1], IR_23_16[2], ~IR_23_16[3], ~IR_23_16[4], IR_23_16[5], ~IR_23_16[6], ~IR_23_16[7]);  // AND_Gate
  and u__37 (_37, IR_23_16[0], ~IR_23_16[1], IR_23_16[2], ~IR_23_16[3], ~IR_23_16[4], IR_23_16[5], ~IR_23_16[6], ~IR_23_16[7]);  // AND_Gate
  and u__38 (_38, ~IR_23_16[0], IR_23_16[1], IR_23_16[2], ~IR_23_16[3], ~IR_23_16[4], IR_23_16[5], ~IR_23_16[6], ~IR_23_16[7]);  // AND_Gate
  and u__39 (_39, IR_23_16[0], IR_23_16[1], IR_23_16[2], ~IR_23_16[3], ~IR_23_16[4], IR_23_16[5], ~IR_23_16[6], ~IR_23_16[7]);  // AND_Gate
  and u__40 (_40, ~IR_23_16[0], ~IR_23_16[1], ~IR_23_16[2], IR_23_16[3], ~IR_23_16[4], IR_23_16[5], ~IR_23_16[6], ~IR_23_16[7]);  // AND_Gate
  and u__41 (_41, IR_23_16[0], ~IR_23_16[1], ~IR_23_16[2], IR_23_16[3], ~IR_23_16[4], IR_23_16[5], ~IR_23_16[6], ~IR_23_16[7]);  // AND_Gate
  and u__42 (_42, ~IR_23_16[0], IR_23_16[1], ~IR_23_16[2], IR_23_16[3], ~IR_23_16[4], IR_23_16[5], ~IR_23_16[6], ~IR_23_16[7]);  // AND_Gate
  and u__43 (_43, IR_23_16[0], IR_23_16[1], ~IR_23_16[2], IR_23_16[3], ~IR_23_16[4], IR_23_16[5], ~IR_23_16[6], ~IR_23_16[7]);  // AND_Gate
  and u__44 (_44, ~IR_23_16[0], ~IR_23_16[1], IR_23_16[2], IR_23_16[3], ~IR_23_16[4], IR_23_16[5], ~IR_23_16[6], ~IR_23_16[7]);  // AND_Gate
  and u__45 (_45, IR_23_16[0], ~IR_23_16[1], IR_23_16[2], IR_23_16[3], ~IR_23_16[4], IR_23_16[5], ~IR_23_16[6], ~IR_23_16[7]);  // AND_Gate
  and u__46 (_46, ~IR_23_16[0], IR_23_16[1], IR_23_16[2], IR_23_16[3], ~IR_23_16[4], IR_23_16[5], ~IR_23_16[6], ~IR_23_16[7]);  // AND_Gate
  and u__47 (_47, IR_23_16[0], IR_23_16[1], IR_23_16[2], IR_23_16[3], ~IR_23_16[4], IR_23_16[5], ~IR_23_16[6], ~IR_23_16[7]);  // AND_Gate
  and u__48 (_48, ~IR_23_16[0], ~IR_23_16[1], ~IR_23_16[2], ~IR_23_16[3], IR_23_16[4], IR_23_16[5], ~IR_23_16[6], ~IR_23_16[7]);  // AND_Gate
  and u__49 (_49, IR_23_16[0], ~IR_23_16[1], ~IR_23_16[2], ~IR_23_16[3], IR_23_16[4], IR_23_16[5], ~IR_23_16[6], ~IR_23_16[7]);  // AND_Gate
  and u__50 (_50, ~IR_23_16[0], IR_23_16[1], ~IR_23_16[2], ~IR_23_16[3], IR_23_16[4], IR_23_16[5], ~IR_23_16[6], ~IR_23_16[7]);  // AND_Gate
  and u__51 (_51, IR_23_16[0], IR_23_16[1], ~IR_23_16[2], ~IR_23_16[3], IR_23_16[4], IR_23_16[5], ~IR_23_16[6], ~IR_23_16[7]);  // AND_Gate
  and u__52 (_52, ~IR_23_16[0], ~IR_23_16[1], IR_23_16[2], ~IR_23_16[3], IR_23_16[4], IR_23_16[5], ~IR_23_16[6], ~IR_23_16[7]);  // AND_Gate
  and u__53 (_53, IR_23_16[0], ~IR_23_16[1], IR_23_16[2], ~IR_23_16[3], IR_23_16[4], IR_23_16[5], ~IR_23_16[6], ~IR_23_16[7]);  // AND_Gate
  and u__54 (_54, ~IR_23_16[0], IR_23_16[1], IR_23_16[2], ~IR_23_16[3], IR_23_16[4], IR_23_16[5], ~IR_23_16[6], ~IR_23_16[7]);  // AND_Gate
  and u__55 (_55, IR_23_16[0], IR_23_16[1], IR_23_16[2], ~IR_23_16[3], IR_23_16[4], IR_23_16[5], ~IR_23_16[6], ~IR_23_16[7]);  // AND_Gate
  and u__56 (_56, ~IR_23_16[0], ~IR_23_16[1], ~IR_23_16[2], IR_23_16[3], IR_23_16[4], IR_23_16[5], ~IR_23_16[6], ~IR_23_16[7]);  // AND_Gate
  and u__57 (_57, IR_23_16[0], ~IR_23_16[1], ~IR_23_16[2], IR_23_16[3], IR_23_16[4], IR_23_16[5], ~IR_23_16[6], ~IR_23_16[7]);  // AND_Gate
  and u__58 (_58, ~IR_23_16[0], IR_23_16[1], ~IR_23_16[2], IR_23_16[3], IR_23_16[4], IR_23_16[5], ~IR_23_16[6], ~IR_23_16[7]);  // AND_Gate
  and u__59 (_59, IR_23_16[0], IR_23_16[1], ~IR_23_16[2], IR_23_16[3], IR_23_16[4], IR_23_16[5], ~IR_23_16[6], ~IR_23_16[7]);  // AND_Gate
  and u__60 (_60, ~IR_23_16[0], ~IR_23_16[1], IR_23_16[2], IR_23_16[3], IR_23_16[4], IR_23_16[5], ~IR_23_16[6], ~IR_23_16[7]);  // AND_Gate
  and u__61 (_61, IR_23_16[0], ~IR_23_16[1], IR_23_16[2], IR_23_16[3], IR_23_16[4], IR_23_16[5], ~IR_23_16[6], ~IR_23_16[7]);  // AND_Gate
  and u__62 (_62, ~IR_23_16[0], IR_23_16[1], IR_23_16[2], IR_23_16[3], IR_23_16[4], IR_23_16[5], ~IR_23_16[6], ~IR_23_16[7]);  // AND_Gate
  and u__63 (_63, IR_23_16[0], IR_23_16[1], IR_23_16[2], IR_23_16[3], IR_23_16[4], IR_23_16[5], ~IR_23_16[6], ~IR_23_16[7]);  // AND_Gate
  and u__64 (_64, ~IR_23_16[0], ~IR_23_16[1], ~IR_23_16[2], ~IR_23_16[3], ~IR_23_16[4], ~IR_23_16[5], IR_23_16[6], ~IR_23_16[7]);  // AND_Gate
  and u__65 (_65, IR_23_16[0], ~IR_23_16[1], ~IR_23_16[2], ~IR_23_16[3], ~IR_23_16[4], ~IR_23_16[5], IR_23_16[6], ~IR_23_16[7]);  // AND_Gate
  and u__66 (_66, ~IR_23_16[0], IR_23_16[1], ~IR_23_16[2], ~IR_23_16[3], ~IR_23_16[4], ~IR_23_16[5], IR_23_16[6], ~IR_23_16[7]);  // AND_Gate
  and u__67 (_67, IR_23_16[0], IR_23_16[1], ~IR_23_16[2], ~IR_23_16[3], ~IR_23_16[4], ~IR_23_16[5], IR_23_16[6], ~IR_23_16[7]);  // AND_Gate
  and u__68 (_68, ~IR_23_16[0], ~IR_23_16[1], IR_23_16[2], ~IR_23_16[3], ~IR_23_16[4], ~IR_23_16[5], IR_23_16[6], ~IR_23_16[7]);  // AND_Gate
  and u__69 (_69, IR_23_16[0], ~IR_23_16[1], IR_23_16[2], ~IR_23_16[3], ~IR_23_16[4], ~IR_23_16[5], IR_23_16[6], ~IR_23_16[7]);  // AND_Gate
  and u__70 (_70, ~IR_23_16[0], IR_23_16[1], IR_23_16[2], ~IR_23_16[3], ~IR_23_16[4], ~IR_23_16[5], IR_23_16[6], ~IR_23_16[7]);  // AND_Gate
  and u__71 (_71, IR_23_16[0], IR_23_16[1], IR_23_16[2], ~IR_23_16[3], ~IR_23_16[4], ~IR_23_16[5], IR_23_16[6], ~IR_23_16[7]);  // AND_Gate
  and u__72 (_72, ~IR_23_16[0], ~IR_23_16[1], ~IR_23_16[2], IR_23_16[3], ~IR_23_16[4], ~IR_23_16[5], IR_23_16[6], ~IR_23_16[7]);  // AND_Gate
  and u__73 (_73, IR_23_16[0], ~IR_23_16[1], ~IR_23_16[2], IR_23_16[3], ~IR_23_16[4], ~IR_23_16[5], IR_23_16[6], ~IR_23_16[7]);  // AND_Gate
  and u__74 (_74, ~IR_23_16[0], IR_23_16[1], ~IR_23_16[2], IR_23_16[3], ~IR_23_16[4], ~IR_23_16[5], IR_23_16[6], ~IR_23_16[7]);  // AND_Gate
  and u__75 (_75, IR_23_16[0], IR_23_16[1], ~IR_23_16[2], IR_23_16[3], ~IR_23_16[4], ~IR_23_16[5], IR_23_16[6], ~IR_23_16[7]);  // AND_Gate
  and u__76 (_76, ~IR_23_16[0], ~IR_23_16[1], IR_23_16[2], IR_23_16[3], ~IR_23_16[4], ~IR_23_16[5], IR_23_16[6], ~IR_23_16[7]);  // AND_Gate
  and u__77 (_77, IR_23_16[0], ~IR_23_16[1], IR_23_16[2], IR_23_16[3], ~IR_23_16[4], ~IR_23_16[5], IR_23_16[6], ~IR_23_16[7]);  // AND_Gate
  and u__78 (_78, ~IR_23_16[0], IR_23_16[1], IR_23_16[2], IR_23_16[3], ~IR_23_16[4], ~IR_23_16[5], IR_23_16[6], ~IR_23_16[7]);  // AND_Gate
  and u__79 (_79, IR_23_16[0], IR_23_16[1], IR_23_16[2], IR_23_16[3], ~IR_23_16[4], ~IR_23_16[5], IR_23_16[6], ~IR_23_16[7]);  // AND_Gate
  and u__80 (_80, ~IR_23_16[0], ~IR_23_16[1], ~IR_23_16[2], ~IR_23_16[3], IR_23_16[4], ~IR_23_16[5], IR_23_16[6], ~IR_23_16[7]);  // AND_Gate
  and u__81 (_81, IR_23_16[0], ~IR_23_16[1], ~IR_23_16[2], ~IR_23_16[3], IR_23_16[4], ~IR_23_16[5], IR_23_16[6], ~IR_23_16[7]);  // AND_Gate
  and u__82 (_82, ~IR_23_16[0], IR_23_16[1], ~IR_23_16[2], ~IR_23_16[3], IR_23_16[4], ~IR_23_16[5], IR_23_16[6], ~IR_23_16[7]);  // AND_Gate
  and u__83 (_83, IR_23_16[0], IR_23_16[1], ~IR_23_16[2], ~IR_23_16[3], IR_23_16[4], ~IR_23_16[5], IR_23_16[6], ~IR_23_16[7]);  // AND_Gate
  and u__84 (_84, ~IR_23_16[0], ~IR_23_16[1], IR_23_16[2], ~IR_23_16[3], IR_23_16[4], ~IR_23_16[5], IR_23_16[6], ~IR_23_16[7]);  // AND_Gate
  and u__85 (_85, IR_23_16[0], ~IR_23_16[1], IR_23_16[2], ~IR_23_16[3], IR_23_16[4], ~IR_23_16[5], IR_23_16[6], ~IR_23_16[7]);  // AND_Gate
  and u__86 (_86, ~IR_23_16[0], IR_23_16[1], IR_23_16[2], ~IR_23_16[3], IR_23_16[4], ~IR_23_16[5], IR_23_16[6], ~IR_23_16[7]);  // AND_Gate
  and u__87 (_87, IR_23_16[0], IR_23_16[1], IR_23_16[2], ~IR_23_16[3], IR_23_16[4], ~IR_23_16[5], IR_23_16[6], ~IR_23_16[7]);  // AND_Gate
  and u__88 (_88, ~IR_23_16[0], ~IR_23_16[1], ~IR_23_16[2], IR_23_16[3], IR_23_16[4], ~IR_23_16[5], IR_23_16[6], ~IR_23_16[7]);  // AND_Gate
  and u__89 (_89, IR_23_16[0], ~IR_23_16[1], ~IR_23_16[2], IR_23_16[3], IR_23_16[4], ~IR_23_16[5], IR_23_16[6], ~IR_23_16[7]);  // AND_Gate
  and u__90 (_90, ~IR_23_16[0], IR_23_16[1], ~IR_23_16[2], IR_23_16[3], IR_23_16[4], ~IR_23_16[5], IR_23_16[6], ~IR_23_16[7]);  // AND_Gate
  and u__91 (_91, IR_23_16[0], IR_23_16[1], ~IR_23_16[2], IR_23_16[3], IR_23_16[4], ~IR_23_16[5], IR_23_16[6], ~IR_23_16[7]);  // AND_Gate
  and u__92 (_92, ~IR_23_16[0], ~IR_23_16[1], IR_23_16[2], IR_23_16[3], IR_23_16[4], ~IR_23_16[5], IR_23_16[6], ~IR_23_16[7]);  // AND_Gate
  and u__93 (_93, IR_23_16[0], ~IR_23_16[1], IR_23_16[2], IR_23_16[3], IR_23_16[4], ~IR_23_16[5], IR_23_16[6], ~IR_23_16[7]);  // AND_Gate
  and u__94 (_94, ~IR_23_16[0], IR_23_16[1], IR_23_16[2], IR_23_16[3], IR_23_16[4], ~IR_23_16[5], IR_23_16[6], ~IR_23_16[7]);  // AND_Gate
  and u__95 (_95, IR_23_16[0], IR_23_16[1], IR_23_16[2], IR_23_16[3], IR_23_16[4], ~IR_23_16[5], IR_23_16[6], ~IR_23_16[7]);  // AND_Gate
  and u__96 (_96, ~IR_23_16[0], ~IR_23_16[1], ~IR_23_16[2], ~IR_23_16[3], ~IR_23_16[4], IR_23_16[5], IR_23_16[6], ~IR_23_16[7]);  // AND_Gate
  and u__97 (_97, IR_23_16[0], ~IR_23_16[1], ~IR_23_16[2], ~IR_23_16[3], ~IR_23_16[4], IR_23_16[5], IR_23_16[6], ~IR_23_16[7]);  // AND_Gate
  and u__98 (_98, ~IR_23_16[0], IR_23_16[1], ~IR_23_16[2], ~IR_23_16[3], ~IR_23_16[4], IR_23_16[5], IR_23_16[6], ~IR_23_16[7]);  // AND_Gate
  and u__99 (_99, IR_23_16[0], IR_23_16[1], ~IR_23_16[2], ~IR_23_16[3], ~IR_23_16[4], IR_23_16[5], IR_23_16[6], ~IR_23_16[7]);  // AND_Gate
  and u__100 (_100, ~IR_23_16[0], ~IR_23_16[1], IR_23_16[2], ~IR_23_16[3], ~IR_23_16[4], IR_23_16[5], IR_23_16[6], ~IR_23_16[7]);  // AND_Gate
  and u__101 (_101, IR_23_16[0], ~IR_23_16[1], IR_23_16[2], ~IR_23_16[3], ~IR_23_16[4], IR_23_16[5], IR_23_16[6], ~IR_23_16[7]);  // AND_Gate
  and u__102 (_102, ~IR_23_16[0], IR_23_16[1], IR_23_16[2], ~IR_23_16[3], ~IR_23_16[4], IR_23_16[5], IR_23_16[6], ~IR_23_16[7]);  // AND_Gate
  and u__103 (_103, IR_23_16[0], IR_23_16[1], IR_23_16[2], ~IR_23_16[3], ~IR_23_16[4], IR_23_16[5], IR_23_16[6], ~IR_23_16[7]);  // AND_Gate
  and u__104 (_104, ~IR_23_16[0], ~IR_23_16[1], ~IR_23_16[2], IR_23_16[3], ~IR_23_16[4], IR_23_16[5], IR_23_16[6], ~IR_23_16[7]);  // AND_Gate
  and u__105 (_105, IR_23_16[0], ~IR_23_16[1], ~IR_23_16[2], IR_23_16[3], ~IR_23_16[4], IR_23_16[5], IR_23_16[6], ~IR_23_16[7]);  // AND_Gate
  and u__106 (_106, ~IR_23_16[0], IR_23_16[1], ~IR_23_16[2], IR_23_16[3], ~IR_23_16[4], IR_23_16[5], IR_23_16[6], ~IR_23_16[7]);  // AND_Gate
  and u__107 (_107, IR_23_16[0], IR_23_16[1], ~IR_23_16[2], IR_23_16[3], ~IR_23_16[4], IR_23_16[5], IR_23_16[6], ~IR_23_16[7]);  // AND_Gate
  and u__108 (_108, ~IR_23_16[0], ~IR_23_16[1], IR_23_16[2], IR_23_16[3], ~IR_23_16[4], IR_23_16[5], IR_23_16[6], ~IR_23_16[7]);  // AND_Gate
  and u__109 (_109, IR_23_16[0], ~IR_23_16[1], IR_23_16[2], IR_23_16[3], ~IR_23_16[4], IR_23_16[5], IR_23_16[6], ~IR_23_16[7]);  // AND_Gate
  and u__110 (_110, ~IR_23_16[0], IR_23_16[1], IR_23_16[2], IR_23_16[3], ~IR_23_16[4], IR_23_16[5], IR_23_16[6], ~IR_23_16[7]);  // AND_Gate
  and u__111 (_111, IR_23_16[0], IR_23_16[1], IR_23_16[2], IR_23_16[3], ~IR_23_16[4], IR_23_16[5], IR_23_16[6], ~IR_23_16[7]);  // AND_Gate
  and u__112 (_112, ~IR_23_16[0], ~IR_23_16[1], ~IR_23_16[2], ~IR_23_16[3], IR_23_16[4], IR_23_16[5], IR_23_16[6], ~IR_23_16[7]);  // AND_Gate
  and u__113 (_113, IR_23_16[0], ~IR_23_16[1], ~IR_23_16[2], ~IR_23_16[3], IR_23_16[4], IR_23_16[5], IR_23_16[6], ~IR_23_16[7]);  // AND_Gate
  and u__114 (_114, ~IR_23_16[0], IR_23_16[1], ~IR_23_16[2], ~IR_23_16[3], IR_23_16[4], IR_23_16[5], IR_23_16[6], ~IR_23_16[7]);  // AND_Gate
  and u__115 (_115, IR_23_16[0], IR_23_16[1], ~IR_23_16[2], ~IR_23_16[3], IR_23_16[4], IR_23_16[5], IR_23_16[6], ~IR_23_16[7]);  // AND_Gate
  and u__116 (_116, ~IR_23_16[0], ~IR_23_16[1], IR_23_16[2], ~IR_23_16[3], IR_23_16[4], IR_23_16[5], IR_23_16[6], ~IR_23_16[7]);  // AND_Gate
  and u__117 (_117, IR_23_16[0], ~IR_23_16[1], IR_23_16[2], ~IR_23_16[3], IR_23_16[4], IR_23_16[5], IR_23_16[6], ~IR_23_16[7]);  // AND_Gate
  and u__118 (_118, ~IR_23_16[0], IR_23_16[1], IR_23_16[2], ~IR_23_16[3], IR_23_16[4], IR_23_16[5], IR_23_16[6], ~IR_23_16[7]);  // AND_Gate
  and u__119 (_119, IR_23_16[0], IR_23_16[1], IR_23_16[2], ~IR_23_16[3], IR_23_16[4], IR_23_16[5], IR_23_16[6], ~IR_23_16[7]);  // AND_Gate
  and u__120 (_120, ~IR_23_16[0], ~IR_23_16[1], ~IR_23_16[2], IR_23_16[3], IR_23_16[4], IR_23_16[5], IR_23_16[6], ~IR_23_16[7]);  // AND_Gate
  and u__121 (_121, IR_23_16[0], ~IR_23_16[1], ~IR_23_16[2], IR_23_16[3], IR_23_16[4], IR_23_16[5], IR_23_16[6], ~IR_23_16[7]);  // AND_Gate
  and u__122 (_122, ~IR_23_16[0], IR_23_16[1], ~IR_23_16[2], IR_23_16[3], IR_23_16[4], IR_23_16[5], IR_23_16[6], ~IR_23_16[7]);  // AND_Gate
  and u__123 (_123, IR_23_16[0], IR_23_16[1], ~IR_23_16[2], IR_23_16[3], IR_23_16[4], IR_23_16[5], IR_23_16[6], ~IR_23_16[7]);  // AND_Gate
  and u__124 (_124, ~IR_23_16[0], ~IR_23_16[1], IR_23_16[2], IR_23_16[3], IR_23_16[4], IR_23_16[5], IR_23_16[6], ~IR_23_16[7]);  // AND_Gate
  and u__125 (_125, IR_23_16[0], ~IR_23_16[1], IR_23_16[2], IR_23_16[3], IR_23_16[4], IR_23_16[5], IR_23_16[6], ~IR_23_16[7]);  // AND_Gate
  and u__126 (_126, ~IR_23_16[0], IR_23_16[1], IR_23_16[2], IR_23_16[3], IR_23_16[4], IR_23_16[5], IR_23_16[6], ~IR_23_16[7]);  // AND_Gate
  and u__127 (_127, IR_23_16[0], IR_23_16[1], IR_23_16[2], IR_23_16[3], IR_23_16[4], IR_23_16[5], IR_23_16[6], ~IR_23_16[7]);  // AND_Gate
  and u__128 (_128, ~IR_23_16[0], ~IR_23_16[1], ~IR_23_16[2], ~IR_23_16[3], ~IR_23_16[4], ~IR_23_16[5], ~IR_23_16[6], IR_23_16[7]);  // AND_Gate
  and u__129 (_129, IR_23_16[0], ~IR_23_16[1], ~IR_23_16[2], ~IR_23_16[3], ~IR_23_16[4], ~IR_23_16[5], ~IR_23_16[6], IR_23_16[7]);  // AND_Gate
  and u__130 (_130, ~IR_23_16[0], IR_23_16[1], ~IR_23_16[2], ~IR_23_16[3], ~IR_23_16[4], ~IR_23_16[5], ~IR_23_16[6], IR_23_16[7]);  // AND_Gate
  and u__131 (_131, IR_23_16[0], IR_23_16[1], ~IR_23_16[2], ~IR_23_16[3], ~IR_23_16[4], ~IR_23_16[5], ~IR_23_16[6], IR_23_16[7]);  // AND_Gate
  and u__132 (_132, ~IR_23_16[0], ~IR_23_16[1], IR_23_16[2], ~IR_23_16[3], ~IR_23_16[4], ~IR_23_16[5], ~IR_23_16[6], IR_23_16[7]);  // AND_Gate
  and u__133 (_133, IR_23_16[0], ~IR_23_16[1], IR_23_16[2], ~IR_23_16[3], ~IR_23_16[4], ~IR_23_16[5], ~IR_23_16[6], IR_23_16[7]);  // AND_Gate
  and u__134 (_134, ~IR_23_16[0], IR_23_16[1], IR_23_16[2], ~IR_23_16[3], ~IR_23_16[4], ~IR_23_16[5], ~IR_23_16[6], IR_23_16[7]);  // AND_Gate
  and u__135 (_135, IR_23_16[0], IR_23_16[1], IR_23_16[2], ~IR_23_16[3], ~IR_23_16[4], ~IR_23_16[5], ~IR_23_16[6], IR_23_16[7]);  // AND_Gate
  and u__136 (_136, ~IR_23_16[0], ~IR_23_16[1], ~IR_23_16[2], IR_23_16[3], ~IR_23_16[4], ~IR_23_16[5], ~IR_23_16[6], IR_23_16[7]);  // AND_Gate
  and u__137 (_137, IR_23_16[0], ~IR_23_16[1], ~IR_23_16[2], IR_23_16[3], ~IR_23_16[4], ~IR_23_16[5], ~IR_23_16[6], IR_23_16[7]);  // AND_Gate
  and u__138 (_138, ~IR_23_16[0], IR_23_16[1], ~IR_23_16[2], IR_23_16[3], ~IR_23_16[4], ~IR_23_16[5], ~IR_23_16[6], IR_23_16[7]);  // AND_Gate
  and u__139 (_139, IR_23_16[0], IR_23_16[1], ~IR_23_16[2], IR_23_16[3], ~IR_23_16[4], ~IR_23_16[5], ~IR_23_16[6], IR_23_16[7]);  // AND_Gate
  and u__140 (_140, ~IR_23_16[0], ~IR_23_16[1], IR_23_16[2], IR_23_16[3], ~IR_23_16[4], ~IR_23_16[5], ~IR_23_16[6], IR_23_16[7]);  // AND_Gate
  and u__141 (_141, IR_23_16[0], ~IR_23_16[1], IR_23_16[2], IR_23_16[3], ~IR_23_16[4], ~IR_23_16[5], ~IR_23_16[6], IR_23_16[7]);  // AND_Gate
  and u__142 (_142, ~IR_23_16[0], IR_23_16[1], IR_23_16[2], IR_23_16[3], ~IR_23_16[4], ~IR_23_16[5], ~IR_23_16[6], IR_23_16[7]);  // AND_Gate
  and u__143 (_143, IR_23_16[0], IR_23_16[1], IR_23_16[2], IR_23_16[3], ~IR_23_16[4], ~IR_23_16[5], ~IR_23_16[6], IR_23_16[7]);  // AND_Gate
  and u__144 (_144, ~IR_23_16[0], ~IR_23_16[1], ~IR_23_16[2], ~IR_23_16[3], IR_23_16[4], ~IR_23_16[5], ~IR_23_16[6], IR_23_16[7]);  // AND_Gate
  and u__145 (_145, IR_23_16[0], ~IR_23_16[1], ~IR_23_16[2], ~IR_23_16[3], IR_23_16[4], ~IR_23_16[5], ~IR_23_16[6], IR_23_16[7]);  // AND_Gate
  and u__146 (_146, ~IR_23_16[0], IR_23_16[1], ~IR_23_16[2], ~IR_23_16[3], IR_23_16[4], ~IR_23_16[5], ~IR_23_16[6], IR_23_16[7]);  // AND_Gate
  and u__147 (_147, IR_23_16[0], IR_23_16[1], ~IR_23_16[2], ~IR_23_16[3], IR_23_16[4], ~IR_23_16[5], ~IR_23_16[6], IR_23_16[7]);  // AND_Gate
  and u__148 (_148, ~IR_23_16[0], ~IR_23_16[1], IR_23_16[2], ~IR_23_16[3], IR_23_16[4], ~IR_23_16[5], ~IR_23_16[6], IR_23_16[7]);  // AND_Gate
  and u__149 (_149, IR_23_16[0], ~IR_23_16[1], IR_23_16[2], ~IR_23_16[3], IR_23_16[4], ~IR_23_16[5], ~IR_23_16[6], IR_23_16[7]);  // AND_Gate
  and u__150 (_150, ~IR_23_16[0], IR_23_16[1], IR_23_16[2], ~IR_23_16[3], IR_23_16[4], ~IR_23_16[5], ~IR_23_16[6], IR_23_16[7]);  // AND_Gate
  and u__151 (_151, IR_23_16[0], IR_23_16[1], IR_23_16[2], ~IR_23_16[3], IR_23_16[4], ~IR_23_16[5], ~IR_23_16[6], IR_23_16[7]);  // AND_Gate
  and u__152 (_152, ~IR_23_16[0], ~IR_23_16[1], ~IR_23_16[2], IR_23_16[3], IR_23_16[4], ~IR_23_16[5], ~IR_23_16[6], IR_23_16[7]);  // AND_Gate
  and u__153 (_153, IR_23_16[0], ~IR_23_16[1], ~IR_23_16[2], IR_23_16[3], IR_23_16[4], ~IR_23_16[5], ~IR_23_16[6], IR_23_16[7]);  // AND_Gate
  and u__154 (_154, ~IR_23_16[0], IR_23_16[1], ~IR_23_16[2], IR_23_16[3], IR_23_16[4], ~IR_23_16[5], ~IR_23_16[6], IR_23_16[7]);  // AND_Gate
  and u__155 (_155, IR_23_16[0], IR_23_16[1], ~IR_23_16[2], IR_23_16[3], IR_23_16[4], ~IR_23_16[5], ~IR_23_16[6], IR_23_16[7]);  // AND_Gate
  and u__156 (_156, ~IR_23_16[0], ~IR_23_16[1], IR_23_16[2], IR_23_16[3], IR_23_16[4], ~IR_23_16[5], ~IR_23_16[6], IR_23_16[7]);  // AND_Gate
  and u__157 (_157, IR_23_16[0], ~IR_23_16[1], IR_23_16[2], IR_23_16[3], IR_23_16[4], ~IR_23_16[5], ~IR_23_16[6], IR_23_16[7]);  // AND_Gate
  and u__158 (_158, ~IR_23_16[0], IR_23_16[1], IR_23_16[2], IR_23_16[3], IR_23_16[4], ~IR_23_16[5], ~IR_23_16[6], IR_23_16[7]);  // AND_Gate
  and u__159 (_159, IR_23_16[0], IR_23_16[1], IR_23_16[2], IR_23_16[3], IR_23_16[4], ~IR_23_16[5], ~IR_23_16[6], IR_23_16[7]);  // AND_Gate
  and u__160 (_160, ~IR_23_16[0], ~IR_23_16[1], ~IR_23_16[2], ~IR_23_16[3], ~IR_23_16[4], IR_23_16[5], ~IR_23_16[6], IR_23_16[7]);  // AND_Gate
  and u__161 (_161, IR_23_16[0], ~IR_23_16[1], ~IR_23_16[2], ~IR_23_16[3], ~IR_23_16[4], IR_23_16[5], ~IR_23_16[6], IR_23_16[7]);  // AND_Gate
  and u__162 (_162, ~IR_23_16[0], IR_23_16[1], ~IR_23_16[2], ~IR_23_16[3], ~IR_23_16[4], IR_23_16[5], ~IR_23_16[6], IR_23_16[7]);  // AND_Gate
  and u__163 (_163, IR_23_16[0], IR_23_16[1], ~IR_23_16[2], ~IR_23_16[3], ~IR_23_16[4], IR_23_16[5], ~IR_23_16[6], IR_23_16[7]);  // AND_Gate
  and u__164 (_164, ~IR_23_16[0], ~IR_23_16[1], IR_23_16[2], ~IR_23_16[3], ~IR_23_16[4], IR_23_16[5], ~IR_23_16[6], IR_23_16[7]);  // AND_Gate
  and u__165 (_165, IR_23_16[0], ~IR_23_16[1], IR_23_16[2], ~IR_23_16[3], ~IR_23_16[4], IR_23_16[5], ~IR_23_16[6], IR_23_16[7]);  // AND_Gate
  and u__166 (_166, ~IR_23_16[0], IR_23_16[1], IR_23_16[2], ~IR_23_16[3], ~IR_23_16[4], IR_23_16[5], ~IR_23_16[6], IR_23_16[7]);  // AND_Gate
  and u__167 (_167, IR_23_16[0], IR_23_16[1], IR_23_16[2], ~IR_23_16[3], ~IR_23_16[4], IR_23_16[5], ~IR_23_16[6], IR_23_16[7]);  // AND_Gate
  and u__168 (_168, ~IR_23_16[0], ~IR_23_16[1], ~IR_23_16[2], IR_23_16[3], ~IR_23_16[4], IR_23_16[5], ~IR_23_16[6], IR_23_16[7]);  // AND_Gate
  and u__169 (_169, IR_23_16[0], ~IR_23_16[1], ~IR_23_16[2], IR_23_16[3], ~IR_23_16[4], IR_23_16[5], ~IR_23_16[6], IR_23_16[7]);  // AND_Gate
  and u__170 (_170, ~IR_23_16[0], IR_23_16[1], ~IR_23_16[2], IR_23_16[3], ~IR_23_16[4], IR_23_16[5], ~IR_23_16[6], IR_23_16[7]);  // AND_Gate
  and u__171 (_171, IR_23_16[0], IR_23_16[1], ~IR_23_16[2], IR_23_16[3], ~IR_23_16[4], IR_23_16[5], ~IR_23_16[6], IR_23_16[7]);  // AND_Gate
  and u__172 (_172, ~IR_23_16[0], ~IR_23_16[1], IR_23_16[2], IR_23_16[3], ~IR_23_16[4], IR_23_16[5], ~IR_23_16[6], IR_23_16[7]);  // AND_Gate
  and u__173 (_173, IR_23_16[0], ~IR_23_16[1], IR_23_16[2], IR_23_16[3], ~IR_23_16[4], IR_23_16[5], ~IR_23_16[6], IR_23_16[7]);  // AND_Gate
  and u__174 (_174, ~IR_23_16[0], IR_23_16[1], IR_23_16[2], IR_23_16[3], ~IR_23_16[4], IR_23_16[5], ~IR_23_16[6], IR_23_16[7]);  // AND_Gate
  and u__175 (_175, IR_23_16[0], IR_23_16[1], IR_23_16[2], IR_23_16[3], ~IR_23_16[4], IR_23_16[5], ~IR_23_16[6], IR_23_16[7]);  // AND_Gate
  and u__176 (_176, ~IR_23_16[0], ~IR_23_16[1], ~IR_23_16[2], ~IR_23_16[3], IR_23_16[4], IR_23_16[5], ~IR_23_16[6], IR_23_16[7]);  // AND_Gate
  and u__177 (_177, IR_23_16[0], ~IR_23_16[1], ~IR_23_16[2], ~IR_23_16[3], IR_23_16[4], IR_23_16[5], ~IR_23_16[6], IR_23_16[7]);  // AND_Gate
  and u__178 (_178, ~IR_23_16[0], IR_23_16[1], ~IR_23_16[2], ~IR_23_16[3], IR_23_16[4], IR_23_16[5], ~IR_23_16[6], IR_23_16[7]);  // AND_Gate
  and u__179 (_179, IR_23_16[0], IR_23_16[1], ~IR_23_16[2], ~IR_23_16[3], IR_23_16[4], IR_23_16[5], ~IR_23_16[6], IR_23_16[7]);  // AND_Gate
  and u__180 (_180, ~IR_23_16[0], ~IR_23_16[1], IR_23_16[2], ~IR_23_16[3], IR_23_16[4], IR_23_16[5], ~IR_23_16[6], IR_23_16[7]);  // AND_Gate
  and u__181 (_181, IR_23_16[0], ~IR_23_16[1], IR_23_16[2], ~IR_23_16[3], IR_23_16[4], IR_23_16[5], ~IR_23_16[6], IR_23_16[7]);  // AND_Gate
  and u__182 (_182, ~IR_23_16[0], IR_23_16[1], IR_23_16[2], ~IR_23_16[3], IR_23_16[4], IR_23_16[5], ~IR_23_16[6], IR_23_16[7]);  // AND_Gate
  and u__183 (_183, IR_23_16[0], IR_23_16[1], IR_23_16[2], ~IR_23_16[3], IR_23_16[4], IR_23_16[5], ~IR_23_16[6], IR_23_16[7]);  // AND_Gate
  and u__184 (_184, ~IR_23_16[0], ~IR_23_16[1], ~IR_23_16[2], IR_23_16[3], IR_23_16[4], IR_23_16[5], ~IR_23_16[6], IR_23_16[7]);  // AND_Gate
  and u__185 (_185, IR_23_16[0], ~IR_23_16[1], ~IR_23_16[2], IR_23_16[3], IR_23_16[4], IR_23_16[5], ~IR_23_16[6], IR_23_16[7]);  // AND_Gate
  and u__186 (_186, ~IR_23_16[0], IR_23_16[1], ~IR_23_16[2], IR_23_16[3], IR_23_16[4], IR_23_16[5], ~IR_23_16[6], IR_23_16[7]);  // AND_Gate
  and u__187 (_187, IR_23_16[0], IR_23_16[1], ~IR_23_16[2], IR_23_16[3], IR_23_16[4], IR_23_16[5], ~IR_23_16[6], IR_23_16[7]);  // AND_Gate
  and u__188 (_188, ~IR_23_16[0], ~IR_23_16[1], IR_23_16[2], IR_23_16[3], IR_23_16[4], IR_23_16[5], ~IR_23_16[6], IR_23_16[7]);  // AND_Gate
  and u__189 (_189, IR_23_16[0], ~IR_23_16[1], IR_23_16[2], IR_23_16[3], IR_23_16[4], IR_23_16[5], ~IR_23_16[6], IR_23_16[7]);  // AND_Gate
  and u__190 (_190, ~IR_23_16[0], IR_23_16[1], IR_23_16[2], IR_23_16[3], IR_23_16[4], IR_23_16[5], ~IR_23_16[6], IR_23_16[7]);  // AND_Gate
  and u__191 (_191, IR_23_16[0], IR_23_16[1], IR_23_16[2], IR_23_16[3], IR_23_16[4], IR_23_16[5], ~IR_23_16[6], IR_23_16[7]);  // AND_Gate
  and u__192 (_192, ~IR_23_16[0], ~IR_23_16[1], ~IR_23_16[2], ~IR_23_16[3], ~IR_23_16[4], ~IR_23_16[5], IR_23_16[6], IR_23_16[7]);  // AND_Gate
  and u__193 (_193, IR_23_16[0], ~IR_23_16[1], ~IR_23_16[2], ~IR_23_16[3], ~IR_23_16[4], ~IR_23_16[5], IR_23_16[6], IR_23_16[7]);  // AND_Gate
  and u__194 (_194, ~IR_23_16[0], IR_23_16[1], ~IR_23_16[2], ~IR_23_16[3], ~IR_23_16[4], ~IR_23_16[5], IR_23_16[6], IR_23_16[7]);  // AND_Gate
  and u__195 (_195, IR_23_16[0], IR_23_16[1], ~IR_23_16[2], ~IR_23_16[3], ~IR_23_16[4], ~IR_23_16[5], IR_23_16[6], IR_23_16[7]);  // AND_Gate
  and u__196 (_196, ~IR_23_16[0], ~IR_23_16[1], IR_23_16[2], ~IR_23_16[3], ~IR_23_16[4], ~IR_23_16[5], IR_23_16[6], IR_23_16[7]);  // AND_Gate
  and u__197 (_197, IR_23_16[0], ~IR_23_16[1], IR_23_16[2], ~IR_23_16[3], ~IR_23_16[4], ~IR_23_16[5], IR_23_16[6], IR_23_16[7]);  // AND_Gate
  and u__198 (_198, ~IR_23_16[0], IR_23_16[1], IR_23_16[2], ~IR_23_16[3], ~IR_23_16[4], ~IR_23_16[5], IR_23_16[6], IR_23_16[7]);  // AND_Gate
  and u__199 (_199, IR_23_16[0], IR_23_16[1], IR_23_16[2], ~IR_23_16[3], ~IR_23_16[4], ~IR_23_16[5], IR_23_16[6], IR_23_16[7]);  // AND_Gate
  and u__200 (_200, ~IR_23_16[0], ~IR_23_16[1], ~IR_23_16[2], IR_23_16[3], ~IR_23_16[4], ~IR_23_16[5], IR_23_16[6], IR_23_16[7]);  // AND_Gate
  and u__201 (_201, IR_23_16[0], ~IR_23_16[1], ~IR_23_16[2], IR_23_16[3], ~IR_23_16[4], ~IR_23_16[5], IR_23_16[6], IR_23_16[7]);  // AND_Gate
  and u__202 (_202, ~IR_23_16[0], IR_23_16[1], ~IR_23_16[2], IR_23_16[3], ~IR_23_16[4], ~IR_23_16[5], IR_23_16[6], IR_23_16[7]);  // AND_Gate
  and u__203 (_203, IR_23_16[0], IR_23_16[1], ~IR_23_16[2], IR_23_16[3], ~IR_23_16[4], ~IR_23_16[5], IR_23_16[6], IR_23_16[7]);  // AND_Gate
  and u__204 (_204, ~IR_23_16[0], ~IR_23_16[1], IR_23_16[2], IR_23_16[3], ~IR_23_16[4], ~IR_23_16[5], IR_23_16[6], IR_23_16[7]);  // AND_Gate
  and u__205 (_205, IR_23_16[0], ~IR_23_16[1], IR_23_16[2], IR_23_16[3], ~IR_23_16[4], ~IR_23_16[5], IR_23_16[6], IR_23_16[7]);  // AND_Gate
  and u__206 (_206, ~IR_23_16[0], IR_23_16[1], IR_23_16[2], IR_23_16[3], ~IR_23_16[4], ~IR_23_16[5], IR_23_16[6], IR_23_16[7]);  // AND_Gate
  and u__207 (_207, IR_23_16[0], IR_23_16[1], IR_23_16[2], IR_23_16[3], ~IR_23_16[4], ~IR_23_16[5], IR_23_16[6], IR_23_16[7]);  // AND_Gate
  and u__208 (_208, ~IR_23_16[0], ~IR_23_16[1], ~IR_23_16[2], ~IR_23_16[3], IR_23_16[4], ~IR_23_16[5], IR_23_16[6], IR_23_16[7]);  // AND_Gate
  and u__209 (_209, IR_23_16[0], ~IR_23_16[1], ~IR_23_16[2], ~IR_23_16[3], IR_23_16[4], ~IR_23_16[5], IR_23_16[6], IR_23_16[7]);  // AND_Gate
  and u__210 (_210, ~IR_23_16[0], IR_23_16[1], ~IR_23_16[2], ~IR_23_16[3], IR_23_16[4], ~IR_23_16[5], IR_23_16[6], IR_23_16[7]);  // AND_Gate
  and u__211 (_211, IR_23_16[0], IR_23_16[1], ~IR_23_16[2], ~IR_23_16[3], IR_23_16[4], ~IR_23_16[5], IR_23_16[6], IR_23_16[7]);  // AND_Gate
  and u__212 (_212, ~IR_23_16[0], ~IR_23_16[1], IR_23_16[2], ~IR_23_16[3], IR_23_16[4], ~IR_23_16[5], IR_23_16[6], IR_23_16[7]);  // AND_Gate
  and u__213 (_213, IR_23_16[0], ~IR_23_16[1], IR_23_16[2], ~IR_23_16[3], IR_23_16[4], ~IR_23_16[5], IR_23_16[6], IR_23_16[7]);  // AND_Gate
  and u__214 (_214, ~IR_23_16[0], IR_23_16[1], IR_23_16[2], ~IR_23_16[3], IR_23_16[4], ~IR_23_16[5], IR_23_16[6], IR_23_16[7]);  // AND_Gate
  and u__215 (_215, IR_23_16[0], IR_23_16[1], IR_23_16[2], ~IR_23_16[3], IR_23_16[4], ~IR_23_16[5], IR_23_16[6], IR_23_16[7]);  // AND_Gate
  and u__216 (_216, ~IR_23_16[0], ~IR_23_16[1], ~IR_23_16[2], IR_23_16[3], IR_23_16[4], ~IR_23_16[5], IR_23_16[6], IR_23_16[7]);  // AND_Gate
  and u__217 (_217, IR_23_16[0], ~IR_23_16[1], ~IR_23_16[2], IR_23_16[3], IR_23_16[4], ~IR_23_16[5], IR_23_16[6], IR_23_16[7]);  // AND_Gate
  and u__218 (_218, ~IR_23_16[0], IR_23_16[1], ~IR_23_16[2], IR_23_16[3], IR_23_16[4], ~IR_23_16[5], IR_23_16[6], IR_23_16[7]);  // AND_Gate
  and u__219 (_219, IR_23_16[0], IR_23_16[1], ~IR_23_16[2], IR_23_16[3], IR_23_16[4], ~IR_23_16[5], IR_23_16[6], IR_23_16[7]);  // AND_Gate
  and u__220 (_220, ~IR_23_16[0], ~IR_23_16[1], IR_23_16[2], IR_23_16[3], IR_23_16[4], ~IR_23_16[5], IR_23_16[6], IR_23_16[7]);  // AND_Gate
  and u__221 (_221, IR_23_16[0], ~IR_23_16[1], IR_23_16[2], IR_23_16[3], IR_23_16[4], ~IR_23_16[5], IR_23_16[6], IR_23_16[7]);  // AND_Gate
  and u__222 (_222, ~IR_23_16[0], IR_23_16[1], IR_23_16[2], IR_23_16[3], IR_23_16[4], ~IR_23_16[5], IR_23_16[6], IR_23_16[7]);  // AND_Gate
  and u__223 (_223, IR_23_16[0], IR_23_16[1], IR_23_16[2], IR_23_16[3], IR_23_16[4], ~IR_23_16[5], IR_23_16[6], IR_23_16[7]);  // AND_Gate
  and u__224 (_224, ~IR_23_16[0], ~IR_23_16[1], ~IR_23_16[2], ~IR_23_16[3], ~IR_23_16[4], IR_23_16[5], IR_23_16[6], IR_23_16[7]);  // AND_Gate
  and u__225 (_225, IR_23_16[0], ~IR_23_16[1], ~IR_23_16[2], ~IR_23_16[3], ~IR_23_16[4], IR_23_16[5], IR_23_16[6], IR_23_16[7]);  // AND_Gate
  and u__226 (_226, ~IR_23_16[0], IR_23_16[1], ~IR_23_16[2], ~IR_23_16[3], ~IR_23_16[4], IR_23_16[5], IR_23_16[6], IR_23_16[7]);  // AND_Gate
endmodule

module COUNTER_RESET (
  input  T3,
  input  T4,
  input  T5,
  input  M0,
  input  M1,
  input  M2,
  input  M3,
  input  M4,
  input  M5,
  input  M6,
  input  M7,
  input  M8,
  input  M9,
  input  M10,
  input  M11,
  input  M12,
  input  M13,
  input  M14,
  input  M15,
  input  M16,
  input  M17,
  input  M18,
  input  M19,
  input  M20,
  input  M21,
  input  M22,
  input  M23,
  input  M24,
  input  M25,
  input  M26,
  input  M27,
  input  M28,
  input  M29,
  input  M30,
  input  M31,
  input  M32,
  input  M33,
  input  M34,
  input  M35,
  input  M36,
  input  M37,
  input  M38,
  input  M39,
  input  M40,
  input  M41,
  input  M42,
  input  M43,
  input  M44,
  input  M45,
  input  M46,
  input  M47,
  input  M48,
  input  M49,
  input  M50,
  input  M51,
  input  M52,
  input  M53,
  input  M54,
  input  M55,
  input  M56,
  input  M57,
  input  M58,
  input  M59,
  input  M60,
  input  M61,
  input  M62,
  input  M63,
  input  M64,
  input  M65,
  input  M66,
  input  M67,
  input  M68,
  input  M69,
  input  M70,
  input  M71,
  input  M72,
  input  M73,
  input  M74,
  input  M75,
  input  M76,
  input  M77,
  input  M78,
  input  M79,
  input  M80,
  input  M81,
  input  M82,
  input  M83,
  input  M84,
  input  M85,
  input  M86,
  input  M87,
  input  M88,
  input  M89,
  input  M90,
  input  M91,
  input  M92,
  input  M93,
  input  M94,
  input  M95,
  input  M96,
  input  M97,
  input  M98,
  input  M99,
  input  M100,
  input  M101,
  input  M102,
  input  M103,
  input  M104,
  input  M105,
  input  M106,
  input  M107,
  input  M108,
  input  M109,
  input  M110,
  input  M111,
  input  M112,
  input  M113,
  input  M114,
  input  M115,
  input  M116,
  input  M117,
  input  M118,
  input  M119,
  input  M120,
  input  M121,
  input  M122,
  input  M123,
  input  M124,
  input  M125,
  input  M126,
  input  M127,
  input  M128,
  input  M129,
  input  M130,
  input  M131,
  input  M132,
  input  M133,
  input  M134,
  input  M135,
  input  M136,
  input  M137,
  input  M138,
  input  M139,
  input  M140,
  input  M141,
  input  M142,
  input  M143,
  input  M144,
  input  M145,
  input  M146,
  input  M147,
  input  M148,
  input  M149,
  input  M150,
  input  M151,
  input  M152,
  input  M153,
  input  M154,
  input  M155,
  input  M156,
  input  M157,
  input  M158,
  input  M159,
  input  M160,
  input  M161,
  input  M162,
  input  M163,
  input  M164,
  input  M165,
  input  M166,
  input  M167,
  input  M168,
  input  M169,
  input  M170,
  input  M171,
  input  M172,
  input  M173,
  input  M174,
  input  M175,
  input  M176,
  input  M177,
  input  M178,
  input  M179,
  input  M180,
  input  M181,
  input  M182,
  input  M183,
  input  M184,
  input  M185,
  input  M186,
  input  M187,
  input  M188,
  input  M189,
  input  M190,
  input  M191,
  input  M192,
  input  M193,
  input  M194,
  input  M195,
  input  M196,
  input  M197,
  input  M198,
  input  M199,
  input  M200,
  input  M201,
  input  M202,
  input  M203,
  input  M204,
  input  M205,
  input  M206,
  input  M207,
  input  M208,
  input  M209,
  input  M210,
  input  M211,
  input  M212,
  input  M213,
  input  M214,
  input  M215,
  input  M216,
  input  M217,
  input  M218,
  input  M219,
  input  M220,
  input  M221,
  input  M222,
  input  M223,
  input  M224,
  input  M225
);

  wire or_1_out, or_2_out, or_3_out, or_4_out, or_5_out, or_6_out;

  or or_1 (or_1_out, M225, M224, M223, M222, M221, M220, M219, M218, M217, M216, M215, M214, M213, M212, M210, M209, M207, M206, M204, M203, M201, M200, M198, M197, M195, M194, M193, M192, M191, M190, M189, M188);
  or or_2 (or_2_out, or_1_out, M187, M186, M185, M169, M167, M166, M165, M164, M163, M152, M150, M149, M148, M147, M146, M135, M133, M132, M131, M130, M129, M118, M116, M115, M114, M113, M112, M101, M99, M98, M97);
  or or_3 (or_3_out, or_2_out, M96, M95, M84, M82, M81, M80, M79, M78, M67, M65, M64, M63, M62, M61, M50, M48, M47, M46, M45, M44, M33, M31, M30, M29, M28, M27, M16, M14, M13, M12, M11);
  or or_4 (or_4_out, M211, M208, M205, M202, M199, M196, M184, M183, M182, M181, M180, M179, M178, M177, M176, M175, M168, M162, M161, M160, M159, M158, M151, M145, M144, M143, M142, M141, M134, M128, M127, M126);
  buf or_5 (or_5_out, or_4_out);  // OR_Gate
  or or_6 (or_6_out, or_3_out, M10);
  // AND_Gate and_1 has open pins: in0=or_6_out, in1=T3, out=open
endmodule
