// Logisim project Microprocessor.circ as structural Verilog
module AND_1 (
  input  AX,
  input  BX,
  input  CX,
  input  DX,
  input  EX,
  input  DR,
  input  IR,
  input  AX__DR,
  input  BX__DR,
  input  CX__DR,
  input  DX__DR,
  input  EX__DR,
  input  AX__IR,
  input  BX__IR,
  input  CX__IR,
  input  DX__IR,
  input  EX__IR,
  input  AX__BX,
  input  AX__CX,
  input  AX__DX,
  input  AX__EX,
  input  BX__CX,
  input  BX__DX,
  input  BX__EX,
  input  CX__DX,
  input  CX__EX,
  input  DX__EX,
  output OUTPUT
);

  wire and_1_out, and_2_out, and_3_out, and_4_out, and_5_out, and_6_out, and_7_out, and_8_out, and_9_out,
       and_10_out, and_11_out, and_12_out, and_13_out, and_14_out, and_15_out, and_16_out, and_17_out,
       and_18_out, and_19_out, and_20_out;

  and and_1 (and_1_out, AX__DR, DR, AX);
  and and_2 (and_2_out, BX__DR, DR, BX);
  and and_3 (and_3_out, CX__DR, DR, CX);
  and and_4 (and_4_out, DX__DR, DR, DX);
  and and_5 (and_5_out, EX__DR, DR, EX);
  and and_6 (and_6_out, AX__IR, IR, AX);
  and and_7 (and_7_out, BX__IR, IR, BX);
  and and_8 (and_8_out, CX__IR, IR, CX);
  and and_9 (and_9_out, DX__IR, IR, DX);
  and and_10 (and_10_out, EX__IR, IR, EX);
  and and_11 (and_11_out, AX__BX, BX, AX);
  and and_12 (and_12_out, AX__CX, CX, AX);
  and and_13 (and_13_out, AX__DX, DX, AX);
  and and_14 (and_14_out, AX__EX, EX, AX);
  and and_15 (and_15_out, BX__CX, CX, BX);
  and and_16 (and_16_out, BX__DX, DX, BX);
  and and_17 (and_17_out, BX__EX, EX, BX);
  and and_18 (and_18_out, CX__DX, DX, CX);
  and and_19 (and_19_out, CX__EX, EX, CX);
  and and_20 (and_20_out, DX__EX, EX, CX);
  or or_1 (OUTPUT, and_1_out, and_2_out, and_3_out, and_4_out, and_5_out, and_6_out, and_7_out, and_8_out, and_9_out, and_10_out, and_11_out, and_12_out, and_13_out, and_14_out, and_15_out, and_16_out, and_17_out, and_18_out, and_19_out, and_20_out);
endmodule

module OR_1 (
  input  AX,
  input  BX,
  input  CX,
  input  DX,
  input  EX,
  input  DR,
  input  IR,
  input  AX__DR,
  input  BX__DR,
  input  CX__DR,
  input  DX__DR,
  input  EX__DR,
  input  AX__IR,
  input  BX__IR,
  input  CX__IR,
  input  DX__IR,
  input  EX__IR,
  input  AX__BX,
  input  AX__CX,
  input  AX__DX,
  input  AX__EX,
  input  BX__CX,
  input  BX__DX,
  input  BX__EX,
  input  CX__DX,
  input  CX__EX,
  input  DX__EX,
  output OUTPUT
);

  wire and_1_out, and_2_out, and_3_out, and_4_out, and_5_out, and_6_out, and_7_out, and_8_out, and_9_out,
       and_10_out, and_11_out, and_12_out, and_13_out, and_14_out, and_15_out, and_16_out, and_17_out,
       and_18_out, and_19_out, and_20_out, or_1_out, or_2_out, or_3_out, or_4_out, or_5_out, or_6_out,
       or_7_out, or_8_out, or_9_out, or_10_out, or_11_out, or_12_out, or_13_out, or_14_out, or_15_out,
       or_16_out, or_17_out, or_18_out, or_19_out, or_20_out;

  or or_1 (or_1_out, DR, AX);
  or or_2 (or_2_out, DR, BX);
  or or_3 (or_3_out, DR, CX);
  or or_4 (or_4_out, DR, DX);
  or or_5 (or_5_out, DR, EX);
  or or_6 (or_6_out, IR, AX);
  or or_7 (or_7_out, IR, BX);
  or or_8 (or_8_out, IR, CX);
  or or_9 (or_9_out, IR, DX);
  or or_10 (or_10_out, IR, EX);
  or or_11 (or_11_out, BX, AX);
  or or_12 (or_12_out, CX, AX);
  or or_13 (or_13_out, DX, AX);
  or or_14 (or_14_out, EX, AX);
  or or_15 (or_15_out, CX, BX);
  or or_16 (or_16_out, DX, BX);
  or or_17 (or_17_out, EX, BX);
  or or_18 (or_18_out, DX, CX);
  or or_19 (or_19_out, EX, CX);
  or or_20 (or_20_out, EX, CX);
  and and_1 (and_1_out, AX__DR, or_1_out);
  and and_2 (and_2_out, BX__DR, or_2_out);
  and and_3 (and_3_out, CX__DR, or_3_out);
  and and_4 (and_4_out, DX__DR, or_4_out);
  and and_5 (and_5_out, EX__DR, or_5_out);
  and and_6 (and_6_out, AX__IR, or_6_out);
  and and_7 (and_7_out, BX__IR, or_7_out);
  and and_8 (and_8_out, CX__IR, or_8_out);
  and and_9 (and_9_out, DX__IR, or_9_out);
  and and_10 (and_10_out, EX__IR, or_10_out);
  and and_11 (and_11_out, AX__BX, or_11_out);
  and and_12 (and_12_out, AX__CX, or_12_out);
  and and_13 (and_13_out, AX__DX, or_13_out);
  and and_14 (and_14_out, AX__EX, or_14_out);
  and and_15 (and_15_out, BX__CX, or_15_out);
  and and_16 (and_16_out, BX__DX, or_16_out);
  and and_17 (and_17_out, BX__EX, or_17_out);
  and and_18 (and_18_out, CX__DX, or_18_out);
  and and_19 (and_19_out, CX__EX, or_19_out);
  and and_20 (and_20_out, DX__EX, or_20_out);
  or or_21 (OUTPUT, and_1_out, and_2_out, and_3_out, and_4_out, and_5_out, and_6_out, and_7_out, and_8_out, and_9_out, and_10_out, and_11_out, and_12_out, and_13_out, and_14_out, and_15_out, and_16_out, and_17_out, and_18_out, and_19_out, and_20_out);
endmodule

module XOR_1 (
  input  AX,
  input  BX,
  input  CX,
  input  DX,
  input  EX,
  input  DR,
  input  IR,
  input  AX__DR,
  input  BX__DR,
  input  CX__DR,
  input  DX__DR,
  input  EX__DR,
  input  AX__IR,
  input  BX__IR,
  input  CX__IR,
  input  DX__IR,
  input  EX__IR,
  input  AX__BX,
  input  AX__CX,
  input  AX__DX,
  input  AX__EX,
  input  BX__CX,
  input  BX__DX,
  input  BX__EX,
  input  CX__DX,
  input  CX__EX,
  input  DX__EX,
  output OUTPUT
);

  wire and_1_out, and_2_out, and_3_out, and_4_out, and_5_out, and_6_out, and_7_out, and_8_out, and_9_out,
       and_10_out, and_11_out, and_12_out, and_13_out, and_14_out, and_15_out, and_16_out, and_17_out,
       and_18_out, and_19_out, and_20_out, xor_1_out, xor_2_out, xor_3_out, xor_4_out, xor_5_out, xor_6_out,
       xor_7_out, xor_8_out, xor_9_out, xor_10_out, xor_11_out, xor_12_out, xor_13_out, xor_14_out,
       xor_15_out, xor_16_out, xor_17_out, xor_18_out, xor_19_out, xor_20_out;

  xor xor_1 (xor_1_out, DR, AX);
  xor xor_2 (xor_2_out, DR, BX);
  xor xor_3 (xor_3_out, DR, CX);
  xor xor_4 (xor_4_out, DR, DX);
  xor xor_5 (xor_5_out, DR, EX);
  xor xor_6 (xor_6_out, IR, AX);
  xor xor_7 (xor_7_out, IR, BX);
  xor xor_8 (xor_8_out, IR, CX);
  xor xor_9 (xor_9_out, IR, DX);
  xor xor_10 (xor_10_out, IR, EX);
  xor xor_11 (xor_11_out, BX, AX);
  xor xor_12 (xor_12_out, CX, AX);
  xor xor_13 (xor_13_out, DX, AX);
  xor xor_14 (xor_14_out, EX, AX);
  xor xor_15 (xor_15_out, CX, BX);
  xor xor_16 (xor_16_out, DX, BX);
  xor xor_17 (xor_17_out, EX, BX);
  xor xor_18 (xor_18_out, DX, CX);
  xor xor_19 (xor_19_out, EX, CX);
  xor xor_20 (xor_20_out, EX, CX);
  and and_1 (and_1_out, AX__DR, xor_1_out);
  and and_2 (and_2_out, BX__DR, xor_2_out);
  and and_3 (and_3_out, CX__DR, xor_3_out);
  and and_4 (and_4_out, DX__DR, xor_4_out);
  and and_5 (and_5_out, EX__DR, xor_5_out);
  and and_6 (and_6_out, AX__IR, xor_6_out);
  and and_7 (and_7_out, BX__IR, xor_7_out);
  and and_8 (and_8_out, CX__IR, xor_8_out);
  and and_9 (and_9_out, DX__IR, xor_9_out);
  and and_10 (and_10_out, EX__IR, xor_10_out);
  and and_11 (and_11_out, AX__BX, xor_11_out);
  and and_12 (and_12_out, AX__CX, xor_12_out);
  and and_13 (and_13_out, AX__DX, xor_13_out);
  and and_14 (and_14_out, AX__EX, xor_14_out);
  and and_15 (and_15_out, BX__CX, xor_15_out);
  and and_16 (and_16_out, BX__DX, xor_16_out);
  and and_17 (and_17_out, BX__EX, xor_17_out);
  and and_18 (and_18_out, CX__DX, xor_18_out);
  and and_19 (and_19_out, CX__EX, xor_19_out);
  and and_20 (and_20_out, DX__EX, xor_20_out);
  or or_1 (OUTPUT, and_1_out, and_2_out, and_3_out, and_4_out, and_5_out, and_6_out, and_7_out, and_8_out, and_9_out, and_10_out, and_11_out, and_12_out, and_13_out, and_14_out, and_15_out, and_16_out, and_17_out, and_18_out, and_19_out, and_20_out);
endmodule

// INPUT ADJUSTER
module LOGIC_INPUT_4to1 (
  input  [3:0] AX,
  input  [3:0] BX,
  input  [3:0] CX,
  input  [3:0] DX,
  input  [3:0] EX,
  input  [3:0] DR,
  input  [3:0] IR,
  output AX3,
  output BX3,
  output CX3,
  output DX3,
  output EX3,
  output DR3,
  output IR3,
  output AX2,
  output BX2,
  output CX2,
  output DX2,
  output EX2,
  output DR2,
  output IR2,
  output AX1,
  output BX1,
  output CX1,
  output DX1,
  output EX1,
  output DR1,
  output IR1,
  output AX0,
  output BX0,
  output CX0,
  output DX0,
  output EX0,
  output DR0,
  output IR0
);


  assign AX0 = AX[0];
  assign AX1 = AX[1];
  assign AX2 = AX[2];
  assign AX3 = AX[3];
  assign BX0 = BX[0];
  assign BX1 = BX[1];
  assign BX2 = BX[2];
  assign BX3 = BX[3];
  assign CX0 = CX[0];
  assign CX1 = CX[1];
  assign CX2 = CX[2];
  assign CX3 = CX[3];
  assign DR0 = DR[0];
  assign DR1 = DR[1];
  assign DR2 = DR[2];
  assign DR3 = DR[3];
  assign DX0 = DX[0];
  assign DX1 = DX[1];
  assign DX2 = DX[2];
  assign DX3 = DX[3];
  assign EX0 = EX[0];
  assign EX1 = EX[1];
  assign EX2 = EX[2];
  assign EX3 = EX[3];
  assign IR0 = IR[0];
  assign IR1 = IR[1];
  assign IR2 = IR[2];
  assign IR3 = IR[3];
endmodule

module AND_4 (
  input  AX__DR,
  input  BX__DR,
  input  CX__DR,
  input  DX__DR,
  input  EX__DR,
  input  AX__IR,
  input  BX__IR,
  input  CX__IR,
  input  DX__IR,
  input  EX__IR,
  input  AX__BX,
  input  AX__CX,
  input  AX__DX,
  input  AX__EX,
  input  BX__CX,
  input  BX__DX,
  input  BX__EX,
  input  CX__DX,
  input  CX__EX,
  input  DX__EX,
  input  [3:0] AX,
  input  [3:0] BX,
  input  [3:0] CX,
  input  [3:0] DX,
  input  [3:0] EX,
  input  [3:0] DR,
  input  [3:0] IR,
  output [3:0] OUTPUT
);

  wire [6:0] logic_input_4to1_1_ir0, logic_input_4to1_1_ir1, logic_input_4to1_1_ir2, logic_input_4to1_1_ir3;

  LOGIC_INPUT_4to1 logic_input_4to1_1 (
    .AX(AX), .BX(BX), .CX(CX), .DX(DX), .EX(EX), .DR(DR), .IR(IR), .AX3(logic_input_4to1_1_ir3[6]),
    .BX3(logic_input_4to1_1_ir3[5]), .CX3(logic_input_4to1_1_ir3[4]), .DX3(logic_input_4to1_1_ir3[3]),
    .EX3(logic_input_4to1_1_ir3[2]), .DR3(logic_input_4to1_1_ir3[1]), .IR3(logic_input_4to1_1_ir3[0]),
    .AX2(logic_input_4to1_1_ir2[6]), .BX2(logic_input_4to1_1_ir2[5]), .CX2(logic_input_4to1_1_ir2[4]),
    .DX2(logic_input_4to1_1_ir2[3]), .EX2(logic_input_4to1_1_ir2[2]), .DR2(logic_input_4to1_1_ir2[1]),
    .IR2(logic_input_4to1_1_ir2[0]), .AX1(logic_input_4to1_1_ir1[6]), .BX1(logic_input_4to1_1_ir1[5]),
    .CX1(logic_input_4to1_1_ir1[4]), .DX1(logic_input_4to1_1_ir1[3]), .EX1(logic_input_4to1_1_ir1[2]),
    .DR1(logic_input_4to1_1_ir1[1]), .IR1(logic_input_4to1_1_ir1[0]), .AX0(logic_input_4to1_1_ir0[6]),
    .BX0(logic_input_4to1_1_ir0[5]), .CX0(logic_input_4to1_1_ir0[4]), .DX0(logic_input_4to1_1_ir0[3]),
    .EX0(logic_input_4to1_1_ir0[2]), .DR0(logic_input_4to1_1_ir0[1]), .IR0(logic_input_4to1_1_ir0[0]));
  AND_1 and_1_1 (
    .AX__DR(AX__DR), .BX__DR(BX__DR), .CX__DR(CX__DR), .DX__DR(DX__DR), .EX__DR(EX__DR), .AX__IR(AX__IR),
    .BX__IR(BX__IR), .CX__IR(CX__IR), .DX__IR(DX__IR), .EX__IR(EX__IR), .AX__BX(AX__BX), .AX__CX(AX__CX),
    .AX__DX(AX__DX), .AX__EX(AX__EX), .BX__CX(BX__CX), .BX__DX(BX__DX), .BX__EX(BX__EX), .CX__DX(CX__DX),
    .CX__EX(CX__EX), .DX__EX(DX__EX), .AX(logic_input_4to1_1_ir3[6]), .BX(logic_input_4to1_1_ir3[5]),
    .CX(logic_input_4to1_1_ir3[4]), .DX(logic_input_4to1_1_ir3[3]), .EX(logic_input_4to1_1_ir3[2]),
    .DR(logic_input_4to1_1_ir3[1]), .IR(logic_input_4to1_1_ir3[0]), .OUTPUT(OUTPUT[3]));
  AND_1 and_1_2 (
    .AX__DR(AX__DR), .BX__DR(BX__DR), .CX__DR(CX__DR), .DX__DR(DX__DR), .EX__DR(EX__DR), .AX__IR(AX__IR),
    .BX__IR(BX__IR), .CX__IR(CX__IR), .DX__IR(DX__IR), .EX__IR(EX__IR), .AX__BX(AX__BX), .AX__CX(AX__CX),
    .AX__DX(AX__DX), .AX__EX(AX__EX), .BX__CX(BX__CX), .BX__DX(BX__DX), .BX__EX(BX__EX), .CX__DX(CX__DX),
    .CX__EX(CX__EX), .DX__EX(DX__EX), .AX(logic_input_4to1_1_ir2[6]), .BX(logic_input_4to1_1_ir2[5]),
    .CX(logic_input_4to1_1_ir2[4]), .DX(logic_input_4to1_1_ir2[3]), .EX(logic_input_4to1_1_ir2[2]),
    .DR(logic_input_4to1_1_ir2[1]), .IR(logic_input_4to1_1_ir2[0]), .OUTPUT(OUTPUT[2]));
  AND_1 and_1_3 (
    .AX__DR(AX__DR), .BX__DR(BX__DR), .CX__DR(CX__DR), .DX__DR(DX__DR), .EX__DR(EX__DR), .AX__IR(AX__IR),
    .BX__IR(BX__IR), .CX__IR(CX__IR), .DX__IR(DX__IR), .EX__IR(EX__IR), .AX__BX(AX__BX), .AX__CX(AX__CX),
    .AX__DX(AX__DX), .AX__EX(AX__EX), .BX__CX(BX__CX), .BX__DX(BX__DX), .BX__EX(BX__EX), .CX__DX(CX__DX),
    .CX__EX(CX__EX), .DX__EX(DX__EX), .AX(logic_input_4to1_1_ir1[6]), .BX(logic_input_4to1_1_ir1[5]),
    .CX(logic_input_4to1_1_ir1[4]), .DX(logic_input_4to1_1_ir1[3]), .EX(logic_input_4to1_1_ir1[2]),
    .DR(logic_input_4to1_1_ir1[1]), .IR(logic_input_4to1_1_ir1[0]), .OUTPUT(OUTPUT[1]));
  AND_1 and_1_4 (
    .AX__DR(AX__DR), .BX__DR(BX__DR), .CX__DR(CX__DR), .DX__DR(DX__DR), .EX__DR(EX__DR), .AX__IR(AX__IR),
    .BX__IR(BX__IR), .CX__IR(CX__IR), .DX__IR(DX__IR), .EX__IR(EX__IR), .AX__BX(AX__BX), .AX__CX(AX__CX),
    .AX__DX(AX__DX), .AX__EX(AX__EX), .BX__CX(BX__CX), .BX__DX(BX__DX), .BX__EX(BX__EX), .CX__DX(CX__DX),
    .CX__EX(CX__EX), .DX__EX(DX__EX), .AX(logic_input_4to1_1_ir0[6]), .BX(logic_input_4to1_1_ir0[5]),
    .CX(logic_input_4to1_1_ir0[4]), .DX(logic_input_4to1_1_ir0[3]), .EX(logic_input_4to1_1_ir0[2]),
    .DR(logic_input_4to1_1_ir0[1]), .IR(logic_input_4to1_1_ir0[0]), .OUTPUT(OUTPUT[0]));
endmodule

module OR_4 (
  input  AX__DR,
  input  BX__DR,
  input  CX__DR,
  input  DX__DR,
  input  EX__DR,
  input  AX__IR,
  input  BX__IR,
  input  CX__IR,
  input  DX__IR,
  input  EX__IR,
  input  AX__BX,
  input  AX__CX,
  input  AX__DX,
  input  AX__EX,
  input  BX__CX,
  input  BX__DX,
  input  BX__EX,
  input  CX__DX,
  input  CX__EX,
  input  DX__EX,
  input  [3:0] AX,
  input  [3:0] BX,
  input  [3:0] CX,
  input  [3:0] DX,
  input  [3:0] EX,
  input  [3:0] DR,
  input  [3:0] IR,
  output [3:0] OUTPUT
);

  wire [6:0] logic_input_4to1_1_ir0, logic_input_4to1_1_ir1, logic_input_4to1_1_ir2, logic_input_4to1_1_ir3;

  LOGIC_INPUT_4to1 logic_input_4to1_1 (
    .AX(AX), .BX(BX), .CX(CX), .DX(DX), .EX(EX), .DR(DR), .IR(IR), .AX3(logic_input_4to1_1_ir3[6]),
    .BX3(logic_input_4to1_1_ir3[5]), .CX3(logic_input_4to1_1_ir3[4]), .DX3(logic_input_4to1_1_ir3[3]),
    .EX3(logic_input_4to1_1_ir3[2]), .DR3(logic_input_4to1_1_ir3[1]), .IR3(logic_input_4to1_1_ir3[0]),
    .AX2(logic_input_4to1_1_ir2[6]), .BX2(logic_input_4to1_1_ir2[5]), .CX2(logic_input_4to1_1_ir2[4]),
    .DX2(logic_input_4to1_1_ir2[3]), .EX2(logic_input_4to1_1_ir2[2]), .DR2(logic_input_4to1_1_ir2[1]),
    .IR2(logic_input_4to1_1_ir2[0]), .AX1(logic_input_4to1_1_ir1[6]), .BX1(logic_input_4to1_1_ir1[5]),
    .CX1(logic_input_4to1_1_ir1[4]), .DX1(logic_input_4to1_1_ir1[3]), .EX1(logic_input_4to1_1_ir1[2]),
    .DR1(logic_input_4to1_1_ir1[1]), .IR1(logic_input_4to1_1_ir1[0]), .AX0(logic_input_4to1_1_ir0[6]),
    .BX0(logic_input_4to1_1_ir0[5]), .CX0(logic_input_4to1_1_ir0[4]), .DX0(logic_input_4to1_1_ir0[3]),
    .EX0(logic_input_4to1_1_ir0[2]), .DR0(logic_input_4to1_1_ir0[1]), .IR0(logic_input_4to1_1_ir0[0]));
  OR_1 or_1_1 (
    .AX__DR(AX__DR), .BX__DR(BX__DR), .CX__DR(CX__DR), .DX__DR(DX__DR), .EX__DR(EX__DR), .AX__IR(AX__IR),
    .BX__IR(BX__IR), .CX__IR(CX__IR), .DX__IR(DX__IR), .EX__IR(EX__IR), .AX__BX(AX__BX), .AX__CX(AX__CX),
    .AX__DX(AX__DX), .AX__EX(AX__EX), .BX__CX(BX__CX), .BX__DX(BX__DX), .BX__EX(BX__EX), .CX__DX(CX__DX),
    .CX__EX(CX__EX), .DX__EX(DX__EX), .AX(logic_input_4to1_1_ir3[6]), .BX(logic_input_4to1_1_ir3[5]),
    .CX(logic_input_4to1_1_ir3[4]), .DX(logic_input_4to1_1_ir3[3]), .EX(logic_input_4to1_1_ir3[2]),
    .DR(logic_input_4to1_1_ir3[1]), .IR(logic_input_4to1_1_ir3[0]), .OUTPUT(OUTPUT[3]));
  OR_1 or_1_2 (
    .AX__DR(AX__DR), .BX__DR(BX__DR), .CX__DR(CX__DR), .DX__DR(DX__DR), .EX__DR(EX__DR), .AX__IR(AX__IR),
    .BX__IR(BX__IR), .CX__IR(CX__IR), .DX__IR(DX__IR), .EX__IR(EX__IR), .AX__BX(AX__BX), .AX__CX(AX__CX),
    .AX__DX(AX__DX), .AX__EX(AX__EX), .BX__CX(BX__CX), .BX__DX(BX__DX), .BX__EX(BX__EX), .CX__DX(CX__DX),
    .CX__EX(CX__EX), .DX__EX(DX__EX), .AX(logic_input_4to1_1_ir2[6]), .BX(logic_input_4to1_1_ir2[5]),
    .CX(logic_input_4to1_1_ir2[4]), .DX(logic_input_4to1_1_ir2[3]), .EX(logic_input_4to1_1_ir2[2]),
    .DR(logic_input_4to1_1_ir2[1]), .IR(logic_input_4to1_1_ir2[0]), .OUTPUT(OUTPUT[2]));
  OR_1 or_1_3 (
    .AX__DR(AX__DR), .BX__DR(BX__DR), .CX__DR(CX__DR), .DX__DR(DX__DR), .EX__DR(EX__DR), .AX__IR(AX__IR),
    .BX__IR(BX__IR), .CX__IR(CX__IR), .DX__IR(DX__IR), .EX__IR(EX__IR), .AX__BX(AX__BX), .AX__CX(AX__CX),
    .AX__DX(AX__DX), .AX__EX(AX__EX), .BX__CX(BX__CX), .BX__DX(BX__DX), .BX__EX(BX__EX), .CX__DX(CX__DX),
    .CX__EX(CX__EX), .DX__EX(DX__EX), .AX(logic_input_4to1_1_ir1[6]), .BX(logic_input_4to1_1_ir1[5]),
    .CX(logic_input_4to1_1_ir1[4]), .DX(logic_input_4to1_1_ir1[3]), .EX(logic_input_4to1_1_ir1[2]),
    .DR(logic_input_4to1_1_ir1[1]), .IR(logic_input_4to1_1_ir1[0]), .OUTPUT(OUTPUT[1]));
  OR_1 or_1_4 (
    .AX__DR(AX__DR), .BX__DR(BX__DR), .CX__DR(CX__DR), .DX__DR(DX__DR), .EX__DR(EX__DR), .AX__IR(AX__IR),
    .BX__IR(BX__IR), .CX__IR(CX__IR), .DX__IR(DX__IR), .EX__IR(EX__IR), .AX__BX(AX__BX), .AX__CX(AX__CX),
    .AX__DX(AX__DX), .AX__EX(AX__EX), .BX__CX(BX__CX), .BX__DX(BX__DX), .BX__EX(BX__EX), .CX__DX(CX__DX),
    .CX__EX(CX__EX), .DX__EX(DX__EX), .AX(logic_input_4to1_1_ir0[6]), .BX(logic_input_4to1_1_ir0[5]),
    .CX(logic_input_4to1_1_ir0[4]), .DX(logic_input_4to1_1_ir0[3]), .EX(logic_input_4to1_1_ir0[2]),
    .DR(logic_input_4to1_1_ir0[1]), .IR(logic_input_4to1_1_ir0[0]), .OUTPUT(OUTPUT[0]));
endmodule

module XOR_4 (
  input  AX__DR,
  input  BX__DR,
  input  CX__DR,
  input  DX__DR,
  input  EX__DR,
  input  AX__IR,
  input  BX__IR,
  input  CX__IR,
  input  DX__IR,
  input  EX__IR,
  input  AX__BX,
  input  AX__CX,
  input  AX__DX,
  input  AX__EX,
  input  BX__CX,
  input  BX__DX,
  input  BX__EX,
  input  CX__DX,
  input  CX__EX,
  input  DX__EX,
  input  [3:0] AX,
  input  [3:0] BX,
  input  [3:0] CX,
  input  [3:0] DX,
  input  [3:0] EX,
  input  [3:0] DR,
  input  [3:0] IR,
  output [3:0] OUTPUT
);

  wire [6:0] logic_input_4to1_1_ir0, logic_input_4to1_1_ir1, logic_input_4to1_1_ir2, logic_input_4to1_1_ir3;

  LOGIC_INPUT_4to1 logic_input_4to1_1 (
    .AX(AX), .BX(BX), .CX(CX), .DX(DX), .EX(EX), .DR(DR), .IR(IR), .AX3(logic_input_4to1_1_ir3[6]),
    .BX3(logic_input_4to1_1_ir3[5]), .CX3(logic_input_4to1_1_ir3[4]), .DX3(logic_input_4to1_1_ir3[3]),
    .EX3(logic_input_4to1_1_ir3[2]), .DR3(logic_input_4to1_1_ir3[1]), .IR3(logic_input_4to1_1_ir3[0]),
    .AX2(logic_input_4to1_1_ir2[6]), .BX2(logic_input_4to1_1_ir2[5]), .CX2(logic_input_4to1_1_ir2[4]),
    .DX2(logic_input_4to1_1_ir2[3]), .EX2(logic_input_4to1_1_ir2[2]), .DR2(logic_input_4to1_1_ir2[1]),
    .IR2(logic_input_4to1_1_ir2[0]), .AX1(logic_input_4to1_1_ir1[6]), .BX1(logic_input_4to1_1_ir1[5]),
    .CX1(logic_input_4to1_1_ir1[4]), .DX1(logic_input_4to1_1_ir1[3]), .EX1(logic_input_4to1_1_ir1[2]),
    .DR1(logic_input_4to1_1_ir1[1]), .IR1(logic_input_4to1_1_ir1[0]), .AX0(logic_input_4to1_1_ir0[6]),
    .BX0(logic_input_4to1_1_ir0[5]), .CX0(logic_input_4to1_1_ir0[4]), .DX0(logic_input_4to1_1_ir0[3]),
    .EX0(logic_input_4to1_1_ir0[2]), .DR0(logic_input_4to1_1_ir0[1]), .IR0(logic_input_4to1_1_ir0[0]));
  XOR_1 xor_1_1 (
    .AX__DR(AX__DR), .BX__DR(BX__DR), .CX__DR(CX__DR), .DX__DR(DX__DR), .EX__DR(EX__DR), .AX__IR(AX__IR),
    .BX__IR(BX__IR), .CX__IR(CX__IR), .DX__IR(DX__IR), .EX__IR(EX__IR), .AX__BX(AX__BX), .AX__CX(AX__CX),
    .AX__DX(AX__DX), .AX__EX(AX__EX), .BX__CX(BX__CX), .BX__DX(BX__DX), .BX__EX(BX__EX), .CX__DX(CX__DX),
    .CX__EX(CX__EX), .DX__EX(DX__EX), .AX(logic_input_4to1_1_ir3[6]), .BX(logic_input_4to1_1_ir3[5]),
    .CX(logic_input_4to1_1_ir3[4]), .DX(logic_input_4to1_1_ir3[3]), .EX(logic_input_4to1_1_ir3[2]),
    .DR(logic_input_4to1_1_ir3[1]), .IR(logic_input_4to1_1_ir3[0]), .OUTPUT(OUTPUT[3]));
  XOR_1 xor_1_2 (
    .AX__DR(AX__DR), .BX__DR(BX__DR), .CX__DR(CX__DR), .DX__DR(DX__DR), .EX__DR(EX__DR), .AX__IR(AX__IR),
    .BX__IR(BX__IR), .CX__IR(CX__IR), .DX__IR(DX__IR), .EX__IR(EX__IR), .AX__BX(AX__BX), .AX__CX(AX__CX),
    .AX__DX(AX__DX), .AX__EX(AX__EX), .BX__CX(BX__CX), .BX__DX(BX__DX), .BX__EX(BX__EX), .CX__DX(CX__DX),
    .CX__EX(CX__EX), .DX__EX(DX__EX), .AX(logic_input_4to1_1_ir2[6]), .BX(logic_input_4to1_1_ir2[5]),
    .CX(logic_input_4to1_1_ir2[4]), .DX(logic_input_4to1_1_ir2[3]), .EX(logic_input_4to1_1_ir2[2]),
    .DR(logic_input_4to1_1_ir2[1]), .IR(logic_input_4to1_1_ir2[0]), .OUTPUT(OUTPUT[2]));
  XOR_1 xor_1_3 (
    .AX__DR(AX__DR), .BX__DR(BX__DR), .CX__DR(CX__DR), .DX__DR(DX__DR), .EX__DR(EX__DR), .AX__IR(AX__IR),
    .BX__IR(BX__IR), .CX__IR(CX__IR), .DX__IR(DX__IR), .EX__IR(EX__IR), .AX__BX(AX__BX), .AX__CX(AX__CX),
    .AX__DX(AX__DX), .AX__EX(AX__EX), .BX__CX(BX__CX), .BX__DX(BX__DX), .BX__EX(BX__EX), .CX__DX(CX__DX),
    .CX__EX(CX__EX), .DX__EX(DX__EX), .AX(logic_input_4to1_1_ir1[6]), .BX(logic_input_4to1_1_ir1[5]),
    .CX(logic_input_4to1_1_ir1[4]), .DX(logic_input_4to1_1_ir1[3]), .EX(logic_input_4to1_1_ir1[2]),
    .DR(logic_input_4to1_1_ir1[1]), .IR(logic_input_4to1_1_ir1[0]), .OUTPUT(OUTPUT[1]));
  XOR_1 xor_1_4 (
    .AX__DR(AX__DR), .BX__DR(BX__DR), .CX__DR(CX__DR), .DX__DR(DX__DR), .EX__DR(EX__DR), .AX__IR(AX__IR),
    .BX__IR(BX__IR), .CX__IR(CX__IR), .DX__IR(DX__IR), .EX__IR(EX__IR), .AX__BX(AX__BX), .AX__CX(AX__CX),
    .AX__DX(AX__DX), .AX__EX(AX__EX), .BX__CX(BX__CX), .BX__DX(BX__DX), .BX__EX(BX__EX), .CX__DX(CX__DX),
    .CX__EX(CX__EX), .DX__EX(DX__EX), .AX(logic_input_4to1_1_ir0[6]), .BX(logic_input_4to1_1_ir0[5]),
    .CX(logic_input_4to1_1_ir0[4]), .DX(logic_input_4to1_1_ir0[3]), .EX(logic_input_4to1_1_ir0[2]),
    .DR(logic_input_4to1_1_ir0[1]), .IR(logic_input_4to1_1_ir0[0]), .OUTPUT(OUTPUT[0]));
endmodule

// INPUT ADJUSTER
module LOGIC_INPUT_16to4 (
  input  [15:0] AX,
  input  [15:0] BX,
  input  [15:0] CX,
  input  [15:0] DX,
  input  [15:0] EX,
  input  [15:0] DR,
  input  [15:0] IR,
  output [3:0] AX_0_3,
  output [3:0] BX_0_3,
  output [3:0] CX_0_3,
  output [3:0] DX_0_3,
  output [3:0] EX_0_3,
  output [3:0] DR_0_3,
  output [3:0] IR_0_3,
  output [3:0] AX_4_7,
  output [3:0] BX_4_7,
  output [3:0] CX_4_7,
  output [3:0] DX_4_7,
  output [3:0] EX_4_7,
  output [3:0] DR_4_7,
  output [3:0] IR_4_7,
  output [3:0] AX_8_11,
  output [3:0] BX_8_11,
  output [3:0] CX_8_11,
  output [3:0] DX_8_11,
  output [3:0] EX_8_11,
  output [3:0] DR_8_11,
  output [3:0] IR_0_3_2,
  output [3:0] AX_12_15,
  output [3:0] BX_12_15,
  output [3:0] CX_12_15,
  output [3:0] DX_12_15,
  output [3:0] EX_12_15,
  output [3:0] DR_12_15,
  output [3:0] IR_12_15
);


  assign AX_0_3 = AX[3:0];
  assign AX_4_7 = AX[7:4];
  assign AX_8_11 = AX[11:8];
  assign AX_12_15 = AX[15:12];
  assign BX_0_3 = BX[3:0];
  assign BX_4_7 = BX[7:4];
  assign BX_8_11 = BX[11:8];
  assign BX_12_15 = BX[15:12];
  assign CX_0_3 = CX[3:0];
  assign CX_4_7 = CX[7:4];
  assign CX_8_11 = CX[11:8];
  assign CX_12_15 = CX[15:12];
  assign DR_0_3 = DR[3:0];
  assign DR_4_7 = DR[7:4];
  assign DR_8_11 = DR[11:8];
  assign DR_12_15 = DR[15:12];
  assign DX_0_3 = DX[3:0];
  assign DX_4_7 = DX[7:4];
  assign DX_8_11 = DX[11:8];
  assign DX_12_15 = DX[15:12];
  assign EX_0_3 = EX[3:0];
  assign EX_4_7 = EX[7:4];
  assign EX_8_11 = EX[11:8];
  assign EX_12_15 = EX[15:12];
  assign IR_0_3 = IR[3:0];
  assign IR_0_3_2 = IR[11:8];
  assign IR_4_7 = IR[7:4];
  assign IR_12_15 = IR[15:12];
endmodule

module AND (
  input  AX__DR,
  input  BX__DR,
  input  CX__DR,
  input  DX__DR,
  input  EX__DR,
  input  AX__IR,
  input  BX__IR,
  input  CX__IR,
  input  DX__IR,
  input  EX__IR,
  input  AX__BX,
  input  AX__CX,
  input  AX__DX,
  input  AX__EX,
  input  BX__CX,
  input  BX__DX,
  input  BX__EX,
  input  CX__DX,
  input  CX__EX,
  input  DX__EX,
  input  [15:0] AX,
  input  [15:0] BX,
  input  [15:0] CX,
  input  [15:0] DX,
  input  [15:0] EX,
  input  [15:0] DR,
  input  [15:0] IR,
  output [15:0] OUTPUT
);

  wire [3:0] logic_input_16to4_1_ax_0_3, logic_input_16to4_1_ax_4_7, logic_input_16to4_1_ax_8_11,
       logic_input_16to4_1_ax_12_15, logic_input_16to4_1_bx_0_3, logic_input_16to4_1_bx_4_7,
       logic_input_16to4_1_bx_8_11, logic_input_16to4_1_bx_12_15, logic_input_16to4_1_cx_0_3,
       logic_input_16to4_1_cx_4_7, logic_input_16to4_1_cx_8_11, logic_input_16to4_1_cx_12_15,
       logic_input_16to4_1_dr_0_3, logic_input_16to4_1_dr_4_7, logic_input_16to4_1_dr_8_11,
       logic_input_16to4_1_dr_12_15, logic_input_16to4_1_dx_0_3, logic_input_16to4_1_dx_4_7,
       logic_input_16to4_1_dx_8_11, logic_input_16to4_1_dx_12_15, logic_input_16to4_1_ex_0_3,
       logic_input_16to4_1_ex_4_7, logic_input_16to4_1_ex_8_11, logic_input_16to4_1_ex_12_15,
       logic_input_16to4_1_ir_0_3, logic_input_16to4_1_ir_0_3_2, logic_input_16to4_1_ir_4_7,
       logic_input_16to4_1_ir_12_15;

  LOGIC_INPUT_16to4 logic_input_16to4_1 (
    .AX(AX), .BX(BX), .CX(CX), .DX(DX), .EX(EX), .DR(DR), .IR(IR), .AX_0_3(logic_input_16to4_1_ax_0_3),
    .BX_0_3(logic_input_16to4_1_bx_0_3), .CX_0_3(logic_input_16to4_1_cx_0_3),
    .DX_0_3(logic_input_16to4_1_dx_0_3), .EX_0_3(logic_input_16to4_1_ex_0_3),
    .DR_0_3(logic_input_16to4_1_dr_0_3), .IR_0_3(logic_input_16to4_1_ir_0_3),
    .AX_4_7(logic_input_16to4_1_ax_4_7), .BX_4_7(logic_input_16to4_1_bx_4_7),
    .CX_4_7(logic_input_16to4_1_cx_4_7), .DX_4_7(logic_input_16to4_1_dx_4_7),
    .EX_4_7(logic_input_16to4_1_ex_4_7), .DR_4_7(logic_input_16to4_1_dr_4_7),
    .IR_4_7(logic_input_16to4_1_ir_4_7), .AX_8_11(logic_input_16to4_1_ax_8_11),
    .BX_8_11(logic_input_16to4_1_bx_8_11), .CX_8_11(logic_input_16to4_1_cx_8_11),
    .DX_8_11(logic_input_16to4_1_dx_8_11), .EX_8_11(logic_input_16to4_1_ex_8_11),
    .DR_8_11(logic_input_16to4_1_dr_8_11), .IR_0_3_2(logic_input_16to4_1_ir_0_3_2),
    .AX_12_15(logic_input_16to4_1_ax_12_15), .BX_12_15(logic_input_16to4_1_bx_12_15),
    .CX_12_15(logic_input_16to4_1_cx_12_15), .DX_12_15(logic_input_16to4_1_dx_12_15),
    .EX_12_15(logic_input_16to4_1_ex_12_15), .DR_12_15(logic_input_16to4_1_dr_12_15),
    .IR_12_15(logic_input_16to4_1_ir_12_15));
  AND_4 and_4_1 (
    .AX(logic_input_16to4_1_ax_0_3), .BX(logic_input_16to4_1_bx_0_3), .CX(logic_input_16to4_1_cx_0_3),
    .DX(logic_input_16to4_1_dx_0_3), .EX(logic_input_16to4_1_ex_0_3), .DR(logic_input_16to4_1_dr_0_3),
    .IR(logic_input_16to4_1_ir_0_3), .AX__DR(AX__DR), .BX__DR(BX__DR), .CX__DR(CX__DR), .DX__DR(DX__DR),
    .EX__DR(EX__DR), .AX__IR(AX__IR), .BX__IR(BX__IR), .CX__IR(CX__IR), .DX__IR(DX__IR), .EX__IR(EX__IR),
    .AX__BX(AX__BX), .AX__CX(AX__CX), .AX__DX(AX__DX), .AX__EX(AX__EX), .BX__CX(BX__CX), .BX__DX(BX__DX),
    .BX__EX(BX__EX), .CX__DX(CX__DX), .CX__EX(CX__EX), .DX__EX(DX__EX), .OUTPUT(OUTPUT[3:0]));
  AND_4 and_4_2 (
    .AX(logic_input_16to4_1_ax_4_7), .BX(logic_input_16to4_1_bx_4_7), .CX(logic_input_16to4_1_cx_4_7),
    .DX(logic_input_16to4_1_dx_4_7), .EX(logic_input_16to4_1_ex_4_7), .DR(logic_input_16to4_1_dr_4_7),
    .IR(logic_input_16to4_1_ir_4_7), .AX__DR(AX__DR), .BX__DR(BX__DR), .CX__DR(CX__DR), .DX__DR(DX__DR),
    .EX__DR(EX__DR), .AX__IR(AX__IR), .BX__IR(BX__IR), .CX__IR(CX__IR), .DX__IR(DX__IR), .EX__IR(EX__IR),
    .AX__BX(AX__BX), .AX__CX(AX__CX), .AX__DX(AX__DX), .AX__EX(AX__EX), .BX__CX(BX__CX), .BX__DX(BX__DX),
    .BX__EX(BX__EX), .CX__DX(CX__DX), .CX__EX(CX__EX), .DX__EX(DX__EX), .OUTPUT(OUTPUT[7:4]));
  AND_4 and_4_3 (
    .AX(logic_input_16to4_1_ax_8_11), .BX(logic_input_16to4_1_bx_8_11), .CX(logic_input_16to4_1_cx_8_11),
    .DX(logic_input_16to4_1_dx_8_11), .EX(logic_input_16to4_1_ex_8_11), .DR(logic_input_16to4_1_dr_8_11),
    .IR(logic_input_16to4_1_ir_0_3_2), .AX__DR(AX__DR), .BX__DR(BX__DR), .CX__DR(CX__DR), .DX__DR(DX__DR),
    .EX__DR(EX__DR), .AX__IR(AX__IR), .BX__IR(BX__IR), .CX__IR(CX__IR), .DX__IR(DX__IR), .EX__IR(EX__IR),
    .AX__BX(AX__BX), .AX__CX(AX__CX), .AX__DX(AX__DX), .AX__EX(AX__EX), .BX__CX(BX__CX), .BX__DX(BX__DX),
    .BX__EX(BX__EX), .CX__DX(CX__DX), .CX__EX(CX__EX), .DX__EX(DX__EX), .OUTPUT(OUTPUT[11:8]));
  AND_4 and_4_4 (
    .AX(logic_input_16to4_1_ax_12_15), .BX(logic_input_16to4_1_bx_12_15), .CX(logic_input_16to4_1_cx_12_15),
    .DX(logic_input_16to4_1_dx_12_15), .EX(logic_input_16to4_1_ex_12_15), .DR(logic_input_16to4_1_dr_12_15),
    .IR(logic_input_16to4_1_ir_12_15), .AX__DR(AX__DR), .BX__DR(BX__DR), .CX__DR(CX__DR), .DX__DR(DX__DR),
    .EX__DR(EX__DR), .AX__IR(AX__IR), .BX__IR(BX__IR), .CX__IR(CX__IR), .DX__IR(DX__IR), .EX__IR(EX__IR),
    .AX__BX(AX__BX), .AX__CX(AX__CX), .AX__DX(AX__DX), .AX__EX(AX__EX), .BX__CX(BX__CX), .BX__DX(BX__DX),
    .BX__EX(BX__EX), .CX__DX(CX__DX), .CX__EX(CX__EX), .DX__EX(DX__EX), .OUTPUT(OUTPUT[15:12]));
endmodule

module OR (
  input  AX__DR,
  input  BX__DR,
  input  CX__DR,
  input  DX__DR,
  input  EX__DR,
  input  AX__IR,
  input  BX__IR,
  input  CX__IR,
  input  DX__IR,
  input  EX__IR,
  input  AX__BX,
  input  AX__CX,
  input  AX__DX,
  input  AX__EX,
  input  BX__CX,
  input  BX__DX,
  input  BX__EX,
  input  CX__DX,
  input  CX__EX,
  input  DX__EX,
  input  [15:0] AX,
  input  [15:0] BX,
  input  [15:0] CX,
  input  [15:0] DX,
  input  [15:0] EX,
  input  [15:0] DR,
  input  [15:0] IR,
  output [15:0] OUTPUT
);

  wire [3:0] logic_input_16to4_1_ax_0_3, logic_input_16to4_1_ax_4_7, logic_input_16to4_1_ax_8_11,
       logic_input_16to4_1_ax_12_15, logic_input_16to4_1_bx_0_3, logic_input_16to4_1_bx_4_7,
       logic_input_16to4_1_bx_8_11, logic_input_16to4_1_bx_12_15, logic_input_16to4_1_cx_0_3,
       logic_input_16to4_1_cx_4_7, logic_input_16to4_1_cx_8_11, logic_input_16to4_1_cx_12_15,
       logic_input_16to4_1_dr_0_3, logic_input_16to4_1_dr_4_7, logic_input_16to4_1_dr_8_11,
       logic_input_16to4_1_dr_12_15, logic_input_16to4_1_dx_0_3, logic_input_16to4_1_dx_4_7,
       logic_input_16to4_1_dx_8_11, logic_input_16to4_1_dx_12_15, logic_input_16to4_1_ex_0_3,
       logic_input_16to4_1_ex_4_7, logic_input_16to4_1_ex_8_11, logic_input_16to4_1_ex_12_15,
       logic_input_16to4_1_ir_0_3, logic_input_16to4_1_ir_0_3_2, logic_input_16to4_1_ir_4_7,
       logic_input_16to4_1_ir_12_15;

  LOGIC_INPUT_16to4 logic_input_16to4_1 (
    .AX(AX), .BX(BX), .CX(CX), .DX(DX), .EX(EX), .DR(DR), .IR(IR), .AX_0_3(logic_input_16to4_1_ax_0_3),
    .BX_0_3(logic_input_16to4_1_bx_0_3), .CX_0_3(logic_input_16to4_1_cx_0_3),
    .DX_0_3(logic_input_16to4_1_dx_0_3), .EX_0_3(logic_input_16to4_1_ex_0_3),
    .DR_0_3(logic_input_16to4_1_dr_0_3), .IR_0_3(logic_input_16to4_1_ir_0_3),
    .AX_4_7(logic_input_16to4_1_ax_4_7), .BX_4_7(logic_input_16to4_1_bx_4_7),
    .CX_4_7(logic_input_16to4_1_cx_4_7), .DX_4_7(logic_input_16to4_1_dx_4_7),
    .EX_4_7(logic_input_16to4_1_ex_4_7), .DR_4_7(logic_input_16to4_1_dr_4_7),
    .IR_4_7(logic_input_16to4_1_ir_4_7), .AX_8_11(logic_input_16to4_1_ax_8_11),
    .BX_8_11(logic_input_16to4_1_bx_8_11), .CX_8_11(logic_input_16to4_1_cx_8_11),
    .DX_8_11(logic_input_16to4_1_dx_8_11), .EX_8_11(logic_input_16to4_1_ex_8_11),
    .DR_8_11(logic_input_16to4_1_dr_8_11), .IR_0_3_2(logic_input_16to4_1_ir_0_3_2),
    .AX_12_15(logic_input_16to4_1_ax_12_15), .BX_12_15(logic_input_16to4_1_bx_12_15),
    .CX_12_15(logic_input_16to4_1_cx_12_15), .DX_12_15(logic_input_16to4_1_dx_12_15),
    .EX_12_15(logic_input_16to4_1_ex_12_15), .DR_12_15(logic_input_16to4_1_dr_12_15),
    .IR_12_15(logic_input_16to4_1_ir_12_15));
  OR_4 or_4_1 (
    .AX(logic_input_16to4_1_ax_0_3), .BX(logic_input_16to4_1_bx_0_3), .CX(logic_input_16to4_1_cx_0_3),
    .DX(logic_input_16to4_1_dx_0_3), .EX(logic_input_16to4_1_ex_0_3), .DR(logic_input_16to4_1_dr_0_3),
    .IR(logic_input_16to4_1_ir_0_3), .AX__DR(AX__DR), .BX__DR(BX__DR), .CX__DR(CX__DR), .DX__DR(DX__DR),
    .EX__DR(EX__DR), .AX__IR(AX__IR), .BX__IR(BX__IR), .CX__IR(CX__IR), .DX__IR(DX__IR), .EX__IR(EX__IR),
    .AX__BX(AX__BX), .AX__CX(AX__CX), .AX__DX(AX__DX), .AX__EX(AX__EX), .BX__CX(BX__CX), .BX__DX(BX__DX),
    .BX__EX(BX__EX), .CX__DX(CX__DX), .CX__EX(CX__EX), .DX__EX(DX__EX), .OUTPUT(OUTPUT[3:0]));
  OR_4 or_4_2 (
    .AX(logic_input_16to4_1_ax_4_7), .BX(logic_input_16to4_1_bx_4_7), .CX(logic_input_16to4_1_cx_4_7),
    .DX(logic_input_16to4_1_dx_4_7), .EX(logic_input_16to4_1_ex_4_7), .DR(logic_input_16to4_1_dr_4_7),
    .IR(logic_input_16to4_1_ir_4_7), .AX__DR(AX__DR), .BX__DR(BX__DR), .CX__DR(CX__DR), .DX__DR(DX__DR),
    .EX__DR(EX__DR), .AX__IR(AX__IR), .BX__IR(BX__IR), .CX__IR(CX__IR), .DX__IR(DX__IR), .EX__IR(EX__IR),
    .AX__BX(AX__BX), .AX__CX(AX__CX), .AX__DX(AX__DX), .AX__EX(AX__EX), .BX__CX(BX__CX), .BX__DX(BX__DX),
    .BX__EX(BX__EX), .CX__DX(CX__DX), .CX__EX(CX__EX), .DX__EX(DX__EX), .OUTPUT(OUTPUT[7:4]));
  OR_4 or_4_3 (
    .AX(logic_input_16to4_1_ax_8_11), .BX(logic_input_16to4_1_bx_8_11), .CX(logic_input_16to4_1_cx_8_11),
    .DX(logic_input_16to4_1_dx_8_11), .EX(logic_input_16to4_1_ex_8_11), .DR(logic_input_16to4_1_dr_8_11),
    .IR(logic_input_16to4_1_ir_0_3_2), .AX__DR(AX__DR), .BX__DR(BX__DR), .CX__DR(CX__DR), .DX__DR(DX__DR),
    .EX__DR(EX__DR), .AX__IR(AX__IR), .BX__IR(BX__IR), .CX__IR(CX__IR), .DX__IR(DX__IR), .EX__IR(EX__IR),
    .AX__BX(AX__BX), .AX__CX(AX__CX), .AX__DX(AX__DX), .AX__EX(AX__EX), .BX__CX(BX__CX), .BX__DX(BX__DX),
    .BX__EX(BX__EX), .CX__DX(CX__DX), .CX__EX(CX__EX), .DX__EX(DX__EX), .OUTPUT(OUTPUT[11:8]));
  OR_4 or_4_4 (
    .AX(logic_input_16to4_1_ax_12_15), .BX(logic_input_16to4_1_bx_12_15), .CX(logic_input_16to4_1_cx_12_15),
    .DX(logic_input_16to4_1_dx_12_15), .EX(logic_input_16to4_1_ex_12_15), .DR(logic_input_16to4_1_dr_12_15),
    .IR(logic_input_16to4_1_ir_12_15), .AX__DR(AX__DR), .BX__DR(BX__DR), .CX__DR(CX__DR), .DX__DR(DX__DR),
    .EX__DR(EX__DR), .AX__IR(AX__IR), .BX__IR(BX__IR), .CX__IR(CX__IR), .DX__IR(DX__IR), .EX__IR(EX__IR),
    .AX__BX(AX__BX), .AX__CX(AX__CX), .AX__DX(AX__DX), .AX__EX(AX__EX), .BX__CX(BX__CX), .BX__DX(BX__DX),
    .BX__EX(BX__EX), .CX__DX(CX__DX), .CX__EX(CX__EX), .DX__EX(DX__EX), .OUTPUT(OUTPUT[15:12]));
endmodule

module XOR (
  input  AX__DR,
  input  BX__DR,
  input  CX__DR,
  input  DX__DR,
  input  EX__DR,
  input  AX__IR,
  input  BX__IR,
  input  CX__IR,
  input  DX__IR,
  input  EX__IR,
  input  AX__BX,
  input  AX__CX,
  input  AX__DX,
  input  AX__EX,
  input  BX__CX,
  input  BX__DX,
  input  BX__EX,
  input  CX__DX,
  input  CX__EX,
  input  DX__EX,
  input  [15:0] AX,
  input  [15:0] BX,
  input  [15:0] CX,
  input  [15:0] DX,
  input  [15:0] EX,
  input  [15:0] DR,
  input  [15:0] IR,
  output [15:0] OUTPUT
);

  wire [3:0] logic_input_16to4_1_ax_0_3, logic_input_16to4_1_ax_4_7, logic_input_16to4_1_ax_8_11,
       logic_input_16to4_1_ax_12_15, logic_input_16to4_1_bx_0_3, logic_input_16to4_1_bx_4_7,
       logic_input_16to4_1_bx_8_11, logic_input_16to4_1_bx_12_15, logic_input_16to4_1_cx_0_3,
       logic_input_16to4_1_cx_4_7, logic_input_16to4_1_cx_8_11, logic_input_16to4_1_cx_12_15,
       logic_input_16to4_1_dr_0_3, logic_input_16to4_1_dr_4_7, logic_input_16to4_1_dr_8_11,
       logic_input_16to4_1_dr_12_15, logic_input_16to4_1_dx_0_3, logic_input_16to4_1_dx_4_7,
       logic_input_16to4_1_dx_8_11, logic_input_16to4_1_dx_12_15, logic_input_16to4_1_ex_0_3,
       logic_input_16to4_1_ex_4_7, logic_input_16to4_1_ex_8_11, logic_input_16to4_1_ex_12_15,
       logic_input_16to4_1_ir_0_3, logic_input_16to4_1_ir_0_3_2, logic_input_16to4_1_ir_4_7,
       logic_input_16to4_1_ir_12_15;

  LOGIC_INPUT_16to4 logic_input_16to4_1 (
    .AX(AX), .BX(BX), .CX(CX), .DX(DX), .EX(EX), .DR(DR), .IR(IR), .AX_0_3(logic_input_16to4_1_ax_0_3),
    .BX_0_3(logic_input_16to4_1_bx_0_3), .CX_0_3(logic_input_16to4_1_cx_0_3),
    .DX_0_3(logic_input_16to4_1_dx_0_3), .EX_0_3(logic_input_16to4_1_ex_0_3),
    .DR_0_3(logic_input_16to4_1_dr_0_3), .IR_0_3(logic_input_16to4_1_ir_0_3),
    .AX_4_7(logic_input_16to4_1_ax_4_7), .BX_4_7(logic_input_16to4_1_bx_4_7),
    .CX_4_7(logic_input_16to4_1_cx_4_7), .DX_4_7(logic_input_16to4_1_dx_4_7),
    .EX_4_7(logic_input_16to4_1_ex_4_7), .DR_4_7(logic_input_16to4_1_dr_4_7),
    .IR_4_7(logic_input_16to4_1_ir_4_7), .AX_8_11(logic_input_16to4_1_ax_8_11),
    .BX_8_11(logic_input_16to4_1_bx_8_11), .CX_8_11(logic_input_16to4_1_cx_8_11),
    .DX_8_11(logic_input_16to4_1_dx_8_11), .EX_8_11(logic_input_16to4_1_ex_8_11),
    .DR_8_11(logic_input_16to4_1_dr_8_11), .IR_0_3_2(logic_input_16to4_1_ir_0_3_2),
    .AX_12_15(logic_input_16to4_1_ax_12_15), .BX_12_15(logic_input_16to4_1_bx_12_15),
    .CX_12_15(logic_input_16to4_1_cx_12_15), .DX_12_15(logic_input_16to4_1_dx_12_15),
    .EX_12_15(logic_input_16to4_1_ex_12_15), .DR_12_15(logic_input_16to4_1_dr_12_15),
    .IR_12_15(logic_input_16to4_1_ir_12_15));
  XOR_4 xor_4_1 (
    .AX(logic_input_16to4_1_ax_0_3), .BX(logic_input_16to4_1_bx_0_3), .CX(logic_input_16to4_1_cx_0_3),
    .DX(logic_input_16to4_1_dx_0_3), .EX(logic_input_16to4_1_ex_0_3), .DR(logic_input_16to4_1_dr_0_3),
    .IR(logic_input_16to4_1_ir_0_3), .AX__DR(AX__DR), .BX__DR(BX__DR), .CX__DR(CX__DR), .DX__DR(DX__DR),
    .EX__DR(EX__DR), .AX__IR(AX__IR), .BX__IR(BX__IR), .CX__IR(CX__IR), .DX__IR(DX__IR), .EX__IR(EX__IR),
    .AX__BX(AX__BX), .AX__CX(AX__CX), .AX__DX(AX__DX), .AX__EX(AX__EX), .BX__CX(BX__CX), .BX__DX(BX__DX),
    .BX__EX(BX__EX), .CX__DX(CX__DX), .CX__EX(CX__EX), .DX__EX(DX__EX), .OUTPUT(OUTPUT[3:0]));
  XOR_4 xor_4_2 (
    .AX(logic_input_16to4_1_ax_4_7), .BX(logic_input_16to4_1_bx_4_7), .CX(logic_input_16to4_1_cx_4_7),
    .DX(logic_input_16to4_1_dx_4_7), .EX(logic_input_16to4_1_ex_4_7), .DR(logic_input_16to4_1_dr_4_7),
    .IR(logic_input_16to4_1_ir_4_7), .AX__DR(AX__DR), .BX__DR(BX__DR), .CX__DR(CX__DR), .DX__DR(DX__DR),
    .EX__DR(EX__DR), .AX__IR(AX__IR), .BX__IR(BX__IR), .CX__IR(CX__IR), .DX__IR(DX__IR), .EX__IR(EX__IR),
    .AX__BX(AX__BX), .AX__CX(AX__CX), .AX__DX(AX__DX), .AX__EX(AX__EX), .BX__CX(BX__CX), .BX__DX(BX__DX),
    .BX__EX(BX__EX), .CX__DX(CX__DX), .CX__EX(CX__EX), .DX__EX(DX__EX), .OUTPUT(OUTPUT[7:4]));
  XOR_4 xor_4_3 (
    .AX(logic_input_16to4_1_ax_8_11), .BX(logic_input_16to4_1_bx_8_11), .CX(logic_input_16to4_1_cx_8_11),
    .DX(logic_input_16to4_1_dx_8_11), .EX(logic_input_16to4_1_ex_8_11), .DR(logic_input_16to4_1_dr_8_11),
    .IR(logic_input_16to4_1_ir_0_3_2), .AX__DR(AX__DR), .BX__DR(BX__DR), .CX__DR(CX__DR), .DX__DR(DX__DR),
    .EX__DR(EX__DR), .AX__IR(AX__IR), .BX__IR(BX__IR), .CX__IR(CX__IR), .DX__IR(DX__IR), .EX__IR(EX__IR),
    .AX__BX(AX__BX), .AX__CX(AX__CX), .AX__DX(AX__DX), .AX__EX(AX__EX), .BX__CX(BX__CX), .BX__DX(BX__DX),
    .BX__EX(BX__EX), .CX__DX(CX__DX), .CX__EX(CX__EX), .DX__EX(DX__EX), .OUTPUT(OUTPUT[11:8]));
  XOR_4 xor_4_4 (
    .AX(logic_input_16to4_1_ax_12_15), .BX(logic_input_16to4_1_bx_12_15), .CX(logic_input_16to4_1_cx_12_15),
    .DX(logic_input_16to4_1_dx_12_15), .EX(logic_input_16to4_1_ex_12_15), .DR(logic_input_16to4_1_dr_12_15),
    .IR(logic_input_16to4_1_ir_12_15), .AX__DR(AX__DR), .BX__DR(BX__DR), .CX__DR(CX__DR), .DX__DR(DX__DR),
    .EX__DR(EX__DR), .AX__IR(AX__IR), .BX__IR(BX__IR), .CX__IR(CX__IR), .DX__IR(DX__IR), .EX__IR(EX__IR),
    .AX__BX(AX__BX), .AX__CX(AX__CX), .AX__DX(AX__DX), .AX__EX(AX__EX), .BX__CX(BX__CX), .BX__DX(BX__DX),
    .BX__EX(BX__EX), .CX__DX(CX__DX), .CX__EX(CX__EX), .DX__EX(DX__EX), .OUTPUT(OUTPUT[15:12]));
endmodule

module ADD_ADC_1 (
  input  AX,
  input  BX,
  input  CX,
  input  DX,
  input  EX,
  input  DR,
  input  IR,
  input  Cin,
  input  AX__DR,
  input  BX__DR,
  input  CX__DR,
  input  DX__DR,
  input  EX__DR,
  input  AX__IR,
  input  BX__IR,
  input  CX__IR,
  input  DX__IR,
  input  EX__IR,
  input  AX__BX,
  input  AX__CX,
  input  AX__DX,
  input  AX__EX,
  input  BX__CX,
  input  BX__DX,
  input  BX__EX,
  input  CX__DX,
  input  CX__EX,
  input  DX__EX,
  output OUTPUT,
  output Cout
);

  wire adder_1_cout, adder_1_out, adder_2_cout, adder_2_out, adder_3_cout, adder_3_out, adder_4_cout,
       adder_4_out, adder_5_cout, adder_5_out, adder_6_cout, adder_6_out, adder_7_cout, adder_7_out,
       adder_8_cout, adder_8_out, adder_9_cout, adder_9_out, adder_10_cout, adder_10_out, adder_11_cout,
       adder_11_out, adder_12_cout, adder_12_out, adder_13_cout, adder_13_out, adder_14_cout, adder_14_out,
       adder_15_cout, adder_15_out, adder_16_cout, adder_16_out, adder_17_cout, adder_17_out, adder_18_cout,
       adder_18_out, adder_19_cout, adder_19_out, adder_20_cout, adder_20_out, and_1_out, and_2_out,
       and_3_out, and_4_out, and_5_out, and_6_out, and_7_out, and_8_out, and_9_out, and_10_out, and_11_out,
       and_12_out, and_13_out, and_14_out, and_15_out, and_16_out, and_17_out, and_18_out, and_19_out,
       and_20_out, or_1_out, or_2_out, or_3_out, or_4_out, or_5_out, or_6_out, or_7_out, or_8_out, or_9_out,
       or_10_out, or_11_out, or_12_out, or_13_out, or_14_out, or_15_out, or_16_out, or_17_out, or_18_out;

  Adder #(.width(1)) adder_1 (.a(DR), .b(AX), .out(adder_1_out), .cin(Cin), .cout(adder_1_cout));
  Adder #(.width(1)) adder_2 (.a(DR), .b(BX), .out(adder_2_out), .cin(Cin), .cout(adder_2_cout));
  Adder #(.width(1)) adder_3 (.a(DR), .b(CX), .out(adder_3_out), .cin(Cin), .cout(adder_3_cout));
  Adder #(.width(1)) adder_4 (.a(DR), .b(DX), .out(adder_4_out), .cin(Cin), .cout(adder_4_cout));
  Adder #(.width(1)) adder_5 (.a(DR), .b(EX), .out(adder_5_out), .cin(Cin), .cout(adder_5_cout));
  Adder #(.width(1)) adder_6 (.a(IR), .b(AX), .out(adder_6_out), .cin(Cin), .cout(adder_6_cout));
  Adder #(.width(1)) adder_7 (.a(IR), .b(BX), .out(adder_7_out), .cin(Cin), .cout(adder_7_cout));
  Adder #(.width(1)) adder_8 (.a(IR), .b(CX), .out(adder_8_out), .cin(Cin), .cout(adder_8_cout));
  Adder #(.width(1)) adder_9 (.a(IR), .b(DX), .out(adder_9_out), .cin(Cin), .cout(adder_9_cout));
  Adder #(.width(1)) adder_10 (.a(IR), .b(EX), .out(adder_10_out), .cin(Cin), .cout(adder_10_cout));
  Adder #(.width(1)) adder_11 (.a(BX), .b(AX), .out(adder_11_out), .cin(Cin), .cout(adder_11_cout));
  Adder #(.width(1)) adder_12 (.a(CX), .b(AX), .out(adder_12_out), .cin(Cin), .cout(adder_12_cout));
  Adder #(.width(1)) adder_13 (.a(DX), .b(AX), .out(adder_13_out), .cin(Cin), .cout(adder_13_cout));
  Adder #(.width(1)) adder_14 (.a(EX), .b(AX), .out(adder_14_out), .cin(Cin), .cout(adder_14_cout));
  Adder #(.width(1)) adder_15 (.a(CX), .b(BX), .out(adder_15_out), .cin(Cin), .cout(adder_15_cout));
  Adder #(.width(1)) adder_16 (.a(DX), .b(BX), .out(adder_16_out), .cin(Cin), .cout(adder_16_cout));
  Adder #(.width(1)) adder_17 (.a(EX), .b(BX), .out(adder_17_out), .cin(Cin), .cout(adder_17_cout));
  Adder #(.width(1)) adder_18 (.a(DX), .b(CX), .out(adder_18_out), .cin(Cin), .cout(adder_18_cout));
  Adder #(.width(1)) adder_19 (.a(EX), .b(CX), .out(adder_19_out), .cin(Cin), .cout(adder_19_cout));
  Adder #(.width(1)) adder_20 (.a(EX), .b(DX), .out(adder_20_out), .cin(Cin), .cout(adder_20_cout));
  or or_1 (or_1_out, adder_2_cout, adder_1_cout);
  or or_2 (or_2_out, adder_3_cout, or_1_out);
  or or_3 (or_3_out, adder_4_cout, or_2_out);
  or or_4 (or_4_out, adder_5_cout, or_3_out);
  or or_5 (or_5_out, adder_6_cout, or_4_out);
  or or_6 (or_6_out, adder_7_cout, or_5_out);
  or or_7 (or_7_out, adder_8_cout, or_6_out);
  or or_8 (or_8_out, adder_9_cout, or_7_out);
  or or_9 (or_9_out, adder_10_cout, or_8_out);
  or or_10 (or_10_out, adder_11_cout, or_9_out);
  or or_11 (or_11_out, adder_12_cout, or_10_out);
  or or_12 (or_12_out, adder_13_cout, or_11_out);
  or or_13 (or_13_out, adder_14_cout, or_12_out);
  or or_14 (or_14_out, adder_15_cout, or_13_out);
  or or_15 (or_15_out, adder_16_cout, or_14_out);
  or or_16 (or_16_out, adder_17_cout, or_15_out);
  or or_17 (or_17_out, adder_18_cout, or_16_out);
  or or_18 (or_18_out, adder_19_cout, or_17_out);
  or or_19 (Cout, adder_20_cout, or_18_out);
  and and_1 (and_1_out, AX__DR, adder_1_out);
  and and_2 (and_2_out, BX__DR, adder_2_out);
  and and_3 (and_3_out, CX__DR, adder_3_out);
  and and_4 (and_4_out, DX__DR, adder_4_out);
  and and_5 (and_5_out, EX__DR, adder_5_out);
  and and_6 (and_6_out, AX__IR, adder_6_out);
  and and_7 (and_7_out, BX__IR, adder_7_out);
  and and_8 (and_8_out, CX__IR, adder_8_out);
  and and_9 (and_9_out, DX__IR, adder_9_out);
  and and_10 (and_10_out, EX__IR, adder_10_out);
  and and_11 (and_11_out, AX__BX, adder_11_out);
  and and_12 (and_12_out, AX__CX, adder_12_out);
  and and_13 (and_13_out, AX__DX, adder_13_out);
  and and_14 (and_14_out, AX__EX, adder_14_out);
  and and_15 (and_15_out, BX__CX, adder_15_out);
  and and_16 (and_16_out, BX__DX, adder_16_out);
  and and_17 (and_17_out, BX__EX, adder_17_out);
  and and_18 (and_18_out, CX__DX, adder_18_out);
  and and_19 (and_19_out, CX__EX, adder_19_out);
  and and_20 (and_20_out, DX__EX, adder_20_out);
  or or_20 (OUTPUT, and_1_out, and_2_out, and_3_out, and_4_out, and_5_out, and_6_out, and_7_out, and_8_out, and_9_out, and_10_out, and_11_out, and_12_out, and_13_out, and_14_out, and_15_out, and_16_out, and_17_out, and_18_out, and_19_out, and_20_out);
endmodule
