// Logisim project 4BitShift.circ as structural Verilog: 1 circuit, main circuit main
module main (
  input  i3,
  input  i2,
  input  i1,
  input  i0,
  input  [2:0] s1_s0,
  input  Clr,
  output Q3,
  output Q2,
  output Q1,
  output Q0
);

  wire clock_1_out, multiplexer_1_out, multiplexer_2_out, multiplexer_3_out, multiplexer_4_out;

  Multiplexer #(.select(3)) multiplexer_1 (
    .in0(Q3), .in1(1'b0), .in2(Q2), .in3(i3), .in4(Q0), .in5(Q2), .out(multiplexer_1_out), .sel(s1_s0));  // open: in6, in7, en
  Multiplexer #(.select(3)) multiplexer_2 (
    .in0(Q2), .in1(Q3), .in2(Q1), .in3(i2), .in4(Q3), .in5(Q1), .out(multiplexer_2_out), .sel(s1_s0));  // open: in6, in7, en
  Multiplexer #(.select(3)) multiplexer_3 (
    .in0(Q1), .in1(Q2), .in2(Q0), .in3(i1), .in4(Q2), .in5(Q0), .out(multiplexer_3_out), .sel(s1_s0));  // open: in6, in7, en
  Multiplexer #(.select(3)) multiplexer_4 (
    .in0(Q0), .in1(Q1), .in2(1'b0), .in3(i0), .in4(Q1), .in5(Q3), .out(multiplexer_4_out), .sel(s1_s0));  // open: in6, in7, en
  Clock clock_1 (.out(clock_1_out));
  D_Flip_Flop d_ff_1 (.clk(clock_1_out), .D(multiplexer_1_out), .Q(Q3), .reset(Clr));  // open: Qn, preset, en
  D_Flip_Flop d_ff_2 (.clk(clock_1_out), .D(multiplexer_2_out), .Q(Q2), .reset(Clr));  // open: Qn, preset, en
  D_Flip_Flop d_ff_3 (.clk(clock_1_out), .D(multiplexer_3_out), .Q(Q1), .reset(Clr));  // open: Qn, preset, en
  D_Flip_Flop d_ff_4 (.clk(clock_1_out), .D(multiplexer_4_out), .Q(Q0), .reset(Clr));  // open: Qn, preset, en
endmodule
